// Logisim project 16bit_2add.circ as structural Verilog: 5 circuits, main circuit main
module main (
  input  [11:0] PC_input,
  output [11:0] PC_INPUT_2
);

  wire Clock, not_1_out, PC_shift_out, Reset, selector_1_output, selector_2_output;
  wire [3:0] MAR_q, MAR_q_2, MAR_q_3, RZ_q_2, RZ_q_3;
  wire [11:0] IR_q, MBR_q, rom_1_data;
  wire [15:0] multiplexer_1_out, multiplexer_2_out, or_1_out, or_1_out_2, or_2_out, or_2_out_2, RA_q,
       ram_1_data, RB_q, register_1_regi_out_02, register_1_regi_out_02_2;
  wire [31:0] bit_extender_1_out, bit_extender_2_out, dhva3_1_aluoutput, dhva3_1_exchange, dhva3_1_register,
       dhva3_1_store, RZ_q;

  Hex_Digit_Display hex_digit_display_1 (.value(PC_input[11:8]));  // open: dp
  Hex_Digit_Display hex_digit_display_2 (.value(PC_input[7:4]));  // open: dp
  Hex_Digit_Display hex_digit_display_3 (.value(MAR_q_3));  // open: dp
  Hex_Digit_Display hex_digit_display_4 (.value(PC_input[3:0]));  // open: dp
  Shift_Register #(.length(6)) PC_shift (
    .in(PC_shift_out), .clk(Clock), .out(PC_shift_out));  // open: shift, load, clr, d0, q0, d1, q1, d2, q2, d3, q3, d4, q4, d5, q5
  Button button_1 (.out(Clock));
  Hex_Digit_Display hex_digit_display_5 (.value(MAR_q));  // open: dp
  Hex_Digit_Display hex_digit_display_6 (.value(MAR_q_2));  // open: dp
  Register_part #(.width(12)) MAR (
    .D(PC_INPUT_2), .Q({MAR_q_3, MAR_q_2, MAR_q}), .clk(Clock), .clr(Reset));  // open: en
  Program_counter program_counter_1 (
    .PC_INput(PC_input), .PC_enable(PC_shift_out), .Clock(Clock), .PC_reset(Reset), .PC_OUT(PC_INPUT_2));
  Button button_2 (.out(Reset));
  not not_1 (not_1_out, PC_shift_out);
  ROM #(.addrWidth(12), .dataWidth(12)) rom_1 (.addr({MAR_q_3, MAR_q_2, MAR_q}), .data(rom_1_data));  // open: sel
  Register_part #(.width(12)) MBR (.D(rom_1_data), .Q(MBR_q), .clk(Clock), .clr(Reset));  // open: en
  selector selector_1 (.Input({or_1_out_2, or_1_out}), .Output(selector_1_output));
  Multiplexer #(.width(16)) multiplexer_1 (
    .in0(RA_q), .in1(or_1_out), .out(multiplexer_1_out), .sel(selector_1_output));  // open: en
  Register_part #(.width(12)) IR (.D(MBR_q), .Q(IR_q), .clk(Clock), .clr(Reset));  // open: en
  RAM #(.addrWidth(16), .dataWidth(16), .bus("separate")) ram_1 (
    .addr(register_1_regi_out_02_2), .din(multiplexer_2_out), .data(ram_1_data), .str(not_1_out),
    .clk(Clock), .ld(not_1_out));  // open: sel, clr
  assign {or_1_out_2, or_1_out} = bit_extender_1_out | dhva3_1_register;  // OR_Gate or_1, 32 bits wide
  Register register_1 (
    .Data_in(multiplexer_1_out), .R_W(not_1_out), .input01(IR_q[7:4]), .Input_02(IR_q[3:0]), .Clock(Clock),
    .Regi_out_02(register_1_regi_out_02), .Regi_out_02_2(register_1_regi_out_02_2));
  Multiplexer #(.width(16)) multiplexer_2 (
    .in0(RB_q), .in1(or_2_out), .out(multiplexer_2_out), .sel(selector_2_output));  // open: en
  Register_part #(.width(16)) RA (.D(register_1_regi_out_02), .Q(RA_q), .clk(Clock), .clr(Reset));  // open: en
  assign {or_2_out_2, or_2_out} = bit_extender_2_out | dhva3_1_store;  // OR_Gate or_2, 32 bits wide
  selector selector_2 (.Input({or_2_out_2, or_2_out}), .Output(selector_2_output));
  Hex_Digit_Display hex_digit_display_7 (.value(RZ_q[31:28]));  // open: dp
  Hex_Digit_Display hex_digit_display_8 (.value(RZ_q_3));  // open: dp
  Register_part #(.width(16)) RB (.D(ram_1_data), .Q(RB_q), .clk(Clock), .clr(Reset));  // open: en
  Hex_Digit_Display hex_digit_display_9 (.value(RZ_q_2));  // open: dp
  Hex_Digit_Display hex_digit_display_10 (.value(RZ_q[19:16]));  // open: dp
  Register_part #(.width(32)) RZ (
    .D(dhva3_1_aluoutput), .Q({RZ_q[31:28], RZ_q_3, RZ_q_2, RZ_q[19:0]}), .clk(Clock), .clr(Reset));  // open: en
  Hex_Digit_Display hex_digit_display_11 (.value(RZ_q[11:8]));  // open: dp
  Hex_Digit_Display hex_digit_display_12 (.value(RZ_q[15:12]));  // open: dp
  assign bit_extender_1_out = {{16{1'b0}}, dhva3_1_exchange[15:0]};  // Bit_Extender bit_extender_1
  assign bit_extender_2_out = {{16{1'b0}}, dhva3_1_exchange[31:16]};  // Bit_Extender bit_extender_2
  Hex_Digit_Display hex_digit_display_13 (.value(RZ_q[7:4]));  // open: dp
  Hex_Digit_Display hex_digit_display_14 (.value(RZ_q[3:0]));  // open: dp
  dhva3 dhva3_1 (
    .input1(RA_q), .input2(RB_q), .SELECT(IR_q[11:8]), .Exchange(dhva3_1_exchange),
    .ALUoutput(dhva3_1_aluoutput), .Register(dhva3_1_register), .Store(dhva3_1_store));  // open: Carry

  // Notes on the sheet:
  //   PC
  //   Code Memory
  //   contents of rom_1 (hex, n*v repeats v):
  //   201 524 431 512 246
  //   Register
  //   ALU
endmodule

module Register (
  input  [15:0] Data_in,
  input  R_W,
  input  [3:0] input01,
  input  [3:0] Input_02,
  input  Clock,
  output [15:0] Regi_out_02,
  output [15:0] Regi_out_02_2
);

  wire decoder_1_out0, decoder_1_out1, decoder_1_out2, decoder_1_out3, decoder_1_out4, decoder_1_out5,
       decoder_1_out6, decoder_1_out7, decoder_1_out8, decoder_1_out9, decoder_1_out10, decoder_1_out11,
       decoder_1_out12, decoder_1_out13, decoder_1_out14, decoder_1_out15, not_1_out;
  wire [15:0] R0_q, R1_q, R2_q, R3_q, R4_q, R5_q, R6_q, R7_q, R8_q, R9_q, R10_q, R11_q, R12_q, R13_q, R14_q,
       R15_q;

  Hex_Digit_Display hex_digit_display_1 (.value(Input_02));  // open: dp
  Decoder #(.select(4), .disabled(0)) decoder_1 (
    .out0(decoder_1_out0), .out1(decoder_1_out1), .out2(decoder_1_out2), .out3(decoder_1_out3),
    .out4(decoder_1_out4), .out5(decoder_1_out5), .out6(decoder_1_out6), .out7(decoder_1_out7),
    .out8(decoder_1_out8), .out9(decoder_1_out9), .out10(decoder_1_out10), .out11(decoder_1_out11),
    .out12(decoder_1_out12), .out13(decoder_1_out13), .out14(decoder_1_out14), .out15(decoder_1_out15),
    .sel(input01), .en(not_1_out));
  not not_1 (not_1_out, R_W);
  Hex_Digit_Display hex_digit_display_2 (.value(input01));  // open: dp
  Register_part #(.width(16)) R0 (.D(Data_in), .en(decoder_1_out0), .Q(R0_q), .clk(Clock));  // open: clr
  Register_part #(.width(16)) R2 (.D(Data_in), .en(decoder_1_out2), .Q(R2_q), .clk(Clock));  // open: clr
  Register_part #(.width(16)) R4 (.D(Data_in), .en(decoder_1_out4), .Q(R4_q), .clk(Clock));  // open: clr
  Register_part #(.width(16)) R6 (.D(Data_in), .en(decoder_1_out6), .Q(R6_q), .clk(Clock));  // open: clr
  Register_part #(.width(16)) R8 (.D(Data_in), .en(decoder_1_out8), .Q(R8_q), .clk(Clock));  // open: clr
  Register_part #(.width(16)) R10 (.D(Data_in), .en(decoder_1_out10), .Q(R10_q), .clk(Clock));  // open: clr
  Register_part #(.width(16)) R12 (.D(Data_in), .en(decoder_1_out12), .Q(R12_q), .clk(Clock));  // open: clr
  Register_part #(.width(16)) R14 (.D(Data_in), .en(decoder_1_out14), .Q(R14_q), .clk(Clock));  // open: clr
  Register_part #(.width(16)) R1 (.D(Data_in), .en(decoder_1_out1), .Q(R1_q), .clk(Clock));  // open: clr
  Register_part #(.width(16)) R3 (.D(Data_in), .en(decoder_1_out3), .Q(R3_q), .clk(Clock));  // open: clr
  Register_part #(.width(16)) R5 (.D(Data_in), .en(decoder_1_out5), .Q(R5_q), .clk(Clock));  // open: clr
  Register_part #(.width(16)) R7 (.D(Data_in), .en(decoder_1_out7), .Q(R7_q), .clk(Clock));  // open: clr
  Register_part #(.width(16)) R9 (.D(Data_in), .en(decoder_1_out9), .Q(R9_q), .clk(Clock));  // open: clr
  Register_part #(.width(16)) R11 (.D(Data_in), .en(decoder_1_out11), .Q(R11_q), .clk(Clock));  // open: clr
  Register_part #(.width(16)) R13 (.D(Data_in), .en(decoder_1_out13), .Q(R13_q), .clk(Clock));  // open: clr
  Register_part #(.width(16)) R15 (.D(Data_in), .en(decoder_1_out15), .Q(R15_q), .clk(Clock));  // open: clr
  Multiplexer #(.select(4), .width(16)) multiplexer_1 (
    .in0(R0_q), .in1(R1_q), .in2(R2_q), .in3(R3_q), .in4(R4_q), .in5(R5_q), .in6(R6_q), .in7(R7_q),
    .in8(R8_q), .in9(R9_q), .in10(R10_q), .in11(R11_q), .in12(R12_q), .in13(R13_q), .in14(R14_q),
    .in15(R15_q), .out(Regi_out_02), .sel(input01), .en(R_W));
  Hex_Digit_Display hex_digit_display_3 (.value(Regi_out_02[11:8]));  // open: dp
  Hex_Digit_Display hex_digit_display_4 (.value(Regi_out_02[15:12]));  // open: dp
  Hex_Digit_Display hex_digit_display_5 (.value(Regi_out_02_2[15:12]));  // open: dp
  Multiplexer #(.select(4), .width(16)) multiplexer_2 (
    .in0(R0_q), .in1(R1_q), .in2(R2_q), .in3(R3_q), .in4(R4_q), .in5(R5_q), .in6(R6_q), .in7(R7_q),
    .in8(R8_q), .in9(R9_q), .in10(R10_q), .in11(R11_q), .in12(R12_q), .in13(R13_q), .in14(R14_q),
    .in15(R15_q), .out(Regi_out_02_2), .sel(Input_02), .en(R_W));
  Hex_Digit_Display hex_digit_display_6 (.value(Regi_out_02[7:4]));  // open: dp
  Hex_Digit_Display hex_digit_display_7 (.value(Regi_out_02[3:0]));  // open: dp
  Hex_Digit_Display hex_digit_display_8 (.value(Regi_out_02_2[7:4]));  // open: dp
  Hex_Digit_Display hex_digit_display_9 (.value(Regi_out_02_2[11:8]));  // open: dp
  Hex_Digit_Display hex_digit_display_10 (.value(Regi_out_02_2[3:0]));  // open: dp

  // Notes on the sheet:
  //   Register (4bits)
  //   Regi_out_02
  //   Regi_out_02
endmodule

module selector (
  input  [31:0] Input,
  output Output
);

  wire bit_extender_1_out, or_1_out;

  or or_1 (or_1_out, Input[0], Input[1], Input[2], Input[3], Input[4], Input[5], Input[6], Input[7], Input[8], Input[9], Input[10], Input[11], Input[12], Input[13], Input[14], Input[15], Input[16], Input[17], Input[18], Input[19], Input[20], Input[21], Input[22], Input[23], Input[24], Input[25], Input[26], Input[27], Input[28], Input[29], Input[30], Input[31]);
  Comparator #(.width(1), .mode("unsigned")) comparator_1 (
    .a(or_1_out), .b(bit_extender_1_out), .eq(Output));  // open: gt, lt
  Bit_Extender #(.in_width(1), .out_width(1)) bit_extender_1 (.in(1'b1), .out(bit_extender_1_out));
endmodule

module dhva3 (
  input  [15:0] input1,
  input  [15:0] input2,
  input  [3:0] SELECT,
  output Carry,
  output [31:0] ALUoutput,
  output [31:0] Register,
  output [31:0] Exchange,
  output [31:0] Store
);

  wire adder_1_cout, subtractor_1_bout;
  wire [3:0] bit_extender_2_out;
  wire [15:0] adder_1_out, adder_2_out, and_1_out, bit_extender_1_out, bit_extender_5_out,
       bit_extender_6_out, divider_1_out, divider_1_rem, multiplier_1_cout, multiplier_1_out, not_1_out,
       or_1_out, shifter_1_out, shifter_2_out, shifter_3_out, shifter_4_out, subtractor_1_out,
       subtractor_2_out;
  wire [31:0] bit_extender_3_out, bit_extender_4_out, bit_extender_7_out, bit_extender_8_out,
       bit_extender_9_out, bit_extender_10_out, bit_extender_11_out, bit_extender_12_out,
       bit_extender_13_out, bit_extender_14_out, bit_extender_15_out, demultiplexer_1_out0,
       demultiplexer_1_out2, demultiplexer_1_out3, demultiplexer_1_out4, demultiplexer_1_out5,
       demultiplexer_1_out6, demultiplexer_1_out7, demultiplexer_1_out8, demultiplexer_1_out9,
       demultiplexer_1_out10, demultiplexer_1_out12, demultiplexer_1_out13, demultiplexer_1_out14;

  assign bit_extender_1_out = {{15{1'b0}}, 1'b1};  // Bit_Extender bit_extender_1
  Bit_Extender #(.in_width(16), .out_width(4)) bit_extender_2 (.in(input2), .out(bit_extender_2_out));
  assign bit_extender_3_out = {{16{1'b0}}, input2};  // Bit_Extender bit_extender_3
  assign bit_extender_4_out = {{16{1'b0}}, input1};  // Bit_Extender bit_extender_4
  Adder #(.width(16)) adder_1 (.a(input1), .b(input2), .out(adder_1_out), .cout(adder_1_cout));  // open: cin
  Subtractor #(.width(16)) subtractor_1 (
    .a(input1), .b(input2), .out(subtractor_1_out), .bout(subtractor_1_bout));  // open: bin
  Multiplier #(.width(16)) multiplier_1 (
    .a(input1), .b(input2), .out(multiplier_1_out), .cout(multiplier_1_cout));  // open: cin
  Divider #(.width(16)) divider_1 (.a(input1), .b(input2), .out(divider_1_out), .rem(divider_1_rem));  // open: upper
  Adder #(.width(16)) adder_2 (.a(input1), .b(bit_extender_1_out), .out(adder_2_out));  // open: cin, cout
  Subtractor #(.width(16)) subtractor_2 (
    .a(input1), .b(bit_extender_1_out), .out(subtractor_2_out));  // open: bin, bout
  assign and_1_out = input1 & input2;  // AND_Gate and_1, 16 bits wide
  assign or_1_out = input1 | input2;  // OR_Gate or_1, 16 bits wide
  assign not_1_out = ~input1;  // NOT_Gate not_1, 16 bits wide
  Shifter #(.width(16), .shift("lr")) shifter_1 (.in(input1), .\dist (bit_extender_2_out), .out(shifter_1_out));
  Shifter #(.width(16)) shifter_2 (.in(input1), .\dist (bit_extender_2_out), .out(shifter_2_out));
  Shifter #(.width(16), .shift("rr")) shifter_3 (.in(input1), .\dist (bit_extender_2_out), .out(shifter_3_out));
  Shifter #(.width(16), .shift("rl")) shifter_4 (.in(input1), .\dist (bit_extender_2_out), .out(shifter_4_out));
  assign bit_extender_5_out = {{15{1'b0}}, adder_1_cout};  // Bit_Extender bit_extender_5
  assign bit_extender_6_out = {{15{1'b0}}, subtractor_1_bout};  // Bit_Extender bit_extender_6
  assign bit_extender_7_out = {{16{1'b0}}, adder_2_out};  // Bit_Extender bit_extender_7
  assign bit_extender_8_out = {{16{1'b0}}, subtractor_2_out};  // Bit_Extender bit_extender_8
  assign bit_extender_9_out = {{16{1'b0}}, and_1_out};  // Bit_Extender bit_extender_9
  assign bit_extender_10_out = {{16{1'b0}}, or_1_out};  // Bit_Extender bit_extender_10
  assign bit_extender_11_out = {{16{1'b0}}, not_1_out};  // Bit_Extender bit_extender_11
  assign bit_extender_12_out = {{16{1'b0}}, shifter_1_out};  // Bit_Extender bit_extender_12
  assign bit_extender_13_out = {{16{1'b0}}, shifter_2_out};  // Bit_Extender bit_extender_13
  assign bit_extender_14_out = {{16{1'b0}}, shifter_3_out};  // Bit_Extender bit_extender_14
  assign bit_extender_15_out = {{16{1'b0}}, shifter_4_out};  // Bit_Extender bit_extender_15
  or or_2 (Carry, adder_1_cout, subtractor_1_bout);
  Multiplexer #(.select(4), .width(32), .disabled(0)) multiplexer_1 (
    .in0(bit_extender_3_out), .in1(bit_extender_4_out), .in2({bit_extender_5_out, adder_1_out}),
    .in3({bit_extender_6_out, subtractor_1_out}), .in4({multiplier_1_cout, multiplier_1_out}),
    .in5({divider_1_rem, divider_1_out}), .in6(bit_extender_7_out), .in7(bit_extender_8_out),
    .in8(bit_extender_9_out), .in9(bit_extender_10_out), .in10(bit_extender_11_out), .in11({input1, input2}),
    .in12(bit_extender_12_out), .in13(bit_extender_13_out), .in14(bit_extender_14_out),
    .in15(bit_extender_15_out), .out(ALUoutput), .sel(SELECT));  // open: en
  Hex_Digit_Display hex_digit_display_1 (.value(SELECT));  // open: dp
  Hex_Digit_Display hex_digit_display_2 (.value(ALUoutput[31:28]));  // open: dp
  Hex_Digit_Display hex_digit_display_3 (.value(ALUoutput[27:24]));  // open: dp
  Hex_Digit_Display hex_digit_display_4 (.value(ALUoutput[23:20]));  // open: dp
  Hex_Digit_Display hex_digit_display_5 (.value(ALUoutput[19:16]));  // open: dp
  Hex_Digit_Display hex_digit_display_6 (.value(ALUoutput[15:12]));  // open: dp
  Hex_Digit_Display hex_digit_display_7 (.value(ALUoutput[11:8]));  // open: dp
  Demultiplexer #(.select(4), .width(32)) demultiplexer_1 (
    .out0(demultiplexer_1_out0), .out1(Store), .out2(demultiplexer_1_out2), .out3(demultiplexer_1_out3),
    .out4(demultiplexer_1_out4), .out5(demultiplexer_1_out5), .out6(demultiplexer_1_out6),
    .out7(demultiplexer_1_out7), .out8(demultiplexer_1_out8), .out9(demultiplexer_1_out9),
    .out10(demultiplexer_1_out10), .out11(Exchange), .out12(demultiplexer_1_out12),
    .out13(demultiplexer_1_out13), .out14(demultiplexer_1_out14), .out15(demultiplexer_1_out14),
    .in(ALUoutput), .sel(SELECT));  // open: en
  Hex_Digit_Display hex_digit_display_8 (.value(ALUoutput[7:4]));  // open: dp
  Hex_Digit_Display hex_digit_display_9 (.value(ALUoutput[3:0]));  // open: dp
  assign Register = demultiplexer_1_out0 | demultiplexer_1_out2 | demultiplexer_1_out3 | demultiplexer_1_out4 | demultiplexer_1_out5 | demultiplexer_1_out6 | demultiplexer_1_out8 | demultiplexer_1_out9 | demultiplexer_1_out10 | demultiplexer_1_out12 | demultiplexer_1_out13 | demultiplexer_1_out14;  // OR_Gate or_3, 32 bits wide
  Hex_Digit_Display hex_digit_display_10 (.value(Exchange[31:28]));  // open: dp
  Hex_Digit_Display hex_digit_display_11 (.value(Store[27:24]));  // open: dp
  Hex_Digit_Display hex_digit_display_12 (.value(Store[31:28]));  // open: dp
  Hex_Digit_Display hex_digit_display_13 (.value(Register[31:28]));  // open: dp
  Hex_Digit_Display hex_digit_display_14 (.value(Register[27:24]));  // open: dp
  Hex_Digit_Display hex_digit_display_15 (.value(Exchange[23:20]));  // open: dp
  Hex_Digit_Display hex_digit_display_16 (.value(Exchange[27:24]));  // open: dp
  Hex_Digit_Display hex_digit_display_17 (.value(Store[19:16]));  // open: dp
  Hex_Digit_Display hex_digit_display_18 (.value(Store[23:20]));  // open: dp
  Hex_Digit_Display hex_digit_display_19 (.value(Register[23:20]));  // open: dp
  Hex_Digit_Display hex_digit_display_20 (.value(Register[19:16]));  // open: dp
  Hex_Digit_Display hex_digit_display_21 (.value(Exchange[15:12]));  // open: dp
  Hex_Digit_Display hex_digit_display_22 (.value(Exchange[19:16]));  // open: dp
  Hex_Digit_Display hex_digit_display_23 (.value(Store[11:8]));  // open: dp
  Hex_Digit_Display hex_digit_display_24 (.value(Store[15:12]));  // open: dp
  Hex_Digit_Display hex_digit_display_25 (.value(Register[11:8]));  // open: dp
  Hex_Digit_Display hex_digit_display_26 (.value(Register[15:12]));  // open: dp
  Hex_Digit_Display hex_digit_display_27 (.value(Exchange[7:4]));  // open: dp
  Hex_Digit_Display hex_digit_display_28 (.value(Exchange[11:8]));  // open: dp
  Hex_Digit_Display hex_digit_display_29 (.value(Store[7:4]));  // open: dp
  Hex_Digit_Display hex_digit_display_30 (.value(Store[3:0]));  // open: dp
  Hex_Digit_Display hex_digit_display_31 (.value(Register[7:4]));  // open: dp
  Hex_Digit_Display hex_digit_display_32 (.value(Register[3:0]));  // open: dp
  Hex_Digit_Display hex_digit_display_33 (.value(Exchange[3:0]));  // open: dp

  // Notes on the sheet:
  //   BitExtender
  //   Increment-----------------------------
  //   Decrement-----------------------
  //   Exchange
  //   Load
  //   Store
  //   Add
  //   Sub
  //   Mul
  //   Div
  //   And
  //   OR
  //   ShiftLeft
  //   Rotateright
  //   RotateLeft
  //   ALU-8bit 
  //   Not
  //   ShiftRight
  //   0-adder|1-sub|2-mpy|3-div|4-and|5-or|6-xnor|7-xor|8-lls|9-lrs|10-ars|11-rr|12-rl
endmodule

module Program_counter (
  input  [11:0] PC_INput,
  input  PC_enable,
  input  Clock,
  input  PC_reset,
  output [11:0] PC_OUT
);

  wire [11:0] adder_1_out;

  Hex_Digit_Display hex_digit_display_1 (.value(PC_INput[11:8]));  // open: dp
  Hex_Digit_Display hex_digit_display_2 (.value(PC_INput[3:0]));  // open: dp
  Hex_Digit_Display hex_digit_display_3 (.value(PC_INput[7:4]));  // open: dp
  Adder #(.width(12)) adder_1 (.a(PC_INput), .b(PC_OUT), .out(adder_1_out), .cin(1'b1));  // open: cout
  Hex_Digit_Display hex_digit_display_4 (.value(PC_OUT[11:8]));  // open: dp
  Hex_Digit_Display hex_digit_display_5 (.value(PC_OUT[7:4]));  // open: dp
  Register_part #(.width(12)) register_1 (.D(adder_1_out), .en(PC_enable), .Q(PC_OUT), .clk(Clock), .clr(PC_reset));
  Hex_Digit_Display hex_digit_display_6 (.value(PC_OUT[3:0]));  // open: dp
endmodule
