// Logisim project 16bit_immediate_adress.circ as structural Verilog: 4 circuits, main circuit main
module main (
  input  [7:0] in_1,
  output [7:0] PC,
  output [31:0] out_3
);

  wire Clock, not_1_out, PC_shift_out, RESET;
  wire [11:0] MAR_q;
  wire [11:8] undriven;
  wire [15:0] bit_extender_1_out, RA_q, RB_q, register_1_regi_out_02, RZ_q;
  wire [19:0] IR_q, MBR_q, rom_1_data;
  wire [31:16] RZ_q_2;

  pc pc_1 (.PC_INput(in_1), .PC_enable(PC_shift_out), .Clock(Clock), .PC_reset(RESET), .PC_OUT(PC));
  Shift_Register #(.length(5)) PC_shift (
    .in(PC_shift_out), .clk(Clock), .out(PC_shift_out));  // open: shift, load, clr, d0, q0, d1, q1, d2, q2, d3, q3, d4, q4
  Register #(.width(12)) MAR (.D({undriven, PC}), .en(PC_shift_out), .Q(MAR_q), .clk(Clock), .clr(RESET));
  not not_1 (not_1_out, PC_shift_out);
  ROM #(.dataWidth(20)) rom_1 (.addr(MAR_q[7:0]), .data(rom_1_data));  // open: sel
  Register #(.width(20)) MBR (.D(rom_1_data), .Q(MBR_q), .clk(Clock), .clr(RESET));  // open: en
  Register #(.width(20)) IR (.D(MBR_q), .Q(IR_q), .clk(Clock), .clr(RESET));  // open: en
  assign bit_extender_1_out = {{8{1'b0}}, IR_q[7:0]};  // Bit_Extender bit_extender_1
  Register #(.width(16)) RA (.D(register_1_regi_out_02), .Q(RA_q), .clk(Clock), .clr(RESET));  // open: en
  register register_1 (
    .Data_in(RZ_q), .R_W(not_1_out), .input01(IR_q[15:12]), .Input_02(IR_q[11:8]), .Clock(Clock),
    .Regi_out_02(register_1_regi_out_02));  // open: Regi_out_01
  Register #(.width(16)) RB (.D(bit_extender_1_out), .Q(RB_q), .clk(Clock), .clr(RESET));  // open: en
  Register #(.width(32)) RZ (.D(out_3), .Q({RZ_q_2, RZ_q}), .clk(Clock), .clr(RESET));  // open: en
  Alu alu_1 (.A(RA_q), .B(RB_q), .SELECT(IR_q[19:16]), .ALU_output(out_3));
  Button button_1 (.out(RESET));
  Hex_Digit_Display hex_digit_display_1 (.value(out_3[31:28]));  // open: dp
  Hex_Digit_Display hex_digit_display_2 (.value(out_3[27:24]));  // open: dp
  Button button_2 (.out(Clock));
  Hex_Digit_Display hex_digit_display_3 (.value(out_3[23:20]));  // open: dp
  Hex_Digit_Display hex_digit_display_4 (.value(out_3[19:16]));  // open: dp
  Hex_Digit_Display hex_digit_display_5 (.value(out_3[15:12]));  // open: dp
  Hex_Digit_Display hex_digit_display_6 (.value(out_3[11:8]));  // open: dp
  Hex_Digit_Display hex_digit_display_7 (.value(out_3[3:0]));  // open: dp
  Hex_Digit_Display hex_digit_display_8 (.value(out_3[7:4]));  // open: dp
  // Pins of 8 and 12 bits meet at {undriven, PC}
  // Pins of 8 and 12 bits meet at MAR_q

  // Notes on the sheet:
  //   Code Memory
  //   contents of rom_1 (hex, n*v repeats v):
  //   21208 111 45 1235 235 20ff 121d 547 5 75 7 45 45
  //   RESULT
endmodule

module register (
  input  [15:0] Data_in,
  input  R_W,
  input  [3:0] input01,
  input  [3:0] Input_02,
  input  Clock,
  output [15:0] Regi_out_01,
  output [15:0] Regi_out_02
);

  wire decoder_1_out0, decoder_1_out1, decoder_1_out2, decoder_1_out3, decoder_1_out4, decoder_1_out5,
       decoder_1_out6, decoder_1_out7, decoder_1_out8, decoder_1_out9, decoder_1_out10, decoder_1_out11,
       decoder_1_out12, decoder_1_out13, decoder_1_out14, decoder_1_out15, not_1_out;
  wire [15:0] R0_q, R1_q, R2_q, R3_q, R4_q, R5_q, R6_q, R7_q, R8_q, R9_q, R10_q, R11_q, R12_q, R13_q, R14_q,
       R15_q;

  Hex_Digit_Display hex_digit_display_1 (.value(Input_02));  // open: dp
  Decoder #(.select(4), .disabled(0)) decoder_1 (
    .out0(decoder_1_out0), .out1(decoder_1_out1), .out2(decoder_1_out2), .out3(decoder_1_out3),
    .out4(decoder_1_out4), .out5(decoder_1_out5), .out6(decoder_1_out6), .out7(decoder_1_out7),
    .out8(decoder_1_out8), .out9(decoder_1_out9), .out10(decoder_1_out10), .out11(decoder_1_out11),
    .out12(decoder_1_out12), .out13(decoder_1_out13), .out14(decoder_1_out14), .out15(decoder_1_out15),
    .sel(input01), .en(not_1_out));
  not not_1 (not_1_out, R_W);
  Hex_Digit_Display hex_digit_display_2 (.value(input01));  // open: dp
  Register #(.width(16)) R0 (.D(Data_in), .en(decoder_1_out0), .Q(R0_q), .clk(Clock));  // open: clr
  Register #(.width(16)) R2 (.D(Data_in), .en(decoder_1_out2), .Q(R2_q), .clk(Clock));  // open: clr
  Register #(.width(16)) R4 (.D(Data_in), .en(decoder_1_out4), .Q(R4_q), .clk(Clock));  // open: clr
  Register #(.width(16)) R6 (.D(Data_in), .en(decoder_1_out6), .Q(R6_q), .clk(Clock));  // open: clr
  Register #(.width(16)) R8 (.D(Data_in), .en(decoder_1_out8), .Q(R8_q), .clk(Clock));  // open: clr
  Register #(.width(16)) R10 (.D(Data_in), .en(decoder_1_out10), .Q(R10_q), .clk(Clock));  // open: clr
  Register #(.width(16)) R12 (.D(Data_in), .en(decoder_1_out12), .Q(R12_q), .clk(Clock));  // open: clr
  Register #(.width(16)) R14 (.D(Data_in), .en(decoder_1_out14), .Q(R14_q), .clk(Clock));  // open: clr
  Register #(.width(16)) R1 (.D(Data_in), .en(decoder_1_out1), .Q(R1_q), .clk(Clock));  // open: clr
  Register #(.width(16)) R3 (.D(Data_in), .en(decoder_1_out3), .Q(R3_q), .clk(Clock));  // open: clr
  Register #(.width(16)) R5 (.D(Data_in), .en(decoder_1_out5), .Q(R5_q), .clk(Clock));  // open: clr
  Register #(.width(16)) R7 (.D(Data_in), .en(decoder_1_out7), .Q(R7_q), .clk(Clock));  // open: clr
  Register #(.width(16)) R9 (.D(Data_in), .en(decoder_1_out9), .Q(R9_q), .clk(Clock));  // open: clr
  Register #(.width(16)) R11 (.D(Data_in), .en(decoder_1_out11), .Q(R11_q), .clk(Clock));  // open: clr
  Register #(.width(16)) R13 (.D(Data_in), .en(decoder_1_out13), .Q(R13_q), .clk(Clock));  // open: clr
  Register #(.width(16)) R15 (.D(Data_in), .en(decoder_1_out15), .Q(R15_q), .clk(Clock));  // open: clr
  Multiplexer #(.select(4), .width(16)) multiplexer_1 (
    .in0(R0_q), .in1(R1_q), .in2(R2_q), .in3(R3_q), .in4(R4_q), .in5(R5_q), .in6(R6_q), .in7(R7_q),
    .in8(R8_q), .in9(R9_q), .in10(R10_q), .in11(R11_q), .in12(R12_q), .in13(R13_q), .in14(R14_q),
    .in15(R15_q), .out(Regi_out_01), .sel(input01), .en(R_W));
  Multiplexer #(.select(4), .width(16), .disabled(0)) multiplexer_2 (
    .in0(R0_q), .in1(R1_q), .in2(R2_q), .in3(R3_q), .in4(R4_q), .in5(R5_q), .in6(R6_q), .in7(R7_q),
    .in8(R8_q), .in9(R9_q), .in10(R10_q), .in11(R11_q), .in12(R12_q), .in13(R13_q), .in14(R14_q),
    .in15(R15_q), .out(Regi_out_02), .sel(Input_02), .en(R_W));

  // Notes on the sheet:
  //   Register (4bits)
  //   Regi_Out_01
endmodule

// ALU
module Alu (
  input  [15:0] A,
  input  [15:0] B,
  input  [3:0] SELECT,
  output [31:0] ALU_output
);

  wire adder_1_cout, subtractor_1_bout;
  wire [3:0] bit_extender_2_out;
  wire [15:0] adder_1_out, adder_2_out, and_1_out, bit_extender_1_out, bit_extender_5_out,
       bit_extender_6_out, divider_1_out, divider_1_rem, multiplier_1_cout, multiplier_1_out, not_1_out,
       or_1_out, shifter_1_out, shifter_2_out, shifter_3_out, shifter_4_out, subtractor_1_out,
       subtractor_2_out;
  wire [31:0] bit_extender_3_out, bit_extender_4_out, bit_extender_7_out, bit_extender_8_out,
       bit_extender_9_out, bit_extender_10_out, bit_extender_11_out, bit_extender_12_out,
       bit_extender_13_out, bit_extender_14_out, bit_extender_15_out;

  assign bit_extender_1_out = {{15{1'b0}}, 1'b1};  // Bit_Extender bit_extender_1
  Bit_Extender #(.in_width(16), .out_width(4)) bit_extender_2 (.in(B), .out(bit_extender_2_out));
  assign bit_extender_3_out = {{16{1'b0}}, B};  // Bit_Extender bit_extender_3
  assign bit_extender_4_out = {{16{1'b0}}, A};  // Bit_Extender bit_extender_4
  Adder #(.width(16)) adder_1 (.a(A), .b(B), .out(adder_1_out), .cout(adder_1_cout));  // open: cin
  Subtractor #(.width(16)) subtractor_1 (.a(A), .b(B), .out(subtractor_1_out), .bout(subtractor_1_bout));  // open: bin
  Multiplier #(.width(16)) multiplier_1 (.a(A), .b(B), .out(multiplier_1_out), .cout(multiplier_1_cout));  // open: cin
  Divider #(.width(16)) divider_1 (.a(A), .b(B), .out(divider_1_out), .rem(divider_1_rem));  // open: upper
  Adder #(.width(16)) adder_2 (.a(A), .b(bit_extender_1_out), .out(adder_2_out));  // open: cin, cout
  Subtractor #(.width(16)) subtractor_2 (.a(A), .b(bit_extender_1_out), .out(subtractor_2_out));  // open: bin, bout
  assign and_1_out = A & B;  // AND_Gate and_1, 16 bits wide
  assign or_1_out = A | B;  // OR_Gate or_1, 16 bits wide
  assign not_1_out = ~A;  // NOT_Gate not_1, 16 bits wide
  Shifter #(.width(16), .shift("lr")) shifter_1 (.in(A), .\dist (bit_extender_2_out), .out(shifter_1_out));
  Shifter #(.width(16)) shifter_2 (.in(A), .\dist (bit_extender_2_out), .out(shifter_2_out));
  Shifter #(.width(16), .shift("rr")) shifter_3 (.in(A), .\dist (bit_extender_2_out), .out(shifter_3_out));
  Shifter #(.width(16), .shift("rl")) shifter_4 (.in(A), .\dist (bit_extender_2_out), .out(shifter_4_out));
  assign bit_extender_5_out = {{15{1'b0}}, adder_1_cout};  // Bit_Extender bit_extender_5
  assign bit_extender_6_out = {{15{1'b0}}, subtractor_1_bout};  // Bit_Extender bit_extender_6
  assign bit_extender_7_out = {{16{1'b0}}, adder_2_out};  // Bit_Extender bit_extender_7
  assign bit_extender_8_out = {{16{1'b0}}, subtractor_2_out};  // Bit_Extender bit_extender_8
  assign bit_extender_9_out = {{16{1'b0}}, and_1_out};  // Bit_Extender bit_extender_9
  assign bit_extender_10_out = {{16{1'b0}}, or_1_out};  // Bit_Extender bit_extender_10
  assign bit_extender_11_out = {{16{1'b0}}, not_1_out};  // Bit_Extender bit_extender_11
  assign bit_extender_12_out = {{16{1'b0}}, shifter_1_out};  // Bit_Extender bit_extender_12
  assign bit_extender_13_out = {{16{1'b0}}, shifter_2_out};  // Bit_Extender bit_extender_13
  assign bit_extender_14_out = {{16{1'b0}}, shifter_3_out};  // Bit_Extender bit_extender_14
  assign bit_extender_15_out = {{16{1'b0}}, shifter_4_out};  // Bit_Extender bit_extender_15
  Multiplexer #(.select(4), .width(32), .disabled(0)) multiplexer_1 (
    .in0(bit_extender_3_out), .in1(bit_extender_4_out), .in2({bit_extender_5_out, adder_1_out}),
    .in3({bit_extender_6_out, subtractor_1_out}), .in4({multiplier_1_cout, multiplier_1_out}),
    .in5({divider_1_rem, divider_1_out}), .in6(bit_extender_7_out), .in7(bit_extender_8_out),
    .in8(bit_extender_9_out), .in9(bit_extender_10_out), .in10(bit_extender_11_out), .in11({A, B}),
    .in12(bit_extender_12_out), .in13(bit_extender_13_out), .in14(bit_extender_14_out),
    .in15(bit_extender_15_out), .out(ALU_output), .sel(SELECT));  // open: en

  // Notes on the sheet:
  //   BitExtender
  //   Increment-----------------------------
  //   Decrement-----------------------
  //   Exchange
  //   Load
  //   Store
  //   Add
  //   Sub
  //   Mul
  //   Div
  //   And
  //   OR
  //   ShiftRight
  //   ShiftLeft
  //   Rotateright
  //   RotateLeft
  //   ALU-8bit 
  //   Not
  //   0-adder|1-sub|2-mpy|3-div|4-and|5-or|6-xnor|7-xor|8-lls|9-lrs|10-ars|11-rr|12-rl
endmodule

module pc (
  input  [7:0] PC_INput,
  input  PC_enable,
  input  Clock,
  input  PC_reset,
  output [7:0] PC_OUT
);

  wire [7:0] adder_1_out;

  Hex_Digit_Display hex_digit_display_1 (.value(PC_INput[3:0]));  // open: dp
  Hex_Digit_Display hex_digit_display_2 (.value(PC_INput[7:4]));  // open: dp
  Adder adder_1 (.a(PC_INput), .b(PC_OUT), .out(adder_1_out), .cin(1'b1));  // open: cout
  Hex_Digit_Display hex_digit_display_3 (.value(PC_OUT[7:4]));  // open: dp
  Register register_1 (.D(adder_1_out), .en(PC_enable), .Q(PC_OUT), .clk(Clock), .clr(PC_reset));
  Hex_Digit_Display hex_digit_display_4 (.value(PC_OUT[3:0]));  // open: dp
endmodule
