// Logisim project 1st processor.circ as structural Verilog: 2 circuits, main circuit main
module main (
  input  [3:0] A,
  input  [3:0] B,
  input  [2:0] OPCODE,
  input  [10:0] in_4,
  output [7:0] RESULT,
  output [7:0] RESULT_2
);

  Hex_Digit_Display hex_digit_display_1 (.value(A));  // open: dp
  Hex_Digit_Display hex_digit_display_2 (.value(B));  // open: dp
  Hex_Digit_Display hex_digit_display_3 (.value(RESULT[7:4]));  // open: dp
  ALU alu_1 (.A_4bits(A), .B_4bits(B), .OPCODE_3bits(OPCODE), .out_4(RESULT));
  ALU alu_2 (.A_4bits(in_4[3:0]), .B_4bits(in_4[7:4]), .OPCODE_3bits(in_4[10:8]), .out_4(RESULT_2));
  Hex_Digit_Display hex_digit_display_4 (.value(RESULT[3:0]));  // open: dp

  // Notes on the sheet:
  //   ALU
endmodule

module ALU (
  input  [3:0] A_4bits,
  input  [3:0] B_4bits,
  input  [2:0] OPCODE_3bits,
  output [7:0] out_4
);

  wire adder_1_cout, subtractor_1_bout;
  wire [3:0] adder_1_out, and_1_out, bit_extender_1_out, bit_extender_2_out, divider_1_out, divider_1_rem,
       multiplier_1_cout, multiplier_1_out, nor_1_out, or_1_out, subtractor_1_out, xor_1_out;

  Hex_Digit_Display hex_digit_display_1 (.value(B_4bits));  // open: dp
  Hex_Digit_Display hex_digit_display_2 (.value(A_4bits));  // open: dp
  Adder #(.width(4)) adder_1 (.a(A_4bits), .b(B_4bits), .out(adder_1_out), .cout(adder_1_cout));  // open: cin
  Subtractor #(.width(4)) subtractor_1 (
    .a(A_4bits), .b(B_4bits), .out(subtractor_1_out), .bout(subtractor_1_bout));  // open: bin
  Multiplier #(.width(4)) multiplier_1 (
    .a(A_4bits), .b(B_4bits), .out(multiplier_1_out), .cout(multiplier_1_cout));  // open: cin
  Divider #(.width(4)) divider_1 (.a(A_4bits), .b(B_4bits), .out(divider_1_out), .rem(divider_1_rem));  // open: upper
  assign and_1_out = A_4bits & B_4bits;  // AND_Gate and_1, 4 bits wide
  assign or_1_out = A_4bits | B_4bits;  // OR_Gate or_1, 4 bits wide
  assign nor_1_out = ~(A_4bits | B_4bits);  // NOR_Gate nor_1, 4 bits wide
  assign xor_1_out = A_4bits ^ B_4bits;  // XOR_Gate xor_1, 4 bits wide
  assign bit_extender_1_out = {{3{1'b0}}, adder_1_cout};  // Bit_Extender bit_extender_1
  assign bit_extender_2_out = {{3{1'b0}}, subtractor_1_bout};  // Bit_Extender bit_extender_2
  Multiplexer #(.select(3), .width(8), .enable("false")) multiplexer_1 (
    .in0({bit_extender_1_out, adder_1_out}), .in1({bit_extender_2_out, subtractor_1_out}),
    .in2({multiplier_1_cout, multiplier_1_out}), .in3({divider_1_rem, divider_1_out}),
    .in4({4'b0000, and_1_out}), .in5({4'b0000, or_1_out}), .in6({4'b0000, nor_1_out}),
    .in7({4'b0000, xor_1_out}), .out(out_4), .sel(OPCODE_3bits));
  Hex_Digit_Display hex_digit_display_3 (.value(out_4[7:4]));  // open: dp
  Hex_Digit_Display hex_digit_display_4 (.value(out_4[3:0]));  // open: dp

  // Notes on the sheet:
  //   Subtractor-------------------------------->
  //   Multiplier-------------------------------->
  //   Divider-------------------------------->
  //   AND-------------------------------->
  //   NOR-------------------------------->
  //   EX-NOR-------------------------------->
  //   OR-------------------------------->
  //   Adder
  //   ALU
  //   Bits extendor
  //   Spiltter
  //   Multiplexer
endmodule
