// Logisim project 8_bit_2_add_register[1][1].circ as structural Verilog: 5 circuits, main circuit main
module main (
  input  [11:0] PC_in,
  output [11:0] PC,
  output [15:0] RESULT,
  output out_4,
  output out_5,
  output out_6,
  output out_7,
  output out_8,
  output out_9,
  output out_10,
  output out_11
);

  wire clock, not_1_out, RESET, undriven;
  wire [3:0] CC;
  wire [7:0] RA_2_q, RA_q, REG_output16bit, REG_output16bit_2, RZ_q;
  wire [11:0] MAR_q, MBR_q, rom_1_data;

  PC u_PC (.PC_In(PC_in), .Clock(clock), .PC_Enable(undriven), .Reset(RESET), .PC_Out(PC));
  Register #(.width(12)) MAR (.D(PC), .en(clock), .Q(MAR_q), .clk(clock), .clr(RESET));
  Shift_Register #(.length(4)) shift_register_1 (
    .in(undriven), .clk(clock));  // open: shift, out, load, clr, d0, q0, d1, q1, d2, q2, d3, q3
  Clock_Cycle u_CLOCK (.Clock(clock), .reset(RESET), .out_3(CC));
  ROM #(.addrWidth(12), .dataWidth(12)) rom_1 (.addr(MAR_q), .data(rom_1_data));  // open: sel
  Hex_Digit_Display hex_digit_display_1 (.value(CC));  // open: dp
  Button button_1 (.out(clock));
  not not_1 (not_1_out, undriven);
  Register #(.width(12)) MBR (.D(rom_1_data), .Q(MBR_q), .clk(clock), .clr(RESET));  // open: en
  Button button_2 (.out(RESET));
  Register RA (.D(REG_output16bit), .Q(RA_q), .clk(clock), .clr(RESET));  // open: en
  Reg_file_16 REG (
    .INPUT(RZ_q), .CLOCK(clock), .READ_WRITE(not_1_out), .SELECTBITS4BIT(MBR_q[7:4]),
    .SELECTBITS4BIT_2(MBR_q[3:0]), .OUTPUT16BIT(REG_output16bit), .OUTPUT16BIT_2(REG_output16bit_2));
  Register RA_2 (.D(REG_output16bit_2), .Q(RA_2_q), .clk(clock), .clr(RESET));  // open: en
  Register RZ (.D(RESULT[7:0]), .Q(RZ_q), .clk(clock), .clr(RESET));  // open: en
  ALU_Final ALU (
    .A(RA_q), .B(RA_2_q), .in_3(clock), .OPERATION(MBR_q[11:8]), .RESULT(RESULT), .out_6(out_10),
    .out_7(out_11), .out_8(out_5), .out_9(out_6), .out_10(out_4), .out_11(out_9), .out_12(out_8),
    .out_13(out_7));
  Hex_Digit_Display hex_digit_display_2 (.value(RESULT[3:0]));  // open: dp
  Hex_Digit_Display hex_digit_display_3 (.value(RESULT[7:4]));  // open: dp

  // Other names for the same wires on the sheet: Carry = out_10; Even_Parity = out_8; Half_Carry = out_11;
  //   Negative = out_6; Odd_Parity = out_9; Overflow_Flag = out_7; Positive = out_5; Zero_Flag = out_4

  // Notes on the sheet:
  //   10000
  //   Code Memory
  //   contents of rom_1 (hex, n*v repeats v):
  //   212 23 4 3 12 11 14 11 14*0 1
  //   CLOCK
  //   PROGRAM STATUS WORD(PSW)
  //   RESULT
endmodule

module PC (
  input  [11:0] PC_In,
  input  Clock,
  input  PC_Enable,
  input  Reset,
  output [11:0] PC_Out
);

  wire [11:0] adder_1_out;

  Adder #(.width(12)) adder_1 (.a(PC_In), .b(PC_Out), .out(adder_1_out), .cin(1'b1));  // open: cout
  Register #(.width(12)) register_1 (.D(adder_1_out), .en(PC_Enable), .Q(PC_Out), .clk(Clock), .clr(Reset));
  Hex_Digit_Display hex_digit_display_1 (.value(PC_Out[11:8]));  // open: dp
  Hex_Digit_Display hex_digit_display_2 (.value(PC_Out[7:4]));  // open: dp
  Hex_Digit_Display hex_digit_display_3 (.value(PC_Out[3:0]));  // open: dp
endmodule

module Clock_Cycle (
  input  Clock,
  input  reset,
  output [3:0] out_3
);

  Counter #(.width(4), .max('h4)) counter_1 (.Q(out_3), .clk(Clock), .clr(reset));  // open: load, D, count, carry
endmodule

// REG
module Reg_file_16 (
  input  [7:0] INPUT,
  input  CLOCK,
  input  READ_WRITE,
  input  [3:0] SELECTBITS4BIT,
  input  [3:0] SELECTBITS4BIT_2,
  output [7:0] OUTPUT16BIT,
  output [7:0] OUTPUT16BIT_2
);

  wire decoder_1_out0, decoder_1_out1, decoder_1_out2, decoder_1_out3, decoder_1_out4, decoder_1_out5,
       decoder_1_out6, decoder_1_out7, decoder_1_out8, decoder_1_out9, decoder_1_out10, decoder_1_out11,
       decoder_1_out12, decoder_1_out13, decoder_1_out14, decoder_1_out15, not_1_out;
  wire [7:0] R0_q, R1_q, R2_q, R3_q, R4_q, R5_q, R6_q, R7_q, R8_q, R9_q, R10_q, R11_q, R12_q, R13_q, R14_q,
       R15_q;

  not not_1 (not_1_out, READ_WRITE);
  Decoder #(.select(4), .disabled(0)) decoder_1 (
    .out0(decoder_1_out0), .out1(decoder_1_out1), .out2(decoder_1_out2), .out3(decoder_1_out3),
    .out4(decoder_1_out4), .out5(decoder_1_out5), .out6(decoder_1_out6), .out7(decoder_1_out7),
    .out8(decoder_1_out8), .out9(decoder_1_out9), .out10(decoder_1_out10), .out11(decoder_1_out11),
    .out12(decoder_1_out12), .out13(decoder_1_out13), .out14(decoder_1_out14), .out15(decoder_1_out15),
    .sel(SELECTBITS4BIT), .en(not_1_out));
  Register R0 (.D(INPUT), .en(decoder_1_out0), .Q(R0_q), .clk(CLOCK));  // open: clr
  Register R1 (.D(INPUT), .en(decoder_1_out1), .Q(R1_q), .clk(CLOCK));  // open: clr
  Register R2 (.D(INPUT), .en(decoder_1_out2), .Q(R2_q), .clk(CLOCK));  // open: clr
  Register R3 (.D(INPUT), .en(decoder_1_out3), .Q(R3_q), .clk(CLOCK));  // open: clr
  Register R4 (.D(INPUT), .en(decoder_1_out4), .Q(R4_q), .clk(CLOCK));  // open: clr
  Register R5 (.D(INPUT), .en(decoder_1_out5), .Q(R5_q), .clk(CLOCK));  // open: clr
  Register R6 (.D(INPUT), .en(decoder_1_out6), .Q(R6_q), .clk(CLOCK));  // open: clr
  Register R7 (.D(INPUT), .en(decoder_1_out7), .Q(R7_q), .clk(CLOCK));  // open: clr
  Register R8 (.D(INPUT), .en(decoder_1_out8), .Q(R8_q), .clk(CLOCK));  // open: clr
  Register R9 (.D(INPUT), .en(decoder_1_out9), .Q(R9_q), .clk(CLOCK));  // open: clr
  Register R10 (.D(INPUT), .en(decoder_1_out10), .Q(R10_q), .clk(CLOCK));  // open: clr
  Register R11 (.D(INPUT), .en(decoder_1_out11), .Q(R11_q), .clk(CLOCK));  // open: clr
  Register R12 (.D(INPUT), .en(decoder_1_out12), .Q(R12_q), .clk(CLOCK));  // open: clr
  Register R13 (.D(INPUT), .en(decoder_1_out13), .Q(R13_q), .clk(CLOCK));  // open: clr
  Register R14 (.D(INPUT), .en(decoder_1_out14), .Q(R14_q), .clk(CLOCK));  // open: clr
  Register R15 (.D(INPUT), .en(decoder_1_out15), .Q(R15_q), .clk(CLOCK));  // open: clr
  Multiplexer #(.select(4), .width(8), .disabled(0)) multiplexer_1 (
    .in0(R0_q), .in1(R1_q), .in2(R2_q), .in3(R3_q), .in4(R4_q), .in5(R5_q), .in6(R6_q), .in7(R7_q),
    .in8(R8_q), .in9(R9_q), .in10(R10_q), .in11(R11_q), .in12(R12_q), .in13(R13_q), .in14(R14_q),
    .in15(R15_q), .out(OUTPUT16BIT), .sel(SELECTBITS4BIT), .en(READ_WRITE));
  Multiplexer #(.select(4), .width(8), .disabled(0)) multiplexer_2 (
    .in0(R0_q), .in1(R1_q), .in2(R2_q), .in3(R3_q), .in4(R4_q), .in5(R5_q), .in6(R6_q), .in7(R7_q),
    .in8(R8_q), .in9(R9_q), .in10(R10_q), .in11(R11_q), .in12(R12_q), .in13(R13_q), .in14(R14_q),
    .in15(R15_q), .out(OUTPUT16BIT_2), .sel(SELECTBITS4BIT_2), .en(READ_WRITE));
endmodule

// ALU
module ALU_Final (
  input  [7:0] A,
  input  [7:0] B,
  input  in_3,
  input  [3:0] OPERATION,
  output [15:0] RESULT,
  output out_6,
  output out_7,
  output out_8,
  output out_9,
  output out_10,
  output out_11,
  output out_12,
  output out_13
);

  wire adder_1_cout, or_2_out, or_3_out, subtractor_1_bout;
  wire [7:0] adder_1_out, adder_2_out, and_1_out, bit_extender_1_out, bit_extender_2_out, bit_extender_3_out,
       bit_extender_4_out, divider_1_out, divider_1_rem, multiplier_1_cout, multiplier_1_out, not_1_out,
       or_1_out, shifter_1_out, shifter_2_out, shifter_3_out, shifter_4_out, subtractor_1_out,
       subtractor_2_out;

  assign bit_extender_1_out = {{7{1'b0}}, 1'b0};  // Bit_Extender bit_extender_1
  assign bit_extender_2_out = {{7{1'b0}}, 1'b0};  // Bit_Extender bit_extender_2
  Adder adder_1 (.a(A), .b(B), .out(adder_1_out), .cout(adder_1_cout));  // open: cin
  Subtractor subtractor_1 (.a(A), .b(B), .out(subtractor_1_out), .bout(subtractor_1_bout));  // open: bin
  Multiplier multiplier_1 (.a(A), .b(B), .out(multiplier_1_out), .cout(multiplier_1_cout));  // open: cin
  Divider divider_1 (.a(A), .b(B), .out(divider_1_out), .rem(divider_1_rem));  // open: upper
  Adder adder_2 (.a(A), .b(8'h1), .out(adder_2_out), .cin(1'b1));  // open: cout
  Subtractor subtractor_2 (.a(A), .b(8'h1), .out(subtractor_2_out), .bin(1'b1));  // open: bout
  assign or_1_out = A | B;  // OR_Gate or_1, 8 bits wide
  assign not_1_out = ~A;  // NOT_Gate not_1, 8 bits wide
  Shifter #(.shift("lr")) shifter_1 (.in(A), .\dist (3'b111), .out(shifter_1_out));
  Shifter shifter_2 (.in(A), .\dist (3'b111), .out(shifter_2_out));
  Shifter #(.shift("rr")) shifter_3 (.in(A), .\dist (3'b111), .out(shifter_3_out));
  Shifter #(.shift("rl")) shifter_4 (.in(A), .\dist (3'b111), .out(shifter_4_out));
  assign bit_extender_3_out = {{7{1'b0}}, adder_1_cout};  // Bit_Extender bit_extender_3
  assign bit_extender_4_out = {{7{1'b0}}, subtractor_1_bout};  // Bit_Extender bit_extender_4
  assign and_1_out = A & B;  // AND_Gate and_1, 8 bits wide
  Multiplexer #(.enable("false")) multiplexer_1 (.in0(adder_1_cout), .in1(subtractor_1_bout), .out(out_6), .sel(in_3));
  Multiplexer #(.select(4), .width(16), .enable("false")) multiplexer_2 (
    .in0({bit_extender_2_out, B}), .in1({bit_extender_2_out, B}), .in2({bit_extender_3_out, adder_1_out}),
    .in3({bit_extender_4_out, subtractor_1_out}), .in4({multiplier_1_cout, multiplier_1_out}),
    .in5({divider_1_rem, divider_1_out}), .in6({bit_extender_1_out, adder_2_out}),
    .in7({bit_extender_1_out, subtractor_2_out}), .in8({bit_extender_1_out, and_1_out}),
    .in9({bit_extender_1_out, or_1_out}), .in10({bit_extender_1_out, not_1_out}), .in11({A, B}),
    .in12({bit_extender_1_out, shifter_1_out}), .in13({bit_extender_1_out, shifter_2_out}),
    .in14({bit_extender_1_out, shifter_3_out}), .in15({bit_extender_1_out, shifter_4_out}),
    .out({RESULT[15:8], out_9, RESULT[6:0]}), .sel(OPERATION));
  or or_2 (or_2_out, RESULT[0], RESULT[1], RESULT[2], RESULT[3], RESULT[4], RESULT[5], RESULT[6], out_9, RESULT[8], RESULT[9], RESULT[10], RESULT[11], RESULT[12], RESULT[13], RESULT[14], RESULT[15]);
  not not_2 (out_7, or_2_out);
  xor odd_parity_1 (out_11, RESULT[0], RESULT[1], RESULT[2], RESULT[3], RESULT[4], RESULT[5], RESULT[6], out_9, RESULT[8], RESULT[9], RESULT[10], RESULT[11], RESULT[12], RESULT[13], RESULT[14], RESULT[15]);
  xnor even_parity_1 (out_12, RESULT[0], RESULT[1], RESULT[2], RESULT[3], RESULT[4], RESULT[5], RESULT[6], out_9, RESULT[8], RESULT[9], RESULT[10], RESULT[11], RESULT[12], RESULT[13], RESULT[14], RESULT[15]);
  and and_2 (out_13, RESULT[0], RESULT[1], RESULT[2], RESULT[3], RESULT[4], RESULT[5], RESULT[6], out_9, RESULT[8], RESULT[9], RESULT[10], RESULT[11], RESULT[12], RESULT[13], RESULT[14], RESULT[15]);
  not not_3 (out_8, out_9);
  or or_3 (or_3_out, RESULT[0], RESULT[1], RESULT[2], RESULT[3], RESULT[4], RESULT[5], RESULT[6], out_9);
  not not_4 (out_10, or_3_out);

  assign RESULT[7] = out_9;

  // Other names for the same wires on the sheet: Carry = out_6; Even_parity = out_12; Half_carry = out_10;
  //   Odd_parity = out_11; Overflow_flag = out_13; Positive = out_8; Negative = out_9; Zero_flag = out_7
endmodule
