// Logisim project COAA Day 18.circ as structural Verilog: 4 circuits, main circuit main
module main (
  input  [15:0] in_1,
  output [15:0] out_2,
  output Carry
);

  wire CLOCK, not_1_out, not_2_out, RESET, shift_register_1_out, shift_register_1_q2, shift_register_2_out;
  wire [3:0] alupractise_1_output, alupractise_1_output_2, alupractise_1_output_3, alupractise_1_output_4,
       alupractise_1_output_5, alupractise_1_output_6, alupractise_1_output_7, alupractise_1_output_8,
       bit_extender_1_out, IR_q_2;
  wire [11:0] demultiplexer_1_out0, demultiplexer_1_out1, IR_q;
  wire [15:0] ACC_q, MAR_q, MBR_q, ram_1_data, register_2_q, registerpractise_1_data_out_8_bits, rom_1_data;
  wire [31:0] register_1_q;

  Button button_1 (.out(CLOCK));
  Button button_2 (.out(RESET));
  PCpractise PC (.PC_Input(in_1), .PC_Enable(shift_register_1_out), .Clock(CLOCK), .PC_Output(out_2), .PC_Reset(RESET));
  Shift_Register #(.length(5)) shift_register_1 (
    .in(shift_register_1_out), .clk(CLOCK), .out(shift_register_1_out), .q2(shift_register_1_q2));  // open: shift, load, clr, d0, q0, d1, q1, d2, d3, q3, d4, q4
  Register #(.width(16)) MAR (.D(out_2), .Q(MAR_q), .clk(CLOCK), .clr(RESET));  // open: en
  Shift_Register #(.length(5)) shift_register_2 (
    .in(shift_register_2_out), .clk(CLOCK), .out(shift_register_2_out));  // open: shift, load, clr, d0, q0, d1, q1, d2, q2, d3, q3, d4, q4
  ROM #(.addrWidth(16), .dataWidth(16)) rom_1 (.addr(MAR_q), .data(rom_1_data));  // open: sel
  Register #(.width(16)) MBR (.D(rom_1_data), .Q(MBR_q), .clk(CLOCK), .clr(RESET));  // open: en
  Demultiplexer #(.width(12), .disabled(0)) demultiplexer_1 (
    .out0(demultiplexer_1_out0), .out1(demultiplexer_1_out1), .in(IR_q), .sel(not_1_out));  // open: en
  Register #(.width(16)) IR (.D(MBR_q), .Q({IR_q_2, IR_q}), .clk(CLOCK), .clr(RESET));  // open: en
  not not_1 (not_1_out, shift_register_1_q2);
  Bit_Extender #(.in_width(12), .out_width(4)) bit_extender_1 (.in(demultiplexer_1_out0), .out(bit_extender_1_out));
  Registerpractise registerpractise_1 (
    .DATA_BITS(register_1_q[15:0]), .Input(bit_extender_1_out), .Clock(CLOCK), .R_W(shift_register_2_out),
    .Data_out_8_Bits(registerpractise_1_data_out_8_bits));
  not not_2 (not_2_out, not_1_out);
  Register #(.width(16)) ACC (
    .D(registerpractise_1_data_out_8_bits), .en(not_2_out), .Q(ACC_q), .clk(CLOCK), .clr(RESET));
  RAM #(.addrWidth(12), .dataWidth(16), .bus("separate")) ram_1 (
    .addr(demultiplexer_1_out1), .data(ram_1_data));  // open: din, str, sel, clk, ld, clr
  Register #(.width(32)) register_1 (
    .D({alupractise_1_output_8, alupractise_1_output_7, alupractise_1_output_6, alupractise_1_output_5, alupractise_1_output_4, alupractise_1_output_3, alupractise_1_output_2, alupractise_1_output}),
    .Q(register_1_q), .clk(CLOCK), .clr(RESET));  // open: en
  Register #(.width(16)) register_2 (.D(ram_1_data), .Q(register_2_q), .clk(CLOCK), .clr(RESET));  // open: en
  ALUpractise alupractise_1 (
    .A(ACC_q), .B(register_2_q), .OpCode(IR_q_2), .CARRY(Carry),
    .Output({alupractise_1_output_8, alupractise_1_output_7, alupractise_1_output_6, alupractise_1_output_5, alupractise_1_output_4, alupractise_1_output_3, alupractise_1_output_2, alupractise_1_output}));
  Hex_Digit_Display hex_digit_display_1 (.value(alupractise_1_output_7));  // open: dp
  Hex_Digit_Display hex_digit_display_2 (.value(alupractise_1_output_8));  // open: dp
  Hex_Digit_Display hex_digit_display_3 (.value(alupractise_1_output_6));  // open: dp
  Hex_Digit_Display hex_digit_display_4 (.value(alupractise_1_output_5));  // open: dp
  Hex_Digit_Display hex_digit_display_5 (.value(alupractise_1_output_3));  // open: dp
  Hex_Digit_Display hex_digit_display_6 (.value(alupractise_1_output_4));  // open: dp
  Hex_Digit_Display hex_digit_display_7 (.value(alupractise_1_output));  // open: dp
  Hex_Digit_Display hex_digit_display_8 (.value(alupractise_1_output_2));  // open: dp

  // Notes on the sheet:
  //   10000
  //   01110
  //   contents of rom_1 (hex, n*v repeats v):
  //   1 21 12
  //   COA PROJECT
endmodule

module ALUpractise (
  input  [15:0] A,
  input  [15:0] B,
  input  [3:0] OpCode,
  output CARRY,
  output [31:0] Output
);

  wire adder_1_cout, adder_2_cout, subtractor_1_bout, subtractor_2_bout;
  wire [3:0] bit_extender_1_out, bit_extender_2_out, bit_extender_3_out, bit_extender_4_out;
  wire [15:0] adder_1_out, adder_2_out, and_1_out, bit_extender_7_out, bit_extender_8_out,
       bit_extender_9_out, bit_extender_13_out, divider_1_out, divider_1_rem, multiplier_1_cout,
       multiplier_1_out, not_1_out, or_1_out, shifter_1_out, shifter_2_out, shifter_3_out, shifter_4_out,
       subtractor_1_out, subtractor_2_out;
  wire [31:0] bit_extender_5_out, bit_extender_6_out, bit_extender_10_out, bit_extender_11_out,
       bit_extender_12_out, bit_extender_14_out, bit_extender_15_out, bit_extender_16_out,
       bit_extender_17_out;

  Bit_Extender #(.in_width(16), .out_width(4)) bit_extender_1 (.in(B), .out(bit_extender_1_out));
  Bit_Extender #(.in_width(16), .out_width(4)) bit_extender_2 (.in(B), .out(bit_extender_2_out));
  Bit_Extender #(.in_width(16), .out_width(4)) bit_extender_3 (.in(B), .out(bit_extender_3_out));
  Bit_Extender #(.in_width(16), .out_width(4)) bit_extender_4 (.in(B), .out(bit_extender_4_out));
  Adder #(.width(16)) adder_1 (.a(A), .b(B), .out(adder_1_out), .cout(adder_1_cout));  // open: cin
  Subtractor #(.width(16)) subtractor_1 (.a(A), .b(B), .out(subtractor_1_out), .bout(subtractor_1_bout));  // open: bin
  Multiplier #(.width(16)) multiplier_1 (.a(A), .b(B), .out(multiplier_1_out), .cout(multiplier_1_cout));  // open: cin
  Divider #(.width(16)) divider_1 (.a(A), .b(B), .out(divider_1_out), .rem(divider_1_rem));  // open: upper
  Adder #(.width(16)) adder_2 (.a(A), .b(16'h1), .out(adder_2_out), .cout(adder_2_cout));  // open: cin
  Subtractor #(.width(16)) subtractor_2 (
    .a(A), .b(16'h1), .out(subtractor_2_out), .bout(subtractor_2_bout));  // open: bin
  assign and_1_out = A & B;  // AND_Gate and_1, 16 bits wide
  assign or_1_out = A | B;  // OR_Gate or_1, 16 bits wide
  assign not_1_out = ~A;  // NOT_Gate not_1, 16 bits wide
  assign bit_extender_5_out = {{16{1'b0}}, A};  // Bit_Extender bit_extender_5
  assign bit_extender_6_out = {{16{1'b0}}, B};  // Bit_Extender bit_extender_6
  assign bit_extender_7_out = {{15{1'b0}}, adder_1_cout};  // Bit_Extender bit_extender_7
  assign bit_extender_8_out = {{15{1'b0}}, subtractor_1_bout};  // Bit_Extender bit_extender_8
  assign bit_extender_9_out = {{15{1'b0}}, adder_2_cout};  // Bit_Extender bit_extender_9
  assign bit_extender_10_out = {{16{1'b0}}, and_1_out};  // Bit_Extender bit_extender_10
  assign bit_extender_11_out = {{16{1'b0}}, or_1_out};  // Bit_Extender bit_extender_11
  assign bit_extender_12_out = {{16{1'b0}}, not_1_out};  // Bit_Extender bit_extender_12
  Shifter #(.width(16), .shift("lr")) shifter_1 (.in(A), .\dist (bit_extender_1_out), .out(shifter_1_out));
  Shifter #(.width(16)) shifter_2 (.in(A), .\dist (bit_extender_2_out), .out(shifter_2_out));
  Shifter #(.width(16), .shift("rr")) shifter_3 (.in(A), .\dist (bit_extender_3_out), .out(shifter_3_out));
  Shifter #(.width(16), .shift("rl")) shifter_4 (.in(A), .\dist (bit_extender_4_out), .out(shifter_4_out));
  assign bit_extender_13_out = {{15{1'b0}}, subtractor_2_bout};  // Bit_Extender bit_extender_13
  assign bit_extender_14_out = {{16{1'b0}}, shifter_1_out};  // Bit_Extender bit_extender_14
  assign bit_extender_15_out = {{16{1'b0}}, shifter_2_out};  // Bit_Extender bit_extender_15
  assign bit_extender_16_out = {{16{1'b0}}, shifter_3_out};  // Bit_Extender bit_extender_16
  assign bit_extender_17_out = {{16{1'b0}}, shifter_4_out};  // Bit_Extender bit_extender_17
  or or_2 (CARRY, adder_1_cout, subtractor_1_bout);
  Multiplexer #(.select(4), .width(32)) multiplexer_1 (
    .in0(bit_extender_6_out), .in1(bit_extender_5_out), .in2({bit_extender_7_out, adder_1_out}),
    .in3({bit_extender_8_out, subtractor_1_out}), .in4({multiplier_1_cout, multiplier_1_out}),
    .in5({divider_1_rem, divider_1_out}), .in6({bit_extender_9_out, adder_2_out}),
    .in7({bit_extender_13_out, subtractor_2_out}), .in8(bit_extender_10_out), .in9(bit_extender_11_out),
    .in10(bit_extender_12_out), .in11({A, B}), .in12(bit_extender_14_out), .in13(bit_extender_15_out),
    .in14(bit_extender_16_out), .in15(bit_extender_17_out), .out(Output), .sel(OpCode));  // open: en
  Hex_Digit_Display hex_digit_display_1 (.value(Output[27:24]));  // open: dp
  Hex_Digit_Display hex_digit_display_2 (.value(Output[31:28]));  // open: dp
  Hex_Digit_Display hex_digit_display_3 (.value(Output[23:20]));  // open: dp
  Hex_Digit_Display hex_digit_display_4 (.value(Output[19:16]));  // open: dp
  Hex_Digit_Display hex_digit_display_5 (.value(Output[11:8]));  // open: dp
  Hex_Digit_Display hex_digit_display_6 (.value(Output[15:12]));  // open: dp
  Hex_Digit_Display hex_digit_display_7 (.value(Output[7:4]));  // open: dp
  Hex_Digit_Display hex_digit_display_8 (.value(Output[3:0]));  // open: dp

  // Notes on the sheet:
  //   A
  //   B
endmodule

module Registerpractise (
  input  [15:0] DATA_BITS,
  input  [3:0] Input,
  input  Clock,
  input  R_W,
  output [15:0] Data_out_8_Bits
);

  wire decoder_1_out0, decoder_1_out1, decoder_1_out2, decoder_1_out3, decoder_1_out4, decoder_1_out5,
       decoder_1_out6, decoder_1_out7, decoder_1_out8, decoder_1_out9, decoder_1_out10, decoder_1_out11,
       decoder_1_out12, decoder_1_out13, decoder_1_out14, decoder_1_out15, not_1_out;
  wire [15:0] R0_q, R1_q, R2_q, R3_q, R5_q, R6_q, R7_q, R8_q, R9_q, R10_q, R11_q, R12_q, R13_q, R14_q, R15_q,
       register_1_q;

  not not_1 (not_1_out, R_W);
  Decoder #(.select(4), .disabled(0)) decoder_1 (
    .out0(decoder_1_out0), .out1(decoder_1_out1), .out2(decoder_1_out2), .out3(decoder_1_out3),
    .out4(decoder_1_out4), .out5(decoder_1_out5), .out6(decoder_1_out6), .out7(decoder_1_out7),
    .out8(decoder_1_out8), .out9(decoder_1_out9), .out10(decoder_1_out10), .out11(decoder_1_out11),
    .out12(decoder_1_out12), .out13(decoder_1_out13), .out14(decoder_1_out14), .out15(decoder_1_out15),
    .sel(Input), .en(not_1_out));
  Register #(.width(16)) R0 (.D(DATA_BITS), .en(decoder_1_out0), .Q(R0_q), .clk(Clock));  // open: clr
  Register #(.width(16)) R1 (.D(DATA_BITS), .en(decoder_1_out1), .Q(R1_q), .clk(Clock));  // open: clr
  Register #(.width(16)) R2 (.D(DATA_BITS), .en(decoder_1_out2), .Q(R2_q), .clk(Clock));  // open: clr
  Register #(.width(16)) R3 (.D(DATA_BITS), .en(decoder_1_out3), .Q(R3_q), .clk(Clock));  // open: clr
  Register #(.width(16)) register_1 (.D(DATA_BITS), .en(decoder_1_out4), .Q(register_1_q), .clk(Clock));  // open: clr
  Register #(.width(16)) R5 (.D(DATA_BITS), .en(decoder_1_out5), .Q(R5_q), .clk(Clock));  // open: clr
  Register #(.width(16)) R6 (.D(DATA_BITS), .en(decoder_1_out6), .Q(R6_q), .clk(Clock));  // open: clr
  Register #(.width(16)) R7 (.D(DATA_BITS), .en(decoder_1_out7), .Q(R7_q), .clk(Clock));  // open: clr
  Register #(.width(16)) R8 (.D(DATA_BITS), .en(decoder_1_out8), .Q(R8_q), .clk(Clock));  // open: clr
  Register #(.width(16)) R9 (.D(DATA_BITS), .en(decoder_1_out9), .Q(R9_q), .clk(Clock));  // open: clr
  Register #(.width(16)) R10 (.D(DATA_BITS), .en(decoder_1_out10), .Q(R10_q), .clk(Clock));  // open: clr
  Register #(.width(16)) R11 (.D(DATA_BITS), .en(decoder_1_out11), .Q(R11_q), .clk(Clock));  // open: clr
  Register #(.width(16)) R12 (.D(DATA_BITS), .en(decoder_1_out12), .Q(R12_q), .clk(Clock));  // open: clr
  Register #(.width(16)) R13 (.D(DATA_BITS), .en(decoder_1_out13), .Q(R13_q), .clk(Clock));  // open: clr
  Register #(.width(16)) R14 (.D(DATA_BITS), .en(decoder_1_out14), .Q(R14_q), .clk(Clock));  // open: clr
  Register #(.width(16)) R15 (.D(DATA_BITS), .en(decoder_1_out15), .Q(R15_q), .clk(Clock));  // open: clr
  Hex_Digit_Display hex_digit_display_1 (.value(Data_out_8_Bits[15:12]));  // open: dp
  Multiplexer #(.select(4), .width(16), .disabled(0)) multiplexer_1 (
    .in0(R0_q), .in1(R1_q), .in2(R2_q), .in3(R3_q), .in4(register_1_q), .in5(R5_q), .in6(R6_q), .in7(R7_q),
    .in8(R8_q), .in9(R9_q), .in10(R10_q), .in11(R11_q), .in12(R12_q), .in13(R13_q), .in14(R14_q),
    .in15(R15_q), .out(Data_out_8_Bits), .sel(Input), .en(R_W));
  Hex_Digit_Display hex_digit_display_2 (.value(Data_out_8_Bits[11:8]));  // open: dp
  Hex_Digit_Display hex_digit_display_3 (.value(Data_out_8_Bits[7:4]));  // open: dp
  Hex_Digit_Display hex_digit_display_4 (.value(Data_out_8_Bits[3:0]));  // open: dp

  // Notes on the sheet:
  //   R4
endmodule

module PCpractise (
  input  [15:0] PC_Input,
  input  PC_Reset,
  input  PC_Enable,
  input  Clock,
  output [15:0] PC_Output
);

  wire [15:0] adder_1_out;

  Hex_Digit_Display hex_digit_display_1 (.value(PC_Input[15:12]));  // open: dp
  Hex_Digit_Display hex_digit_display_2 (.value(PC_Input[7:4]));  // open: dp
  Hex_Digit_Display hex_digit_display_3 (.value(PC_Input[11:8]));  // open: dp
  Hex_Digit_Display hex_digit_display_4 (.value(PC_Input[3:0]));  // open: dp
  Adder #(.width(16)) adder_1 (.a(PC_Input), .b(PC_Output), .out(adder_1_out), .cin(1'b1));  // open: cout
  Register #(.width(16)) register_1 (.D(adder_1_out), .en(PC_Enable), .Q(PC_Output), .clk(Clock), .clr(PC_Reset));
  Hex_Digit_Display hex_digit_display_5 (.value(PC_Output[15:12]));  // open: dp
  Hex_Digit_Display hex_digit_display_6 (.value(PC_Output[7:4]));  // open: dp
  Hex_Digit_Display hex_digit_display_7 (.value(PC_Output[11:8]));  // open: dp
  Hex_Digit_Display hex_digit_display_8 (.value(PC_Output[3:0]));  // open: dp
endmodule
