// Logisim project Final16bit2IM.circ as structural Verilog
module main (
  input  [15:0] PC_feed,
  input  clock,
  input  PC_reset,
  input  enable,
  input  in_5,
  input  in_6,
  output [15:0] out_7,
  output [31:0] Output,
  output Even_parity,
  output Odd_parity,
  output [15:0] Rout,
  output out_12,
  output Half_carry,
  output Borrow,
  output Carry,
  output Zero,
  output Sign,
  output out_18,
  output [19:0] IR
);

  wire decoder_1_out0, decoder_1_out1, not_1_out, or_1_out, or_2_out, xor_1_out;
  wire [3:0] bit_extender_1_out_2, bit_extender_1_out_3;
  wire [7:0] bit_extender_1_out;
  wire [15:0] bit_extender_2_out, MAR_q, R0_R15_dataout;

  pc PC (.PC_in(PC_feed), .Clock(clock), .Pc_en(out_18), .PC_reset(PC_reset), .PC_out(out_7));
  Register #(.width(16)) MAR (.D(out_7), .en(enable), .Q(MAR_q), .clk(clock), .clr(PC_reset));
  Shift_Register #(.length(2)) PC_shift (
    .in(out_18), .clk(clock), .out(out_18), .clr(in_6));  // open: shift, load, d0, q0, d1, q1
  RAM #(.addrWidth(16), .dataWidth(20)) ram_1 (.addr(MAR_q), .data(IR), .clk(clock));  // open: sel, ld, clr
  assign {bit_extender_1_out_3, bit_extender_1_out_2, bit_extender_1_out} = {{8{1'b0}}, IR[7:0]};  // Bit_Extender bit_extender_1
  Decoder #(.disabled(0)) decoder_1 (.out0(decoder_1_out0), .out1(decoder_1_out1), .sel(or_1_out), .en(enable));
  or or_1 (or_1_out, IR[16], IR[17], IR[18], IR[19]);
  not not_1 (not_1_out, decoder_1_out0);
  or or_2 (or_2_out, not_1_out, decoder_1_out1);
  Hex_Digit_Display hex_digit_display_1 (.value(bit_extender_1_out_3));  // open: dp
  Hex_Digit_Display hex_digit_display_2 (.value(bit_extender_1_out_2));  // open: dp
  Hex_Digit_Display hex_digit_display_3 (.value(bit_extender_1_out[7:4]));  // open: dp
  assign bit_extender_2_out = {{8{1'b0}}, IR[7:0]};  // Bit_Extender bit_extender_2
  \reg  R0_R15 (
    .DataIn({bit_extender_1_out_3, bit_extender_1_out_2, bit_extender_1_out}), .clock(clock),
    .R_W_prime(or_2_out), .Rx(IR[11:8]), .Dataout(R0_R15_dataout));
  \reg  R0_R15_2 (.DataIn(Output[15:0]), .clock(clock), .R_W_prime(out_12), .Rx(IR[15:12]), .Dataout(Rout));
  Shift_Register #(.length(2)) R_W_shift (
    .shift(enable), .in(out_12), .clk(clock), .out(out_12), .clr(in_5));  // open: load, d0, q0, d1, q1
  Hex_Digit_Display hex_digit_display_4 (.value(bit_extender_1_out[3:0]));  // open: dp
  alu Alu (
    .A(R0_R15_dataout), .B(bit_extender_2_out), .Ax(IR[19:16]), .Zero(Zero), .Result(Output), .Carry(Carry),
    .Borrow(Borrow), .HalfCarry(Half_carry));
  Hex_Digit_Display hex_digit_display_5 (.value(R0_R15_dataout[11:8]));  // open: dp
  Hex_Digit_Display hex_digit_display_6 (.value(R0_R15_dataout[15:12]));  // open: dp
  Hex_Digit_Display hex_digit_display_7 (.value(R0_R15_dataout[7:4]));  // open: dp
  Hex_Digit_Display hex_digit_display_8 (.value(R0_R15_dataout[3:0]));  // open: dp
  Hex_Digit_Display hex_digit_display_9 (.value(Output[15:12]));  // open: dp
  Hex_Digit_Display hex_digit_display_10 (.value(Output[11:8]));  // open: dp
  Hex_Digit_Display hex_digit_display_11 (.value(Output[3:0]));  // open: dp
  Hex_Digit_Display hex_digit_display_12 (.value(Output[7:4]));  // open: dp
  ExactlyOne xor_1 (
    .out(xor_1_out), .in0(Output[0]), .in1(Output[1]), .in2(Output[2]), .in3(Output[3]), .in4(Output[4]),
    .in5(Output[5]), .in6(Output[6]), .in7(Output[7]), .in8(Output[8]), .in9(Output[9]), .in10(Output[10]),
    .in11(Output[11]), .in12(Output[12]), .in13(Output[13]), .in14(Output[14]), .in15(Output[15]));
  not not_2 (Even_parity, Odd_parity);
  and and_1 (Odd_parity, xor_1_out, 1'b1);

  assign Sign = Output[16];
endmodule

module alu (
  input  [15:0] A,
  input  [15:0] B,
  input  [3:0] Ax,
  output Zero,
  output [31:0] Result,
  output Carry,
  output Borrow,
  output HalfCarry
);

  wire adder_1_cout, adder_2_cout, not_2_out, not_3_out, not_4_out, subtractor_1_bout, subtractor_2_bout;
  wire [15:0] adder_1_out, adder_2_out, and_1_out, bit_extender_1_out, bit_extender_2_out,
       bit_extender_3_out, bit_extender_4_out, bit_extender_5_out, bit_extender_9_out, divider_1_out,
       divider_1_rem, multiplier_1_cout, multiplier_1_out, not_1_out, or_1_out, shifter_1_out, shifter_2_out,
       shifter_3_out, shifter_4_out, subtractor_1_out, subtractor_2_out;
  wire [31:0] bit_extender_10_out, undriven;

  Adder #(.width(16)) adder_1 (.a(A), .b(B), .out(adder_1_out), .cin(1'b0), .cout(adder_1_cout));
  Subtractor #(.width(16)) subtractor_1 (.a(A), .b(B), .out(subtractor_1_out), .bin(1'b0), .bout(subtractor_1_bout));
  Multiplier #(.width(16)) multiplier_1 (
    .a(A), .b(B), .out(multiplier_1_out), .cin({16{1'b0}}), .cout(multiplier_1_cout));
  Divider #(.width(16)) divider_1 (.a(A), .b(B), .out(divider_1_out), .upper({16{1'b0}}), .rem(divider_1_rem));
  Adder #(.width(16)) adder_2 (.a(A), .b(B), .out(adder_2_out), .cin(1'b0), .cout(adder_2_cout));
  Subtractor #(.width(16)) subtractor_2 (.a(A), .b(B), .out(subtractor_2_out), .bin(1'b0), .bout(subtractor_2_bout));
  assign and_1_out = A & B;  // AND_Gate and_1, 16 bits wide
  assign or_1_out = A | B;  // OR_Gate or_1, 16 bits wide
  assign not_1_out = ~A;  // NOT_Gate not_1, 16 bits wide
  Shifter #(.width(16), .shift("lr")) shifter_1 (.in(A), .\dist (B[3:0]), .out(shifter_1_out));
  Shifter #(.width(16)) shifter_2 (.in(A), .\dist (B[3:0]), .out(shifter_2_out));
  Shifter #(.width(16), .shift("rr")) shifter_3 (.in(A), .\dist (B[3:0]), .out(shifter_3_out));
  Shifter #(.width(16), .shift("rl")) shifter_4 (.in(A), .\dist (B[3:0]), .out(shifter_4_out));
  assign bit_extender_1_out = {{15{1'b0}}, adder_1_cout};  // Bit_Extender bit_extender_1
  assign bit_extender_2_out = {{15{1'b0}}, subtractor_1_bout};  // Bit_Extender bit_extender_2
  assign bit_extender_3_out = {{15{1'b0}}, adder_2_cout};  // Bit_Extender bit_extender_3
  assign bit_extender_4_out = {{15{1'b0}}, subtractor_2_bout};  // Bit_Extender bit_extender_4
  assign bit_extender_5_out = {{15{1'b0}}, 1'b0};  // Bit_Extender bit_extender_5
  assign shifter_2_out = {{15{1'b0}}, 1'b0};  // Bit_Extender bit_extender_6
  assign shifter_3_out = {{15{1'b0}}, 1'b0};  // Bit_Extender bit_extender_7
  assign shifter_4_out = {{15{1'b0}}, 1'b0};  // Bit_Extender bit_extender_8
  assign bit_extender_9_out = {{15{1'b0}}, 1'b0};  // Bit_Extender bit_extender_9
  assign bit_extender_10_out = {{16{1'b0}}, not_1_out};  // Bit_Extender bit_extender_10
  Multiplexer #(.select(4), .width(32), .enable("false")) multiplexer_1 (
    .in1(undriven), .in2({bit_extender_1_out, adder_1_out}), .in3({bit_extender_2_out, subtractor_1_out}),
    .in4({multiplier_1_cout, multiplier_1_out}), .in5({divider_1_rem, divider_1_out}),
    .in6({bit_extender_3_out, adder_2_out}), .in7({bit_extender_4_out, subtractor_2_out}),
    .in8({bit_extender_9_out, and_1_out}), .in9({bit_extender_9_out, or_1_out}), .in10(bit_extender_10_out),
    .in11({A, B}), .in12({bit_extender_5_out, shifter_1_out}), .in13({shifter_2_out, shifter_2_out}),
    .in14({shifter_3_out, shifter_3_out}), .in15({shifter_4_out, shifter_4_out}), .out(Result), .sel(Ax));  // open: in0
  not not_2 (not_2_out, Ax[0]);
  not not_3 (not_3_out, Ax[2]);
  not not_4 (not_4_out, Ax[3]);
  and and_2 (Carry, not_2_out, Ax[1], not_3_out, not_4_out, adder_1_cout);
  and and_3 (Borrow, Ax[0], Ax[1], not_3_out, not_4_out, subtractor_1_bout);
  nor nor_1 (Zero, Result[0], Result[1], Result[2], Result[3], Result[4], Result[5], Result[6], Result[7], Result[8], Result[9], Result[10], Result[11], Result[12], Result[13], Result[14], Result[15]);
  Adder adder_3 (.a(A[7:0]), .b(B[7:0]), .cout(HalfCarry));  // open: out, cin
endmodule

module \reg  (
  input  [15:0] DataIn,
  input  clock,
  input  R_W_prime,
  input  [3:0] Rx,
  output [15:0] Dataout
);

  wire decoder_1_out0, decoder_1_out1, decoder_1_out2, decoder_1_out3, decoder_1_out4, decoder_1_out5,
       decoder_1_out6, decoder_1_out7, decoder_1_out8, decoder_1_out9, decoder_1_out10, decoder_1_out11,
       decoder_1_out12, decoder_1_out13, decoder_1_out14, decoder_1_out15, not_1_out;
  wire [15:0] R0_q, R1_q, R2_q, R3_q, R4_q, R5_q, R6_q, R7_q, R8_q, R9_q, R10_q, R11_q, R12_q, R13_q, R14_q,
       R15_q;

  not not_1 (not_1_out, R_W_prime);
  Decoder #(.select(4), .disabled(0)) decoder_1 (
    .out0(decoder_1_out0), .out1(decoder_1_out1), .out2(decoder_1_out2), .out3(decoder_1_out3),
    .out4(decoder_1_out4), .out5(decoder_1_out5), .out6(decoder_1_out6), .out7(decoder_1_out7),
    .out8(decoder_1_out8), .out9(decoder_1_out9), .out10(decoder_1_out10), .out11(decoder_1_out11),
    .out12(decoder_1_out12), .out13(decoder_1_out13), .out14(decoder_1_out14), .out15(decoder_1_out15),
    .sel(Rx), .en(not_1_out));
  Register #(.width(16)) R0 (.D(DataIn), .en(decoder_1_out0), .Q(R0_q), .clk(clock));  // open: clr
  Register #(.width(16)) R1 (.D(DataIn), .en(decoder_1_out1), .Q(R1_q), .clk(clock));  // open: clr
  Register #(.width(16)) R2 (.D(DataIn), .en(decoder_1_out2), .Q(R2_q), .clk(clock));  // open: clr
  Register #(.width(16)) R3 (.D(DataIn), .en(decoder_1_out3), .Q(R3_q), .clk(clock));  // open: clr
  Register #(.width(16)) R4 (.D(DataIn), .en(decoder_1_out4), .Q(R4_q), .clk(clock));  // open: clr
  Register #(.width(16)) R5 (.D(DataIn), .en(decoder_1_out5), .Q(R5_q), .clk(clock));  // open: clr
  Register #(.width(16)) R6 (.D(DataIn), .en(decoder_1_out6), .Q(R6_q), .clk(clock));  // open: clr
  Register #(.width(16)) R7 (.D(DataIn), .en(decoder_1_out7), .Q(R7_q), .clk(clock));  // open: clr
  Register #(.width(16)) R8 (.D(DataIn), .en(decoder_1_out8), .Q(R8_q), .clk(clock));  // open: clr
  Register #(.width(16)) R9 (.D(DataIn), .en(decoder_1_out9), .Q(R9_q), .clk(clock));  // open: clr
  Register #(.width(16)) R10 (.D(DataIn), .en(decoder_1_out10), .Q(R10_q), .clk(clock));  // open: clr
  Register #(.width(16)) R11 (.D(DataIn), .en(decoder_1_out11), .Q(R11_q), .clk(clock));  // open: clr
  Register #(.width(16)) R12 (.D(DataIn), .en(decoder_1_out12), .Q(R12_q), .clk(clock));  // open: clr
  Register #(.width(16)) R13 (.D(DataIn), .en(decoder_1_out13), .Q(R13_q), .clk(clock));  // open: clr
  Register #(.width(16)) R14 (.D(DataIn), .en(decoder_1_out14), .Q(R14_q), .clk(clock));  // open: clr
  Register #(.width(16)) R15 (.D(DataIn), .en(decoder_1_out15), .Q(R15_q), .clk(clock));  // open: clr
  Multiplexer #(.select(4), .width(16)) multiplexer_1 (
    .in0(R0_q), .in1(R1_q), .in2(R2_q), .in3(R3_q), .in4(R4_q), .in5(R5_q), .in6(R6_q), .in7(R7_q),
    .in8(R8_q), .in9(R9_q), .in10(R10_q), .in11(R11_q), .in12(R12_q), .in13(R13_q), .in14(R14_q),
    .in15(R15_q), .out(Dataout), .sel(Rx), .en(R_W_prime));
endmodule

module pc (
  input  [15:0] PC_in,
  input  Clock,
  input  Pc_en,
  input  PC_reset,
  output [15:0] PC_out
);

  wire [15:0] adder_1_out;

  Adder #(.width(16)) adder_1 (.a(PC_in), .b(PC_out), .out(adder_1_out), .cin(1'b1));  // open: cout
  Register #(.width(16)) register_1 (.D(adder_1_out), .en(Pc_en), .Q(PC_out), .clk(Clock), .clr(PC_reset));
endmodule
