// Logisim project Final_processor.circ as structural Verilog: 4 circuits, main circuit main
module main (
  input  [7:0] in_1,
  output [7:0] PC,
  output [15:0] out_3
);

  wire Clock_out, not_1_out, not_2_out, PC_shift_out, Reg_shift_out, RESET, undriven, undriven_2;
  wire [7:0] IR_q, MAR_q, RA_q, ram_1_data, RB_q, Reg_file_out_5, RZ_q;
  wire [15:0] MBR_q, rom_1_data;
  wire [15:8] IR_q_2, RZ_q_2;

  Clock Clock (.out(Clock_out));
  PC pc_1 (.PC_INput(in_1), .PC_enable(PC_shift_out), .Clock(Clock_out), .PC_reset(RESET), .PC_OUT(PC));
  Shift_Register #(.length(2)) PC_shift (
    .in(PC_shift_out), .clk(Clock_out), .out(PC_shift_out));  // open: shift, load, clr, d0, q0, d1, q1
  Register MAR (.D(PC), .en(PC_shift_out), .Q(MAR_q), .clk(Clock_out), .clr(RESET));
  not not_1 (not_1_out, PC_shift_out);
  Shift_Register #(.length(5)) Reg_shift (
    .in(Reg_shift_out), .clk(undriven), .out(Reg_shift_out));  // open: shift, load, clr, d0, q0, d1, q1, d2, q2, d3, q3, d4, q4
  ROM #(.dataWidth(16)) rom_1 (.addr(MAR_q), .data(rom_1_data));  // open: sel
  Register #(.width(16)) MBR (.D(rom_1_data), .Q(MBR_q), .clk(Clock_out), .clr(RESET));  // open: en
  not not_2 (not_2_out, not_1_out);
  Register #(.width(16)) IR (.D(MBR_q), .Q({IR_q_2, IR_q}), .clk(Clock_out), .clr(RESET));  // open: en
  Register RA (.D(Reg_file_out_5), .Q(RA_q), .clk(Clock_out), .clr(RESET));  // open: en
  Register_file Reg_file (.Input(RZ_q), .R_W(not_1_out), .RX(IR_q_2[10:8]), .Clock(Clock_out), .out_5(Reg_file_out_5));
  RAM #(.bus("separate")) ram_1 (
    .addr(IR_q), .din(RB_q), .data(ram_1_data), .str(not_2_out), .clk(Clock_out), .ld(not_1_out),
    .clr(undriven_2));  // open: sel
  Register RB (.D(ram_1_data), .Q(RB_q), .clk(Clock_out), .clr(RESET));  // open: en
  Register #(.width(16)) RZ (.D(out_3), .Q({RZ_q_2, RZ_q}), .clk(Clock_out), .clr(RESET));  // open: en
  ALU ALU (.A(RA_q), .B(RB_q), ._1(IR_q_2[14:11]), .out_4(out_3));
  Button button_1 (.out(RESET));
  Hex_Digit_Display hex_digit_display_1 (.value(out_3[11:8]));  // open: dp
  Hex_Digit_Display hex_digit_display_2 (.value(out_3[15:12]));  // open: dp
  Hex_Digit_Display hex_digit_display_3 (.value(out_3[3:0]));  // open: dp
  Hex_Digit_Display hex_digit_display_4 (.value(out_3[7:4]));  // open: dp

  // Notes on the sheet:
  //   Code Memory
  //   contents of rom_1 (hex, n*v repeats v):
  //   1234 111 0 1235 235 20ff 121d
  //   Data Memory
  //   RESULT
endmodule

module Register_file (
  input  [7:0] Input,
  input  R_W,
  input  [2:0] RX,
  input  Clock,
  output [7:0] out_5
);

  wire decoder_1_out0, decoder_1_out1, decoder_1_out2, decoder_1_out3, decoder_1_out4, decoder_1_out5,
       decoder_1_out6, decoder_1_out7, not_1_out;
  wire [7:0] R0_q, R1_q, R2_q, R3_q, R4_q, R5_q, R6_q, R7_q;

  Hex_Digit_Display hex_digit_display_1 (.value(Input[7:4]));  // open: dp
  Hex_Digit_Display hex_digit_display_2 (.value(Input[3:0]));  // open: dp
  Decoder #(.select(3), .disabled(0)) decoder_1 (
    .out0(decoder_1_out0), .out1(decoder_1_out1), .out2(decoder_1_out2), .out3(decoder_1_out3),
    .out4(decoder_1_out4), .out5(decoder_1_out5), .out6(decoder_1_out6), .out7(decoder_1_out7), .sel(RX),
    .en(not_1_out));
  not not_1 (not_1_out, R_W);
  Register R0 (.D(Input), .en(decoder_1_out0), .Q(R0_q), .clk(Clock));  // open: clr
  Register R1 (.D(Input), .en(decoder_1_out1), .Q(R1_q), .clk(Clock));  // open: clr
  Register R2 (.D(Input), .en(decoder_1_out2), .Q(R2_q), .clk(Clock));  // open: clr
  Register R3 (.D(Input), .en(decoder_1_out3), .Q(R3_q), .clk(Clock));  // open: clr
  Register R4 (.D(Input), .en(decoder_1_out4), .Q(R4_q), .clk(Clock));  // open: clr
  Register R5 (.D(Input), .en(decoder_1_out5), .Q(R5_q), .clk(Clock));  // open: clr
  Register R6 (.D(Input), .en(decoder_1_out6), .Q(R6_q), .clk(Clock));  // open: clr
  Register R7 (.D(Input), .en(decoder_1_out7), .Q(R7_q), .clk(Clock));  // open: clr
  Multiplexer #(.select(3), .width(8), .disabled(0)) multiplexer_1 (
    .in0(R0_q), .in1(R1_q), .in2(R2_q), .in3(R3_q), .in4(R4_q), .in5(R5_q), .in6(R6_q), .in7(R7_q),
    .out(out_5), .sel(RX), .en(R_W));

  // Notes on the sheet:
  //   fLOATING STATE DECODER-OFF IT IS NOT HIGH OR LOW STATE
endmodule

module ALU (
  input  [7:0] A,
  input  [7:0] B,
  input  [3:0] _1,
  output [15:0] out_4
);

  wire adder_1_cout, subtractor_1_bout;
  wire [2:0] bit_extender_1_out;
  wire [7:0] adder_1_out, and_1_out, bit_extender_2_out, bit_extender_3_out, divider_1_out, divider_1_rem,
       multiplier_1_cout, multiplier_1_out, nor_1_out, or_1_out, shifter_1_out, shifter_2_out, shifter_3_out,
       shifter_4_out, shifter_5_out, subtractor_1_out, xnor_1_out;
  wire [15:0] bit_extender_4_out, bit_extender_5_out, bit_extender_6_out, bit_extender_7_out,
       bit_extender_8_out, bit_extender_9_out, bit_extender_10_out, bit_extender_11_out, bit_extender_12_out;

  Hex_Digit_Display hex_digit_display_1 (.value(A[7:4]));  // open: dp
  Hex_Digit_Display hex_digit_display_2 (.value(B[7:4]));  // open: dp
  Hex_Digit_Display hex_digit_display_3 (.value(A[3:0]));  // open: dp
  Hex_Digit_Display hex_digit_display_4 (.value(B[3:0]));  // open: dp
  Bit_Extender #(.out_width(3)) bit_extender_1 (.in(B), .out(bit_extender_1_out));
  Adder adder_1 (.a(A), .b(B), .out(adder_1_out), .cout(adder_1_cout));  // open: cin
  Subtractor subtractor_1 (.a(A), .b(B), .out(subtractor_1_out), .bout(subtractor_1_bout));  // open: bin
  Multiplier multiplier_1 (.a(A), .b(B), .out(multiplier_1_out), .cout(multiplier_1_cout));  // open: cin
  Divider divider_1 (.a(A), .b(B), .out(divider_1_out), .rem(divider_1_rem));  // open: upper
  assign and_1_out = A & B;  // AND_Gate and_1, 8 bits wide
  assign or_1_out = A | B;  // OR_Gate or_1, 8 bits wide
  assign xnor_1_out = ~(A ^ B);  // XNOR_Gate xnor_1, 8 bits wide
  assign nor_1_out = ~(A | B);  // NOR_Gate nor_1, 8 bits wide
  Shifter shifter_1 (.in(A), .\dist (bit_extender_1_out), .out(shifter_1_out));
  Shifter #(.shift("lr")) shifter_2 (.in(A), .\dist (bit_extender_1_out), .out(shifter_2_out));
  Shifter #(.shift("ar")) shifter_3 (.in(A), .\dist (bit_extender_1_out), .out(shifter_3_out));
  Shifter #(.shift("rl")) shifter_4 (.in(A), .\dist (bit_extender_1_out), .out(shifter_4_out));
  Shifter #(.shift("rr")) shifter_5 (.in(A), .\dist (bit_extender_1_out), .out(shifter_5_out));
  assign bit_extender_2_out = {{7{1'b0}}, adder_1_cout};  // Bit_Extender bit_extender_2
  assign bit_extender_3_out = {{7{1'b0}}, subtractor_1_bout};  // Bit_Extender bit_extender_3
  assign bit_extender_4_out = {{8{1'b0}}, and_1_out};  // Bit_Extender bit_extender_4
  assign bit_extender_5_out = {{8{1'b0}}, or_1_out};  // Bit_Extender bit_extender_5
  assign bit_extender_6_out = {{8{1'b0}}, xnor_1_out};  // Bit_Extender bit_extender_6
  assign bit_extender_7_out = {{8{1'b0}}, nor_1_out};  // Bit_Extender bit_extender_7
  assign bit_extender_8_out = {{8{1'b0}}, shifter_1_out};  // Bit_Extender bit_extender_8
  assign bit_extender_9_out = {{8{1'b0}}, shifter_2_out};  // Bit_Extender bit_extender_9
  assign bit_extender_10_out = {{8{1'b0}}, shifter_3_out};  // Bit_Extender bit_extender_10
  assign bit_extender_11_out = {{8{1'b0}}, shifter_4_out};  // Bit_Extender bit_extender_11
  assign bit_extender_12_out = {{8{1'b0}}, shifter_5_out};  // Bit_Extender bit_extender_12
  Multiplexer #(.select(4), .width(16), .enable("false")) multiplexer_1 (
    .in0({bit_extender_2_out, adder_1_out}), .in1({bit_extender_3_out, subtractor_1_out}),
    .in2({multiplier_1_cout, multiplier_1_out}), .in3({divider_1_rem, divider_1_out}),
    .in4(bit_extender_4_out), .in5(bit_extender_5_out), .in6(bit_extender_6_out), .in7(bit_extender_7_out),
    .in8(bit_extender_8_out), .in9(bit_extender_9_out), .in10(bit_extender_10_out),
    .in11(bit_extender_11_out), .in12(bit_extender_12_out), .out(out_4), .sel(_1));  // open: in13, in14, in15
  Hex_Digit_Display hex_digit_display_5 (.value(out_4[11:8]));  // open: dp
  Hex_Digit_Display hex_digit_display_6 (.value(out_4[15:12]));  // open: dp
  Hex_Digit_Display hex_digit_display_7 (.value(_1));  // open: dp
  Hex_Digit_Display hex_digit_display_8 (.value(out_4[7:4]));  // open: dp
  Hex_Digit_Display hex_digit_display_9 (.value(out_4[3:0]));  // open: dp

  // Notes on the sheet:
  //   BitExtender
  //   ALU-8bit 
  //   Add
  //   Sub
  //   Mul
  //   Div
  //   And
  //   OR
  //   XNor
  //   OR
  //   LogicLeft
  //   LogicRight
  //   ArithRight
  //   RotateLeft
  //   Rotateright
  //   0-adder|1-sub|2-mpy|3-div|4-and|5-or|6-xnor|7-xor|8-lls|9-lrs|10-ars|11-rr|12-rl
endmodule

module PC (
  input  [7:0] PC_INput,
  input  PC_enable,
  input  Clock,
  input  PC_reset,
  output [7:0] PC_OUT
);

  wire [7:0] adder_1_out;

  Adder adder_1 (.a(PC_INput), .b(PC_OUT), .out(adder_1_out), .cin(1'b1));  // open: cout
  Hex_Digit_Display hex_digit_display_1 (.value(PC_OUT[7:4]));  // open: dp
  Register register_1 (.D(adder_1_out), .en(PC_enable), .Q(PC_OUT), .clk(Clock), .clr(PC_reset));
  Hex_Digit_Display hex_digit_display_2 (.value(PC_OUT[3:0]));  // open: dp
endmodule
