// Logisim project Full_Half_Adder.circ as structural Verilog: 3 circuits, main circuit main
module main (
  input  A,
  input  B,
  input  C,
  output SUM,
  output Carry
);

  Half_adder half_adder_1 (.A(A), .B(B), .out_3(SUM), .out_4(Carry));
  FULL_adder full_adder_1 (.A(A), .B(B), .C(C), .out_4(SUM), .out_5(Carry));
endmodule

module Half_adder (
  input  A,
  input  B,
  output out_3,
  output out_4
);

  xor xor_1 (out_3, A, B);
  and and_1 (out_4, A, B);
endmodule

module FULL_adder (
  input  A,
  input  B,
  input  C,
  output out_4,
  output out_5
);

  wire and_1_out, and_2_out, xor_1_out;

  xor xor_1 (xor_1_out, A, B);
  and and_1 (and_1_out, A, B);
  and and_2 (and_2_out, C, xor_1_out);
  xor xor_2 (out_4, xor_1_out, C);
  or or_1 (out_5, and_2_out, and_1_out);
endmodule
