// Logisim project MUX.circ as structural Verilog: 1 circuit, main circuit main
module main (
  input  [3:0] I0,
  input  [3:0] I1,
  input  [3:0] I2,
  input  [3:0] I3,
  input  [1:0] s1_so,
  output [3:0] out_6
);

  Multiplexer #(.select(2), .width(4), .enable("false")) multiplexer_1 (
    .in0(I0), .in1(I1), .in2(I2), .in3(I3), .out(out_6), .sel(s1_so));
endmodule
