// Logisim project My1stMemory.circ as structural Verilog: 4 circuits, main circuit main
module main (
  input  D1,
  input  D2,
  input  R_W,
  input  in_4,
  output out_5,
  output out_6,
  output out_7,
  output out_8,
  output out_9,
  output out_10
);

  wire clock_1_out, decoder_1_out0, decoder_1_out1;

  Decoder decoder_1 (.out0(decoder_1_out0), .out1(decoder_1_out1), .sel(in_4));  // open: en
  Clock clock_1 (.out(clock_1_out));
  _1bitram u_1bitram_1 (.Select(decoder_1_out0), .Clock(clock_1_out), .R_W(R_W), .Data(D1), .Result(out_5));
  _1bitram u_1bitram_2 (.Select(decoder_1_out1), .Clock(clock_1_out), .R_W(R_W), .Data(D1), .Result(out_7));
  _1bitram u_1bitram_3 (.Select(decoder_1_out0), .Clock(clock_1_out), .R_W(R_W), .Data(D2), .Result(out_6));
  _1bitram u_1bitram_4 (.Select(decoder_1_out1), .Clock(clock_1_out), .R_W(R_W), .Data(D2), .Result(out_8));
  Multiplexer multiplexer_1 (.in0(out_6), .in1(out_8), .out(out_9), .sel(in_4));  // open: en
  Multiplexer multiplexer_2 (.in0(out_5), .in1(out_7), .out(out_10), .sel(in_4));  // open: en
endmodule

module _1bitram (
  input  R_W,
  input  Data,
  input  Select,
  input  Clock,
  output Result
);

  wire A1_out, A2_out, not_1_out, not_2_out, s_r_ff_1_q;

  not not_1 (not_1_out, R_W);
  not not_2 (not_2_out, Data);
  and A1 (A1_out, Data, not_1_out);
  and A2 (A2_out, not_2_out, not_1_out);
  S_R_Flip_Flop s_r_ff_1 (.S(A1_out), .clk(Clock), .R(A2_out), .Q(s_r_ff_1_q), .en(Select));  // open: Qn, preset, reset
  and and_1 (Result, s_r_ff_1_q, R_W);
endmodule

module _1_2 (
  input  R_W,
  input  Data,
  input  Select,
  input  D2,
  output out_5,
  output out_6
);

  wire A1_2_out, A1_out, A2_2_out, A2_out, Clock_out, not_1_out, not_2_out, not_3_out, s_r_ff_1_q, s_r_ff_2_q;

  not not_1 (not_1_out, R_W);
  not not_2 (not_2_out, Data);
  Clock Clock (.out(Clock_out));
  and A1 (A1_out, Data, not_1_out);
  and A2 (A2_out, not_2_out, not_1_out);
  S_R_Flip_Flop s_r_ff_1 (
    .S(A1_out), .clk(Clock_out), .R(A2_out), .Q(s_r_ff_1_q), .en(Select));  // open: Qn, preset, reset
  and and_1 (out_5, s_r_ff_1_q, R_W);
  not not_3 (not_3_out, D2);
  and A1_2 (A1_2_out, D2, not_1_out);
  and A2_2 (A2_2_out, not_3_out, not_1_out);
  S_R_Flip_Flop s_r_ff_2 (
    .S(A1_2_out), .clk(Clock_out), .R(A2_2_out), .Q(s_r_ff_2_q), .en(Select));  // open: Qn, preset, reset
  and and_2 (out_6, s_r_ff_2_q, R_W);
endmodule

module _2_2 (
  input  R_W,
  input  D1,
  input  D2,
  input  in_4,
  output [1:0] out_5,
  output [1:0] out_6
);

  wire A1_2_out, A1_3_out, A1_4_out, A1_out, A2_2_out, A2_3_out, A2_4_out, A2_out, Clock_out, decoder_1_out0,
       decoder_1_out1, not_1_out, not_2_out, not_3_out, s_r_ff_1_q, s_r_ff_2_q, s_r_ff_3_q, s_r_ff_4_q;

  Clock Clock (.out(Clock_out));
  Decoder decoder_1 (.out0(decoder_1_out0), .out1(decoder_1_out1), .sel(in_4));  // open: en
  not not_1 (not_1_out, R_W);
  not not_2 (not_2_out, D1);
  and A1 (A1_out, D1, not_1_out);
  and A2 (A2_out, not_2_out, not_1_out);
  and A1_2 (A1_2_out, D1, not_1_out);
  and A2_2 (A2_2_out, not_2_out, not_1_out);
  S_R_Flip_Flop s_r_ff_1 (
    .S(A1_out), .clk(Clock_out), .R(A2_out), .Q(s_r_ff_1_q), .en(decoder_1_out0));  // open: Qn, preset, reset
  S_R_Flip_Flop s_r_ff_2 (
    .S(A1_2_out), .clk(Clock_out), .R(A2_2_out), .Q(s_r_ff_2_q), .en(decoder_1_out1));  // open: Qn, preset, reset
  and and_1 (out_6[1], s_r_ff_2_q, R_W);
  and and_2 (out_5[1], s_r_ff_1_q, R_W);
  not not_3 (not_3_out, D2);
  and A1_3 (A1_3_out, D2, not_1_out);
  and A2_3 (A2_3_out, not_3_out, not_1_out);
  and A1_4 (A1_4_out, D2, not_1_out);
  and A2_4 (A2_4_out, not_3_out, not_1_out);
  S_R_Flip_Flop s_r_ff_3 (
    .S(A1_4_out), .clk(Clock_out), .R(A2_4_out), .Q(s_r_ff_3_q), .en(decoder_1_out0));  // open: Qn, preset, reset
  S_R_Flip_Flop s_r_ff_4 (
    .S(A1_3_out), .clk(Clock_out), .R(A2_3_out), .Q(s_r_ff_4_q), .en(decoder_1_out1));  // open: Qn, preset, reset
  and and_3 (out_5[0], s_r_ff_3_q, R_W);
  and and_4 (out_6[0], s_r_ff_4_q, R_W);
endmodule
