// Logisim project RAM (all subckts).circ as structural Verilog: 3 circuits, main circuit main
module main (
  input  R_W_prime,
  input  DATA,
  input  SELECT,
  output DATA_OUT
);

  wire and_1_out, and_2_out, clock_1_out, not_1_out, not_2_out, s_r_ff_1_q;

  not not_1 (not_1_out, R_W_prime);
  Clock clock_1 (.out(clock_1_out));
  not not_2 (not_2_out, DATA);
  and and_1 (and_1_out, DATA, not_1_out);
  and and_2 (and_2_out, not_2_out, not_1_out);
  S_R_Flip_Flop s_r_ff_1 (
    .S(and_1_out), .clk(clock_1_out), .R(and_2_out), .Q(s_r_ff_1_q), .en(SELECT));  // open: Qn, preset, reset
  and and_3 (DATA_OUT, s_r_ff_1_q, R_W_prime);
endmodule

module _1_2_ram (
  input  R_W_prime,
  input  D0,
  input  D1,
  input  SELECT,
  output D1_OUT,
  output D0_OUT
);

  wire and_1_out, and_2_out, and_4_out, and_5_out, CLK_out, not_1_out, not_2_out, not_3_out, s_r_ff_1_q,
       s_r_ff_2_q;

  not not_1 (not_1_out, R_W_prime);
  Clock CLK (.out(CLK_out));
  not not_2 (not_2_out, D0);
  and and_1 (and_1_out, D0, not_1_out);
  and and_2 (and_2_out, not_2_out, not_1_out);
  S_R_Flip_Flop s_r_ff_1 (
    .S(and_1_out), .clk(CLK_out), .R(and_2_out), .Q(s_r_ff_1_q), .en(SELECT));  // open: Qn, preset, reset
  and and_3 (D0_OUT, s_r_ff_1_q, R_W_prime);
  not not_3 (not_3_out, D1);
  and and_4 (and_4_out, D1, not_1_out);
  and and_5 (and_5_out, not_3_out, not_1_out);
  S_R_Flip_Flop s_r_ff_2 (
    .S(and_4_out), .clk(CLK_out), .R(and_5_out), .Q(s_r_ff_2_q), .en(SELECT));  // open: Qn, preset, reset
  and and_6 (D1_OUT, s_r_ff_2_q, R_W_prime);
endmodule

module _2_2_ram (
  input  D0,
  input  R_W_prime,
  input  D1,
  input  in_4,
  output [1:0] out_5,
  output [1:0] out_6
);

  wire and_1_out, and_2_out, and_3_out, and_4_out, and_9_out, and_10_out, CLK_out, decoder_1_out0,
       decoder_1_out1, not_1_out, not_2_out, not_3_out, s_r_ff_1_q, s_r_ff_2_q, s_r_ff_3_q, s_r_ff_4_q;

  not not_1 (not_1_out, R_W_prime);
  Clock CLK (.out(CLK_out));
  Decoder #(.enable("false")) decoder_1 (.out0(decoder_1_out0), .out1(decoder_1_out1), .sel(in_4));
  not not_2 (not_2_out, D1);
  and and_1 (and_1_out, D1, not_1_out);
  and and_2 (and_2_out, not_2_out, not_1_out);
  and and_3 (and_3_out, D1, not_1_out);
  and and_4 (and_4_out, not_2_out, not_1_out);
  S_R_Flip_Flop s_r_ff_1 (
    .S(and_1_out), .clk(CLK_out), .R(and_2_out), .Q(s_r_ff_1_q), .en(decoder_1_out0));  // open: Qn, preset, reset
  S_R_Flip_Flop s_r_ff_2 (
    .S(and_3_out), .clk(CLK_out), .R(and_4_out), .Q(s_r_ff_2_q), .en(decoder_1_out1));  // open: Qn, preset, reset
  and and_5 (out_5[1], s_r_ff_1_q, R_W_prime);
  and and_6 (out_6[1], s_r_ff_2_q, R_W_prime);
  not not_3 (not_3_out, D0);
  // AND_Gate and_7 has open pins: in0=D0, in1=not_1_out, out=open
  // AND_Gate and_8 has open pins: in0=not_3_out, in1=not_1_out, out=open
  and and_9 (and_9_out, D0, not_1_out);
  and and_10 (and_10_out, not_3_out, not_1_out);
  S_R_Flip_Flop s_r_ff_3 (.clk(CLK_out), .Q(s_r_ff_3_q), .en(decoder_1_out0));  // open: S, R, Qn, preset, reset
  S_R_Flip_Flop s_r_ff_4 (
    .S(and_9_out), .clk(CLK_out), .R(and_10_out), .Q(s_r_ff_4_q), .en(decoder_1_out1));  // open: Qn, preset, reset
  and and_11 (out_5[0], s_r_ff_3_q, R_W_prime);
  and and_12 (out_6[0], s_r_ff_4_q, R_W_prime);
endmodule
