// Logisim project SR_flipFlop.circ as structural Verilog: 1 circuit, main circuit main
module main (
  input  A,
  input  B,
  output out_3
);

  wire Clock_out;

  Clock Clock (.out(Clock_out));
  S_R_Flip_Flop s_r_ff_1 (.S(A), .clk(Clock_out), .R(B), .Q(out_3));  // open: Qn, preset, reset, en
endmodule
