// Logisim project Tunnel.circ as structural Verilog: 1 circuit, main circuit main
module main (
  input  in_1,
  input  in_2,
  output out_3
);

  and and_1 (out_3, in_1, in_2);

  // Other names for the same wires on the sheet: A = in_1; B = in_2; Y = out_3
endmodule
