// Logisim project alu (1).circ as structural Verilog: 1 circuit, main circuit main
module main (
  input  [15:0] A,
  input  [15:0] B,
  input  [15:0] in_3,
  input  [3:0] in_4,
  input  [3:0] in_5,
  output [31:0] Output
);

  wire adder_1_cout, adder_2_cout, subtractor_1_bout, subtractor_2_bout;
  wire [15:0] adder_1_out, adder_2_out, and_1_out, bit_extender_1_out, bit_extender_2_out,
       bit_extender_5_out, bit_extender_6_out, divider_1_out, multiplier_1_out, not_1_out, or_1_out,
       shifter_1_out, shifter_2_out, shifter_3_out, shifter_4_out, subtractor_1_out, subtractor_2_out,
       xor_1_out, xor_2_out, xor_3_out;
  wire [31:0] bit_extender_3_out, bit_extender_4_out, bit_extender_7_out, bit_extender_8_out,
       bit_extender_9_out, bit_extender_10_out, bit_extender_11_out, bit_extender_12_out,
       bit_extender_13_out, bit_extender_14_out;

  Adder #(.width(16)) adder_1 (.a(A), .b(B), .out(adder_1_out), .cout(adder_1_cout));  // open: cin
  Subtractor #(.width(16)) subtractor_1 (.a(A), .b(B), .out(subtractor_1_out), .bout(subtractor_1_bout));  // open: bin
  Multiplier #(.width(16)) multiplier_1 (.a(A), .b(B), .out(multiplier_1_out));  // open: cin, cout
  Divider #(.width(16)) divider_1 (.a(A), .b(B), .out(divider_1_out));  // open: upper, rem
  Adder #(.width(16)) adder_2 (.a(A), .b(in_3), .out(adder_2_out), .cout(adder_2_cout));  // open: cin
  Subtractor #(.width(16)) subtractor_2 (
    .a(A), .b(in_3), .out(subtractor_2_out), .bout(subtractor_2_bout));  // open: bin
  assign not_1_out = ~B;  // NOT_Gate not_1, 16 bits wide
  Shifter #(.width(16), .shift("lr")) shifter_1 (.in(B), .\dist (in_5), .out(shifter_1_out));
  Shifter #(.width(16)) shifter_2 (.in(B), .\dist (in_5), .out(shifter_2_out));
  Shifter #(.width(16), .shift("rr")) shifter_3 (.in(B), .\dist (in_5), .out(shifter_3_out));
  Shifter #(.width(16), .shift("rl")) shifter_4 (.in(B), .\dist (in_5), .out(shifter_4_out));
  assign bit_extender_1_out = {{15{1'b0}}, adder_1_cout};  // Bit_Extender bit_extender_1
  assign bit_extender_2_out = {{15{1'b0}}, subtractor_1_bout};  // Bit_Extender bit_extender_2
  assign bit_extender_3_out = {{16{1'b0}}, multiplier_1_out};  // Bit_Extender bit_extender_3
  assign bit_extender_4_out = {{16{1'b0}}, divider_1_out};  // Bit_Extender bit_extender_4
  assign bit_extender_5_out = {{15{1'b0}}, adder_2_cout};  // Bit_Extender bit_extender_5
  assign bit_extender_6_out = {{15{1'b0}}, subtractor_2_bout};  // Bit_Extender bit_extender_6
  assign bit_extender_7_out = {{16{1'b0}}, and_1_out};  // Bit_Extender bit_extender_7
  assign and_1_out = A & B;  // AND_Gate and_1, 16 bits wide
  assign or_1_out = A | B;  // OR_Gate or_1, 16 bits wide
  assign bit_extender_8_out = {{16{1'b0}}, or_1_out};  // Bit_Extender bit_extender_8
  assign bit_extender_9_out = {{16{1'b0}}, not_1_out};  // Bit_Extender bit_extender_9
  assign xor_1_out = A ^ B;  // XOR_Gate xor_1, 16 bits wide
  assign xor_2_out = A ^ xor_1_out;  // XOR_Gate xor_2, 16 bits wide
  assign bit_extender_10_out = {{16{1'b0}}, shifter_1_out};  // Bit_Extender bit_extender_10
  assign bit_extender_11_out = {{16{1'b0}}, shifter_2_out};  // Bit_Extender bit_extender_11
  assign bit_extender_12_out = {{16{1'b0}}, shifter_3_out};  // Bit_Extender bit_extender_12
  assign bit_extender_13_out = {{16{1'b0}}, shifter_4_out};  // Bit_Extender bit_extender_13
  assign xor_3_out = xor_2_out ^ B;  // XOR_Gate xor_3, 16 bits wide
  assign bit_extender_14_out = {{16{1'b0}}, xor_3_out};  // Bit_Extender bit_extender_14
  Multiplexer #(.select(4), .width(32), .enable("false")) multiplexer_1 (
    .in0({B, A}), .in1({B, A}), .in2({bit_extender_1_out, adder_1_out}),
    .in3({bit_extender_2_out, subtractor_1_out}), .in4(bit_extender_3_out), .in5(bit_extender_4_out),
    .in6({bit_extender_5_out, adder_2_out}), .in7({bit_extender_6_out, subtractor_2_out}),
    .in8(bit_extender_7_out), .in9(bit_extender_8_out), .in10(bit_extender_9_out),
    .in11(bit_extender_14_out), .in12(bit_extender_10_out), .in13(bit_extender_11_out),
    .in14(bit_extender_12_out), .in15(bit_extender_13_out), .out(Output), .sel(in_4));
endmodule
