// Logisim project combining ALU & REG..circ as structural Verilog: 4 circuits, main circuit main
module main (
  input  [14:0] INSTRUCTION,
  input  [7:0] DATA_IN,
  input  [7:0] DATA,
  input  R_W_prime,
  output [15:0] out_5
);

  wire clock_1_out, not_1_out;
  wire [7:0] ram_1_data, register_8_bits_1_data_out;

  Clock clock_1 (.out(clock_1_out));
  not not_1 (not_1_out, R_W_prime);
  RAM #(.bus("separate")) ram_1 (
    .addr(INSTRUCTION[7:0]), .din(DATA), .data(ram_1_data), .str(not_1_out), .clk(clock_1_out), .ld(R_W_prime));  // open: sel, clr
  REGISTER_8_BITS register_8_bits_1 (
    .DATA_IN(DATA_IN), .CLOCK(clock_1_out), .R_W_prime(R_W_prime), .RX(INSTRUCTION[10:8]),
    .DATA_OUT(register_8_bits_1_data_out));
  ALU_8BITS alu_8bits_1 (.A(register_8_bits_1_data_out), .B(ram_1_data), .in_3(INSTRUCTION[14:11]), .DATA_OUT(out_5));
  Hex_Digit_Display hex_digit_display_1 (.value(out_5[15:12]));  // open: dp
  Hex_Digit_Display hex_digit_display_2 (.value(out_5[11:8]));  // open: dp
  Hex_Digit_Display hex_digit_display_3 (.value(out_5[7:4]));  // open: dp
  Hex_Digit_Display hex_digit_display_4 (.value(out_5[3:0]));  // open: dp
endmodule

// ALU
module ALU_8BITS (
  input  [7:0] A,
  input  [7:0] B,
  input  [3:0] in_3,
  output [15:0] DATA_OUT
);

  wire adder_1_cout, comparator_1_eq, comparator_1_gt, comparator_1_lt, subtractor_1_bout;
  wire [2:0] bit_extender_1_out;
  wire [3:0] bit_extender_12_out, bit_extender_13_out;
  wire [7:0] adder_1_out, and_1_out, bit_extender_2_out, bit_extender_3_out, bit_extender_14_out,
       divider_1_out, divider_1_rem, multiplier_1_cout, multiplier_1_out, nand_1_out, or_1_out,
       shifter_1_out, shifter_2_out, shifter_3_out, shifter_4_out, subtractor_1_out, xor_1_out;
  wire [15:0] bit_extender_4_out, bit_extender_5_out, bit_extender_6_out, bit_extender_7_out,
       bit_extender_8_out, bit_extender_9_out, bit_extender_10_out, bit_extender_11_out;

  Bit_Extender #(.out_width(3)) bit_extender_1 (.in(B), .out(bit_extender_1_out));
  Adder adder_1 (.a(A), .b(B), .out(adder_1_out), .cout(adder_1_cout));  // open: cin
  Subtractor subtractor_1 (.a(A), .b(B), .out(subtractor_1_out), .bout(subtractor_1_bout));  // open: bin
  Multiplier multiplier_1 (.a(A), .b(B), .out(multiplier_1_out), .cout(multiplier_1_cout));  // open: cin
  Divider divider_1 (.a(A), .b(B), .out(divider_1_out), .rem(divider_1_rem));  // open: upper
  assign and_1_out = A & B;  // AND_Gate and_1, 8 bits wide
  assign or_1_out = A | B;  // OR_Gate or_1, 8 bits wide
  assign xor_1_out = A ^ B;  // XOR_Gate xor_1, 8 bits wide
  assign nand_1_out = ~(A & B);  // NAND_Gate nand_1, 8 bits wide
  Shifter shifter_1 (.in(A), .\dist (bit_extender_1_out), .out(shifter_1_out));
  Shifter #(.shift("lr")) shifter_2 (.in(A), .\dist (bit_extender_1_out), .out(shifter_2_out));
  Shifter #(.shift("rl")) shifter_3 (.in(A), .\dist (bit_extender_1_out), .out(shifter_3_out));
  Shifter #(.shift("rr")) shifter_4 (.in(A), .\dist (bit_extender_1_out), .out(shifter_4_out));
  Comparator comparator_1 (.a(A), .b(B), .gt(comparator_1_gt), .eq(comparator_1_eq), .lt(comparator_1_lt));
  assign bit_extender_2_out = {{7{1'b0}}, adder_1_cout};  // Bit_Extender bit_extender_2
  assign bit_extender_3_out = {{7{1'b0}}, subtractor_1_bout};  // Bit_Extender bit_extender_3
  assign bit_extender_4_out = {{8{1'b0}}, and_1_out};  // Bit_Extender bit_extender_4
  assign bit_extender_5_out = {{8{1'b0}}, or_1_out};  // Bit_Extender bit_extender_5
  assign bit_extender_6_out = {{8{1'b0}}, xor_1_out};  // Bit_Extender bit_extender_6
  assign bit_extender_7_out = {{8{1'b0}}, nand_1_out};  // Bit_Extender bit_extender_7
  assign bit_extender_8_out = {{8{1'b0}}, shifter_1_out};  // Bit_Extender bit_extender_8
  assign bit_extender_9_out = {{8{1'b0}}, shifter_2_out};  // Bit_Extender bit_extender_9
  assign bit_extender_10_out = {{8{1'b0}}, shifter_3_out};  // Bit_Extender bit_extender_10
  assign bit_extender_11_out = {{8{1'b0}}, shifter_4_out};  // Bit_Extender bit_extender_11
  assign bit_extender_12_out = {{3{1'b0}}, comparator_1_gt};  // Bit_Extender bit_extender_12
  assign bit_extender_13_out = {{3{1'b0}}, comparator_1_eq};  // Bit_Extender bit_extender_13
  assign bit_extender_14_out = {{7{1'b0}}, comparator_1_lt};  // Bit_Extender bit_extender_14
  Multiplexer #(.select(4), .width(16), .enable("false")) multiplexer_1 (
    .in0({bit_extender_2_out, adder_1_out}), .in1({bit_extender_3_out, subtractor_1_out}),
    .in2({multiplier_1_cout, multiplier_1_out}), .in3({divider_1_rem, divider_1_out}),
    .in4(bit_extender_4_out), .in5(bit_extender_5_out), .in6(bit_extender_6_out), .in7(bit_extender_7_out),
    .in8(bit_extender_8_out), .in9(bit_extender_9_out), .in10(bit_extender_10_out),
    .in11(bit_extender_11_out), .in12({bit_extender_14_out, bit_extender_13_out, bit_extender_12_out}),
    .out(DATA_OUT), .sel(in_3));  // open: in13, in14, in15
endmodule

// REG FILE
module REGISTER_8_BITS (
  input  CLOCK,
  input  [7:0] DATA_IN,
  input  [2:0] RX,
  input  R_W_prime,
  output [7:0] DATA_OUT
);

  wire decoder_1_out0, decoder_1_out1, decoder_1_out2, decoder_1_out3, decoder_1_out4, decoder_1_out5,
       decoder_1_out6, decoder_1_out7, not_1_out;
  wire [7:0] register_1_q, register_2_q, register_3_q, register_4_q, register_5_q, register_6_q,
       register_7_q, register_8_q;

  Hex_Digit_Display hex_digit_display_1 (.value(DATA_IN[7:4]));  // open: dp
  not not_1 (not_1_out, R_W_prime);
  Hex_Digit_Display hex_digit_display_2 (.value(DATA_IN[3:0]));  // open: dp
  Decoder #(.select(3), .disabled(0)) decoder_1 (
    .out0(decoder_1_out0), .out1(decoder_1_out1), .out2(decoder_1_out2), .out3(decoder_1_out3),
    .out4(decoder_1_out4), .out5(decoder_1_out5), .out6(decoder_1_out6), .out7(decoder_1_out7), .sel(RX),
    .en(not_1_out));
  Register register_1 (.D(DATA_IN), .en(decoder_1_out0), .Q(register_1_q), .clk(CLOCK));  // open: clr
  Register register_2 (.D(DATA_IN), .en(decoder_1_out1), .Q(register_2_q), .clk(CLOCK));  // open: clr
  Register register_3 (.D(DATA_IN), .en(decoder_1_out2), .Q(register_3_q), .clk(CLOCK));  // open: clr
  Register register_4 (.D(DATA_IN), .en(decoder_1_out3), .Q(register_4_q), .clk(CLOCK));  // open: clr
  Register register_5 (.D(DATA_IN), .en(decoder_1_out4), .Q(register_5_q), .clk(CLOCK));  // open: clr
  Register register_6 (.D(DATA_IN), .en(decoder_1_out5), .Q(register_6_q), .clk(CLOCK));  // open: clr
  Register register_7 (.D(DATA_IN), .en(decoder_1_out6), .Q(register_7_q), .clk(CLOCK));  // open: clr
  Register register_8 (.D(DATA_IN), .en(decoder_1_out7), .Q(register_8_q), .clk(CLOCK));  // open: clr
  Multiplexer #(.select(3), .width(8)) multiplexer_1 (
    .in0(register_1_q), .in1(register_2_q), .in2(register_3_q), .in3(register_4_q), .in4(register_5_q),
    .in5(register_6_q), .in6(register_7_q), .in7(register_8_q), .out(DATA_OUT), .sel(RX), .en(R_W_prime));
  Hex_Digit_Display hex_digit_display_3 (.value(DATA_OUT[7:4]));  // open: dp
  Hex_Digit_Display hex_digit_display_4 (.value(DATA_OUT[3:0]));  // open: dp
endmodule

module Using_ROM_for_instruction (
  input  [7:0] in_1,
  input  [7:0] DATA_IN,
  input  [7:0] DATA,
  input  R_W_prime,
  output [15:0] out_5
);

  wire clock_1_out, not_1_out;
  wire [7:0] ram_1_data, register_8_bits_1_data_out;
  wire [14:0] rom_1_data;

  Clock clock_1 (.out(clock_1_out));
  ROM #(.dataWidth(15)) rom_1 (.addr(in_1), .data(rom_1_data));  // open: sel
  not not_1 (not_1_out, R_W_prime);
  RAM #(.bus("separate")) ram_1 (
    .addr(rom_1_data[7:0]), .din(DATA), .data(ram_1_data), .str(not_1_out), .clk(clock_1_out), .ld(R_W_prime));  // open: sel, clr
  REGISTER_8_BITS register_8_bits_1 (
    .DATA_IN(DATA_IN), .CLOCK(clock_1_out), .R_W_prime(R_W_prime), .RX(rom_1_data[10:8]),
    .DATA_OUT(register_8_bits_1_data_out));
  ALU_8BITS alu_8bits_1 (.A(register_8_bits_1_data_out), .B(ram_1_data), .in_3(rom_1_data[14:11]), .DATA_OUT(out_5));
  Hex_Digit_Display hex_digit_display_1 (.value(out_5[11:8]));  // open: dp
  Hex_Digit_Display hex_digit_display_2 (.value(out_5[15:12]));  // open: dp
  Hex_Digit_Display hex_digit_display_3 (.value(out_5[7:4]));  // open: dp
  Hex_Digit_Display hex_digit_display_4 (.value(out_5[3:0]));  // open: dp

  // Notes on the sheet:
  //   Code Memory
endmodule
