// Logisim project faltu.circ as structural Verilog: 3 circuits, main circuit main
module main (
  input  [7:0] Address,
  input  [15:0] Data_in,
  input  in_3,
  output [7:0] out_4,
  output [7:0] out_5,
  output [15:0] out_6,
  output [7:0] out_7,
  output [7:0] out_8,
  output [15:0] out_9
);

  wire clock_1_out, decoder_1_out0, decoder_1_out1, not_1_out, not_2_out;

  Decoder decoder_1 (.out0(decoder_1_out0), .out1(decoder_1_out1), .sel(in_3));  // open: en
  Clock clock_1 (.out(clock_1_out));
  not not_1 (not_1_out, decoder_1_out0);
  not not_2 (not_2_out, decoder_1_out1);
  RAM #(.bus("separate")) ram_1 (
    .addr(Address), .din(Data_in[15:8]), .data(out_4), .str(not_1_out), .clk(clock_1_out), .ld(decoder_1_out0));  // open: sel, clr
  RAM #(.bus("separate")) ram_2 (
    .addr(Address), .din(Data_in[15:8]), .data(out_7), .str(not_2_out), .clk(clock_1_out), .ld(decoder_1_out1));  // open: sel, clr
  RAM #(.bus("separate")) ram_3 (
    .addr(Address), .din(Data_in[7:0]), .data(out_5), .str(not_1_out), .clk(clock_1_out), .ld(decoder_1_out0));  // open: sel, clr
  RAM #(.bus("separate")) ram_4 (
    .addr(Address), .din(Data_in[7:0]), .data(out_8), .str(not_2_out), .clk(clock_1_out), .ld(decoder_1_out1));  // open: sel, clr

  assign out_6 = {out_4, out_5};
  assign out_9 = {out_7, out_8};
endmodule

module uisngsplitter (
  input  [15:0] Data_In,
  input  [8:0] Addr,
  input  R_W,
  input  CLr,
  output [15:0] out_5,
  output [15:0] out_6
);

  wire clock_1_out, decoder_1_out0, decoder_1_out1, not_1_out;

  Decoder decoder_1 (.out0(decoder_1_out0), .out1(decoder_1_out1), .sel(Addr[8]));  // open: en
  Clock clock_1 (.out(clock_1_out));
  not not_1 (not_1_out, R_W);
  RAM #(.bus("separate")) ram_1 (
    .addr(Addr[7:0]), .din(Data_In[15:8]), .data(out_5[15:8]), .str(not_1_out), .sel(decoder_1_out0),
    .clk(clock_1_out), .ld(R_W), .clr(CLr));
  RAM #(.bus("separate")) ram_2 (
    .addr(Addr[7:0]), .din(Data_In[15:8]), .data(out_6[15:8]), .str(not_1_out), .sel(decoder_1_out1),
    .clk(clock_1_out), .ld(R_W), .clr(CLr));
  RAM #(.bus("separate")) ram_3 (
    .addr(Addr[7:0]), .din(Data_In[7:0]), .data(out_5[7:0]), .sel(decoder_1_out0), .clk(clock_1_out),
    .ld(R_W), .clr(CLr));  // open: str
  RAM #(.bus("separate")) ram_4 (
    .addr(Addr[7:0]), .din(Data_In[7:0]), .data(out_6[7:0]), .sel(decoder_1_out1), .clk(clock_1_out),
    .ld(R_W), .clr(CLr));  // open: str
endmodule

module _256_16using64_8 (
  input  in_1,
  input  [7:0] ADDr,
  input  in_3,
  output [7:0] out_4
);

  wire decoder_1_out0, decoder_1_out1, decoder_1_out2, decoder_1_out3, not_1_out, undriven, undriven_2,
       undriven_3, undriven_4;

  Decoder #(.select(2), .tristate("true")) decoder_1 (
    .out0(decoder_1_out0), .out1(decoder_1_out1), .out2(decoder_1_out2), .out3(decoder_1_out3),
    .sel(ADDr[7:6]));  // open: en
  Clock clock_1 (.out(in_3));
  not not_1 (not_1_out, in_3);
  RAM #(.addrWidth(6), .dataWidth(3), .bus("separate")) ram_1 (
    .addr(ADDr[5:0]), .str(not_1_out), .sel(decoder_1_out0), .clk(in_3), .ld(in_3));  // open: din, data, clr
  RAM #(.addrWidth(6), .dataWidth(3), .bus("separate")) ram_2 (
    .str(not_1_out), .sel(undriven_2), .clk(in_3), .ld(in_3));  // open: addr, din, data, clr
  RAM #(.addrWidth(6), .dataWidth(3), .bus("separate")) ram_3 (
    .str(not_1_out), .sel(undriven_4), .clk(in_3), .ld(in_3));  // open: addr, din, data, clr
  RAM #(.addrWidth(6), .dataWidth(3), .bus("separate")) ram_4 (
    .str(not_1_out), .sel(undriven), .clk(in_3), .ld(in_3));  // open: addr, din, data, clr
  RAM #(.addrWidth(6), .dataWidth(3), .bus("separate")) ram_5 (
    .str(not_1_out), .sel(decoder_1_out0), .clk(in_3), .ld(in_3));  // open: addr, din, data, clr
  RAM #(.addrWidth(6), .dataWidth(3), .bus("separate")) ram_6 (
    .str(not_1_out), .sel(undriven_3), .clk(in_3), .ld(in_3));  // open: addr, din, data, clr
  RAM #(.addrWidth(6), .dataWidth(3), .bus("separate")) ram_7 (
    .str(not_1_out), .sel(undriven_4), .clk(in_3), .ld(in_3));  // open: addr, din, data, clr
  RAM #(.addrWidth(6), .dataWidth(3), .bus("separate")) ram_8 (
    .str(not_1_out), .sel(undriven), .clk(in_3), .ld(in_3));  // open: addr, din, data, clr
endmodule
