// Logisim project final verybad 1.circ as structural Verilog: 7 circuits, main circuit main
module main (
  input  [31:0] in_1,
  input  [31:0] PC_In,
  output [31:0] PC_OUT,
  output [31:0] RESULT
);

  wire bit_extender_1_out, bit_extender_2_out, clock, MUX_2_out, mux_shifter_1, mux_shifter_2, not_1_out,
       not_2_out, PC_SHIFTER_out, reset;
  wire [3:0] ALU_OPCODE, CC;
  wire [11:0] bit_extender_3_out, direct_addr, IR_q, multiplexer_1_out, multiplexer_2_out, ram_1_data;
  wire [31:0] AC_q, demultiplexer_1_out0, dmx_output, dmx_output_t, MAR_q, MBR_q, multiplexer_3_out, RA_q,
       rom_1_data;

  Button button_1 (.out(reset));
  Clock clock_1 (.out(clock));
  PC pc_1 (.data_in(PC_In), .clock(clock), .PC_Enable(PC_SHIFTER_out), .reset(reset), .data_out(PC_OUT));
  counter counter_1 (.clock(clock), .out_2(CC));
  Register #(.width(32)) MAR (.D(PC_OUT), .en(PC_SHIFTER_out), .Q(MAR_q), .clk(clock), .clr(reset));
  Shift_Register #(.length(6)) PC_SHIFTER (
    .in(PC_SHIFTER_out), .clk(clock), .out(PC_SHIFTER_out));  // open: shift, load, clr, d0, q0, d1, q1, d2, q2, d3, q3, d4, q4, d5, q5
  Bit_Extender #(.in_width(20), .out_width(1)) bit_extender_1 (.in(MAR_q[31:12]), .out(bit_extender_1_out));
  Hex_Digit_Display hex_digit_display_1 (.value(CC));  // open: dp
  Multiplexer #(.width(12), .enable("false")) multiplexer_1 (
    .in0(MAR_q[11:0]), .in1(direct_addr), .out(multiplexer_1_out), .sel(mux_shifter_1));
  not not_1 (not_1_out, PC_SHIFTER_out);
  Demultiplexer #(.width(32), .enable("false")) demultiplexer_1 (
    .out0(demultiplexer_1_out0), .out1(dmx_output_t), .in(rom_1_data), .sel(MUX_2_out));
  Shift_Register #(.length(5)) MUX (
    .in(mux_shifter_1), .clk(clock), .out(mux_shifter_1));  // open: shift, load, clr, d0, q0, d1, q1, d2, q2, d3, q3, d4, q4
  Register #(.width(32)) MBR (.D(demultiplexer_1_out0), .Q(MBR_q), .clk(clock), .clr(reset));  // open: en
  ROM #(.addrWidth(12), .dataWidth(32)) rom_1 (.addr(multiplexer_1_out), .data(rom_1_data));  // open: sel
  Bit_Extender #(.in_width(16), .out_width(1)) bit_extender_2 (.in(MBR_q[31:16]), .out(bit_extender_2_out));
  Register #(.width(16)) IR (.D(MBR_q[15:0]), .Q({ALU_OPCODE, IR_q}), .clk(clock), .clr(reset));  // open: en
  Shift_Register #(.length(6)) MUX_2 (
    .in(MUX_2_out), .clk(clock), .out(MUX_2_out));  // open: shift, load, clr, d0, q0, d1, q1, d2, q2, d3, q3, d4, q4, d5, q5
  not not_2 (not_2_out, not_1_out);
  Multiplexer #(.width(12)) multiplexer_2 (
    .in0(direct_addr), .in1(bit_extender_3_out), .out(multiplexer_2_out), .sel(not_2_out));  // open: en
  RAM #(.addrWidth(12), .dataWidth(12), .bus("separate")) ram_1 (
    .addr(IR_q), .din(multiplexer_2_out), .data(ram_1_data), .str(not_2_out), .clk(clock), .ld(not_1_out));  // open: sel, clr
  Register #(.width(12)) RY (.D(ram_1_data), .Q(direct_addr), .clk(clock), .clr(reset));  // open: en
  Register #(.width(32)) RA (.D(in_1), .Q(RA_q), .clk(clock), .clr(reset));  // open: en
  Shift_Register #(.length(7)) MUX_3 (
    .in(mux_shifter_2), .clk(clock), .out(mux_shifter_2));  // open: shift, load, clr, d0, q0, d1, q1, d2, q2, d3, q3, d4, q4, d5, q5, d6, q6
  Multiplexer #(.width(32), .enable("false")) multiplexer_3 (
    .in0(dmx_output), .in1(RESULT), .out(multiplexer_3_out), .sel(mux_shifter_2));
  Register #(.width(32)) AC (.D(multiplexer_3_out), .Q(AC_q), .clk(clock), .clr(reset));  // open: en
  ALU_final alu_final_1 (.A(RA_q), .B(AC_q), .opcode(ALU_OPCODE), .DATA_OUT(RESULT));  // open: in_2, out_6
  Bit_Extender #(.in_width(32), .out_width(12)) bit_extender_3 (.in(RESULT), .out(bit_extender_3_out));
  // also tied to GND on the sheet: {bit_extender_1_out, bit_extender_2_out}

  // Notes on the sheet:
  //   000001
  //   Code Memory
  //   contents of rom_1 (hex, n*v repeats v):
  //   2201 2201 4*0 300 505*0 5 0 25
  //   00001
  //   100000
  //   DATA MEMORY
  //   1000000
endmodule

// REGISTER
module register_file (
  input  [31:0] DATA_inside,
  input  clk,
  input  r_w_prime,
  input  [3:0] opcode,
  output [31:0] data_out
);

  wire decoder_1_out0, decoder_1_out1, decoder_1_out2, decoder_1_out3, decoder_1_out4, decoder_1_out5,
       decoder_1_out6, decoder_1_out7, decoder_1_out8, decoder_1_out9, decoder_1_out10, decoder_1_out11,
       decoder_1_out12, decoder_1_out13, decoder_1_out14, decoder_1_out15, not_1_out;
  wire [31:0] register_1_q, register_2_q, register_3_q, register_4_q, register_5_q, register_6_q,
       register_7_q, register_8_q, register_9_q, register_10_q, register_11_q, register_12_q, register_13_q,
       register_14_q, register_15_q, register_16_q;

  not not_1 (not_1_out, r_w_prime);
  Decoder #(.select(4)) decoder_1 (
    .out0(decoder_1_out0), .out1(decoder_1_out1), .out2(decoder_1_out2), .out3(decoder_1_out3),
    .out4(decoder_1_out4), .out5(decoder_1_out5), .out6(decoder_1_out6), .out7(decoder_1_out7),
    .out8(decoder_1_out8), .out9(decoder_1_out9), .out10(decoder_1_out10), .out11(decoder_1_out11),
    .out12(decoder_1_out12), .out13(decoder_1_out13), .out14(decoder_1_out14), .out15(decoder_1_out15),
    .sel(opcode), .en(not_1_out));
  Register #(.width(32)) register_1 (.D(DATA_inside), .en(decoder_1_out0), .Q(register_1_q), .clk(clk));  // open: clr
  Register #(.width(32)) register_2 (.D(DATA_inside), .en(decoder_1_out1), .Q(register_2_q), .clk(clk));  // open: clr
  Register #(.width(32)) register_3 (.D(DATA_inside), .en(decoder_1_out2), .Q(register_3_q), .clk(clk));  // open: clr
  Register #(.width(32)) register_4 (.D(DATA_inside), .en(decoder_1_out3), .Q(register_4_q), .clk(clk));  // open: clr
  Register #(.width(32)) register_5 (.D(DATA_inside), .en(decoder_1_out4), .Q(register_5_q), .clk(clk));  // open: clr
  Register #(.width(32)) register_6 (.D(DATA_inside), .en(decoder_1_out5), .Q(register_6_q), .clk(clk));  // open: clr
  Register #(.width(32)) register_7 (.D(DATA_inside), .en(decoder_1_out6), .Q(register_7_q), .clk(clk));  // open: clr
  Register #(.width(32)) register_8 (.D(DATA_inside), .en(decoder_1_out7), .Q(register_8_q), .clk(clk));  // open: clr
  Register #(.width(32)) register_9 (.D(DATA_inside), .en(decoder_1_out8), .Q(register_9_q), .clk(clk));  // open: clr
  Register #(.width(32)) register_10 (.D(DATA_inside), .en(decoder_1_out9), .Q(register_10_q), .clk(clk));  // open: clr
  Register #(.width(32)) register_11 (
    .D(DATA_inside), .en(decoder_1_out10), .Q(register_11_q), .clk(clk));  // open: clr
  Register #(.width(32)) register_12 (
    .D(DATA_inside), .en(decoder_1_out11), .Q(register_12_q), .clk(clk));  // open: clr
  Register #(.width(32)) register_13 (
    .D(DATA_inside), .en(decoder_1_out12), .Q(register_13_q), .clk(clk));  // open: clr
  Register #(.width(32)) register_14 (
    .D(DATA_inside), .en(decoder_1_out13), .Q(register_14_q), .clk(clk));  // open: clr
  Register #(.width(32)) register_15 (
    .D(DATA_inside), .en(decoder_1_out14), .Q(register_15_q), .clk(clk));  // open: clr
  Register #(.width(32)) register_16 (
    .D(DATA_inside), .en(decoder_1_out15), .Q(register_16_q), .clk(clk));  // open: clr
  Multiplexer #(.select(4), .width(32)) multiplexer_1 (
    .in0(register_1_q), .in1(register_2_q), .in2(register_3_q), .in3(register_4_q), .in4(register_5_q),
    .in5(register_6_q), .in6(register_7_q), .in7(register_8_q), .in8(register_9_q), .in9(register_10_q),
    .in10(register_11_q), .in11(register_12_q), .in12(register_13_q), .in13(register_14_q),
    .in14(register_15_q), .in15(register_16_q), .out(data_out), .sel(opcode), .en(r_w_prime));
endmodule

module PC (
  input  [31:0] data_in,
  input  PC_Enable,
  input  clock,
  input  reset,
  output [31:0] data_out
);

  wire [31:0] adder_1_out;

  Adder #(.width(32)) adder_1 (.a(data_in), .b(data_out), .out(adder_1_out), .cin(1'b1));  // open: cout
  Register #(.width(32)) register_1 (.D(adder_1_out), .en(PC_Enable), .Q(data_out), .clk(clock), .clr(reset));
  Hex_Digit_Display hex_digit_display_1 (.value(data_out[27:24]));  // open: dp
  Hex_Digit_Display hex_digit_display_2 (.value(data_out[31:28]));  // open: dp
  Hex_Digit_Display hex_digit_display_3 (.value(data_out[19:16]));  // open: dp
  Hex_Digit_Display hex_digit_display_4 (.value(data_out[23:20]));  // open: dp
  Hex_Digit_Display hex_digit_display_5 (.value(data_out[15:12]));  // open: dp
  Hex_Digit_Display hex_digit_display_6 (.value(data_out[11:8]));  // open: dp
  Hex_Digit_Display hex_digit_display_7 (.value(data_out[3:0]));  // open: dp
  Hex_Digit_Display hex_digit_display_8 (.value(data_out[7:4]));  // open: dp
endmodule

// ALU
module ALU_final (
  input  [31:0] A,
  input  in_2,
  input  [31:0] B,
  input  [3:0] opcode,
  output [31:0] DATA_OUT,
  output out_6
);

  wire adder_1_cout, subtractor_1_bout;
  wire [4:0] bit_extender_3_out;
  wire [15:0] bit_extender_1_out;
  wire [31:0] adder_1_out, adder_2_out, and_1_out, divider_1_out, multiplier_1_out, not_1_out, or_1_out,
       shifter_1_out, shifter_2_out, shifter_3_out, shifter_4_out, subtractor_1_out, subtractor_2_out;
  wire [31:16] bit_extender_2_out;

  Bit_Extender #(.in_width(32)) bit_extender_1 (.in(B), .out(bit_extender_1_out));
  Bit_Extender #(.in_width(32)) bit_extender_2 (.in(A), .out(bit_extender_2_out));
  Bit_Extender #(.in_width(32), .out_width(5)) bit_extender_3 (.in(B), .out(bit_extender_3_out));
  Adder #(.width(32)) adder_1 (.a(A), .b(B), .out(adder_1_out), .cout(adder_1_cout));  // open: cin
  Subtractor #(.width(32)) subtractor_1 (.a(A), .b(B), .out(subtractor_1_out), .bout(subtractor_1_bout));  // open: bin
  Multiplier #(.width(32)) multiplier_1 (.a(A), .b(B), .out(multiplier_1_out));  // open: cin, cout
  Divider #(.width(32)) divider_1 (.a(A), .b(B), .out(divider_1_out));  // open: upper, rem
  Adder #(.width(32)) adder_2 (.a(A), .b(32'hc), .out(adder_2_out));  // open: cin, cout
  Subtractor #(.width(32)) subtractor_2 (.a(A), .b(32'hc), .out(subtractor_2_out));  // open: bin, bout
  assign and_1_out = A & B;  // AND_Gate and_1, 32 bits wide
  assign or_1_out = A | B;  // OR_Gate or_1, 32 bits wide
  assign not_1_out = ~A;  // NOT_Gate not_1, 32 bits wide
  Shifter #(.width(32)) shifter_1 (.in(A), .\dist (bit_extender_3_out), .out(shifter_1_out));
  Shifter #(.width(32), .shift("lr")) shifter_2 (.in(A), .\dist (bit_extender_3_out), .out(shifter_2_out));
  Shifter #(.width(32), .shift("rl")) shifter_3 (.in(A), .\dist (bit_extender_3_out), .out(shifter_3_out));
  Shifter #(.width(32), .shift("rr")) shifter_4 (.in(A), .\dist (bit_extender_3_out), .out(shifter_4_out));
  Multiplexer #(.enable("false")) multiplexer_1 (.in0(adder_1_cout), .in1(subtractor_1_bout), .out(out_6), .sel(in_2));
  Multiplexer #(.select(4), .width(32), .enable("false")) multiplexer_2 (
    .in0(B), .in1(A), .in2(adder_1_out), .in3(subtractor_1_out), .in4(multiplier_1_out), .in5(divider_1_out),
    .in6(adder_2_out), .in7(subtractor_2_out), .in8(and_1_out), .in9(or_1_out), .in10(not_1_out),
    .in11({bit_extender_2_out, bit_extender_1_out}), .in12(shifter_1_out), .in13(shifter_2_out),
    .in14(shifter_3_out), .in15(shifter_4_out), .out(DATA_OUT), .sel(opcode));

  // Other names for the same wires on the sheet: carry = out_6
endmodule

module trial (
  input  [31:0] in_1,
  input  [31:0] PC_In,
  input  in_3,
  input  [3:0] opcode,
  output [31:0] PC_OUT,
  output [31:0] RESULT
);

  wire bit_extender_1_out, bit_extender_2_out, clock, MUX_out, not_1_out, not_2_out, PC_Shift_out, reset;
  wire [3:0] CC;
  wire [11:0] multiplexer_1_out, ram_1_data, RY_q, undriven;
  wire [15:0] IR_q;
  wire [31:0] AC_q, MAR_q, MBR_q, multiplexer_2_out, RA_q, RB_q, register_file_1_data_out, rom_1_data,
       undriven_2, undriven_3;

  PC pc_1 (.data_in(PC_In), .clock(clock), .PC_Enable(PC_Shift_out), .reset(reset), .data_out(PC_OUT));
  counter counter_1 (.clock(clock), .out_2(CC));
  Register #(.width(32)) MAR (.D(PC_OUT), .en(PC_Shift_out), .Q(MAR_q), .clk(clock), .clr(reset));
  Shift_Register #(.length(5)) PC_Shift (
    .in(PC_Shift_out), .clk(clock), .out(PC_Shift_out));  // open: shift, load, clr, d0, q0, d1, q1, d2, q2, d3, q3, d4, q4
  Shift_Register #(.length(3)) MUX (
    .shift(1'b1), .in(MUX_out), .clk(clock), .out(MUX_out));  // open: load, clr, d0, q0, d1, q1, d2, q2
  Bit_Extender #(.in_width(20), .out_width(1)) bit_extender_1 (.in(MAR_q[31:12]), .out(bit_extender_1_out));
  Multiplexer #(.width(12), .enable("false")) multiplexer_1 (
    .in0(MAR_q[11:0]), .in1(RY_q), .out(multiplexer_1_out), .sel(MUX_out));
  not not_1 (not_1_out, PC_Shift_out);
  Hex_Digit_Display hex_digit_display_1 (.value(CC));  // open: dp
  Register #(.width(32)) MBR (.D(rom_1_data), .Q(MBR_q), .clk(clock), .clr(reset));  // open: en
  ROM #(.addrWidth(12), .dataWidth(32)) rom_1 (.addr(multiplexer_1_out), .data(rom_1_data));  // open: sel
  Clock clock_1 (.out(clock));
  Bit_Extender #(.in_width(16), .out_width(1)) bit_extender_2 (.in(MBR_q[31:16]), .out(bit_extender_2_out));
  Register #(.width(16)) IR (.D(MBR_q[15:0]), .Q(IR_q), .clk(clock), .clr(reset));  // open: en
  not not_2 (not_2_out, not_1_out);
  RAM #(.addrWidth(12), .dataWidth(12), .bus("separate")) ram_1 (
    .addr(IR_q[11:0]), .din(undriven), .data(ram_1_data), .str(not_2_out), .clk(clock), .ld(not_1_out));  // open: sel, clr
  register_file register_file_1 (
    .DATA_inside(in_1), .clk(clock), .r_w_prime(not_1_out), .data_out(register_file_1_data_out),
    .opcode(opcode));
  Register #(.width(12)) RY (.D(ram_1_data), .Q(RY_q), .clk(clock));  // open: en, clr
  Register #(.width(32)) RA (.D(register_file_1_data_out), .Q(RA_q), .clk(clock), .clr(reset));  // open: en
  Multiplexer #(.width(32), .enable("false")) multiplexer_2 (
    .in0(undriven_2), .in1(RESULT), .out(multiplexer_2_out), .sel(in_3));
  Register #(.width(32)) AC (.D(multiplexer_2_out), .Q(AC_q), .clk(clock), .clr(reset));  // open: en
  ALU_final alu_final_1 (.A(RA_q), .B(AC_q), .opcode(IR_q[15:12]), .DATA_OUT(RESULT));  // open: in_2, out_6
  Register #(.width(32)) RB (.D(undriven_3), .Q(RB_q));  // open: en, clk, clr
  assign undriven_3[31:12] = {{19{1'b0}}, 1'b0};  // Bit_Extender bit_extender_3
  // also tied to GND on the sheet: {bit_extender_1_out, bit_extender_2_out}

  // Notes on the sheet:
  //   Code Memory
  //   contents of rom_1 (hex, n*v repeats v):
  //   6*0 300
  //   DATA MEMORY
endmodule

module counter (
  input  clock,
  output [3:0] out_2
);

  Counter #(.width(4), .max('h4)) counter_1 (.Q(out_2), .clk(clock));  // open: load, D, count, carry, clr
endmodule

module \reg  (
  input  [31:0] DATA_inside,
  input  clk,
  input  r_w_prime,
  input  [3:0] opcode,
  output [31:0] data_out
);

  wire decoder_1_out0, decoder_1_out1, decoder_1_out2, decoder_1_out3, decoder_1_out4, decoder_1_out5,
       decoder_1_out6, decoder_1_out7, decoder_1_out8, decoder_1_out9, decoder_1_out10, decoder_1_out11,
       decoder_1_out12, decoder_1_out13, decoder_1_out14, decoder_1_out15, not_1_out;
  wire [31:0] register_1_q, register_2_q, register_3_q, register_4_q, register_5_q, register_6_q,
       register_7_q, register_8_q, register_9_q, register_10_q, register_11_q, register_12_q, register_13_q,
       register_14_q, register_15_q, register_16_q;

  not not_1 (not_1_out, r_w_prime);
  Decoder #(.select(4)) decoder_1 (
    .out0(decoder_1_out0), .out1(decoder_1_out1), .out2(decoder_1_out2), .out3(decoder_1_out3),
    .out4(decoder_1_out4), .out5(decoder_1_out5), .out6(decoder_1_out6), .out7(decoder_1_out7),
    .out8(decoder_1_out8), .out9(decoder_1_out9), .out10(decoder_1_out10), .out11(decoder_1_out11),
    .out12(decoder_1_out12), .out13(decoder_1_out13), .out14(decoder_1_out14), .out15(decoder_1_out15),
    .sel(opcode), .en(not_1_out));
  Register #(.width(32)) register_1 (.D(DATA_inside), .en(decoder_1_out0), .Q(register_1_q), .clk(clk));  // open: clr
  Register #(.width(32)) register_2 (.D(DATA_inside), .en(decoder_1_out1), .Q(register_2_q), .clk(clk));  // open: clr
  Register #(.width(32)) register_3 (.D(DATA_inside), .en(decoder_1_out2), .Q(register_3_q), .clk(clk));  // open: clr
  Register #(.width(32)) register_4 (.D(DATA_inside), .en(decoder_1_out3), .Q(register_4_q), .clk(clk));  // open: clr
  Register #(.width(32)) register_5 (.D(DATA_inside), .en(decoder_1_out4), .Q(register_5_q), .clk(clk));  // open: clr
  Register #(.width(32)) register_6 (.D(DATA_inside), .en(decoder_1_out5), .Q(register_6_q), .clk(clk));  // open: clr
  Register #(.width(32)) register_7 (.D(DATA_inside), .en(decoder_1_out6), .Q(register_7_q), .clk(clk));  // open: clr
  Register #(.width(32)) register_8 (.D(DATA_inside), .en(decoder_1_out7), .Q(register_8_q), .clk(clk));  // open: clr
  Register #(.width(32)) register_9 (.D(DATA_inside), .en(decoder_1_out8), .Q(register_9_q), .clk(clk));  // open: clr
  Register #(.width(32)) register_10 (.D(DATA_inside), .en(decoder_1_out9), .Q(register_10_q), .clk(clk));  // open: clr
  Register #(.width(32)) register_11 (
    .D(DATA_inside), .en(decoder_1_out10), .Q(register_11_q), .clk(clk));  // open: clr
  Register #(.width(32)) register_12 (
    .D(DATA_inside), .en(decoder_1_out11), .Q(register_12_q), .clk(clk));  // open: clr
  Register #(.width(32)) register_13 (
    .D(DATA_inside), .en(decoder_1_out12), .Q(register_13_q), .clk(clk));  // open: clr
  Register #(.width(32)) register_14 (
    .D(DATA_inside), .en(decoder_1_out13), .Q(register_14_q), .clk(clk));  // open: clr
  Register #(.width(32)) register_15 (
    .D(DATA_inside), .en(decoder_1_out14), .Q(register_15_q), .clk(clk));  // open: clr
  Register #(.width(32)) register_16 (
    .D(DATA_inside), .en(decoder_1_out15), .Q(register_16_q), .clk(clk));  // open: clr
  Multiplexer #(.select(4), .width(32)) multiplexer_1 (
    .in0(register_1_q), .in1(register_2_q), .in2(register_3_q), .in3(register_4_q), .in4(register_5_q),
    .in5(register_6_q), .in6(register_7_q), .in7(register_8_q), .in8(register_9_q), .in9(register_10_q),
    .in10(register_11_q), .in11(register_12_q), .in12(register_13_q), .in13(register_14_q),
    .in14(register_15_q), .in15(register_16_q), .out(data_out), .sel(opcode), .en(r_w_prime));
endmodule
