// Logisim project final1_kus-1.circ as structural Verilog: 6 circuits, main circuit main
module main (
  input  in_1,
  input  in_2,
  input  [15:0] in_3,
  output [3:0] out_4,
  output [3:0] out_5,
  output [15:0] out_6,
  output [7:0] out_7
);

  wire for_store_exchange_prime_o_p_for_ram, not_1_out, or_1_out, s1, s2, shift_register_1_out;
  wire [3:0] multiplexer_1_out, register_1_q, register_1_q_2;
  wire [7:0] AC_data, demultiplexer_1_out0, demultiplexer_1_out1, MAR_q, Operand_fetched, PC_pointer,
       ram_1_data, rom_1_data;

  PC PC (.counter(s1), .clock(in_1), .pointer(PC_pointer), .Reset(in_2));
  Shift_Register #(.length(5)) shift_register_1 (
    .in(shift_register_1_out), .clk(in_1), .out(shift_register_1_out), .q3(s2), .q4(s1));  // open: shift, load, clr, d0, q0, d1, q1, d2, q2, d3, d4
  or or_1 (or_1_out, s2, s1);
  Register MAR (.D(PC_pointer), .Q(MAR_q), .clk(in_1), .clr(in_2));  // open: en
  Multiplexer #(.width(4), .enable("false")) multiplexer_1 (
    .in0(out_4), .in1(register_1_q), .out(multiplexer_1_out), .sel(or_1_out));
  ac_ram_enable for_store_exchange_prime (
    .Opcode_in(out_5), .shift(s1), .o_p_for_RAM(for_store_exchange_prime_o_p_for_ram));  // open: out_3, out_5
  ROM rom_1 (.addr(MAR_q), .data(rom_1_data));  // open: sel
  Register MBR (.D(rom_1_data), .Q({out_5, out_4}), .clk(in_1), .clr(in_2));  // open: en
  RAM #(.addrWidth(4), .bus("separate")) ram_1 (
    .addr(multiplexer_1_out), .din(out_6[15:8]), .data(ram_1_data),
    .str(for_store_exchange_prime_o_p_for_ram), .clk(in_1), .ld(1'b1));  // open: sel, clr
  Demultiplexer #(.width(8), .enable("false")) demultiplexer_1 (
    .out0(demultiplexer_1_out0), .out1(demultiplexer_1_out1), .in(ram_1_data), .sel(not_1_out));
  not not_1 (not_1_out, or_1_out);
  Register register_1 (
    .D(demultiplexer_1_out1), .en(not_1_out), .Q({register_1_q_2, register_1_q}), .clk(in_1), .clr(in_2));
  Register register_2 (.D(demultiplexer_1_out0), .en(or_1_out), .Q(Operand_fetched), .clk(in_1), .clr(in_2));
  Register AC (.D(out_6[7:0]), .en(s1), .Q(AC_data), .clk(in_1), .clr(in_2));
  // ALU ALU: pin names not known; wires that end beside it: Operand_fetched, AC_data, out_6, out_5
  Hex_Digit_Display hex_digit_display_1 (.value(out_6[15:12]));  // open: dp
  Hex_Digit_Display hex_digit_display_2 (.value(out_6[11:8]));  // open: dp
  Hex_Digit_Display hex_digit_display_3 (.value(out_6[7:4]));  // open: dp
  Hex_Digit_Display hex_digit_display_4 (.value(out_6[3:0]));  // open: dp
  psw psw_1 (
    .OPERAND_A(AC_data), .OPERAND_B(Operand_fetched), .zero_16bit(in_3), .opcode(out_5), .Final_O(out_6),
    .FlagBits(out_7));  // open: in_5, in_6

  // Other names for the same wires on the sheet: memloc[3:0] = out_4; Opcode[3:0] = out_5; ALU_Output[15:0] = out_6;
  //   ALU_output_LSB[7:0] = out_6[7:0]; ALU_output_MSB[7:0] = out_6[15:8]; Clock = in_1; Reset = in_2

  // Notes on the sheet:
  //   contents of rom_1 (hex, n*v repeats v):
  //   1 21 23 33 0 f
endmodule

module PC (
  input  counter,
  input  Reset,
  input  clock,
  output [7:0] pointer
);

  Counter counter_1 (.load(1'b0), .D(pointer), .count(counter), .Q(pointer), .clk(clock), .clr(Reset));  // open: carry
endmodule

module ALU (
  input  [15:0] DataIn_A_8,
  input  [15:0] DataIn_B_8,
  input  [3:0] Opera,
  output [31:0] DataOut
);

  wire adder_1_cout, adder_2_cout, subtractor_1_bout, subtractor_2_bout;
  wire [15:0] adder_1_out, adder_2_out, and_1_out, bit_extender_1_out, bit_extender_2_out,
       bit_extender_3_out, bit_extender_4_out, divider_1_out, divider_1_rem, multiplier_1_cout,
       multiplier_1_out, not_1_out, or_1_out, subtractor_1_out, subtractor_2_out;
  wire [31:0] shifter_1_out, shifter_2_out, shifter_3_out, shifter_4_out;

  Adder #(.width(16)) adder_1 (.a(DataIn_A_8), .b(DataIn_B_8), .out(adder_1_out), .cout(adder_1_cout));  // open: cin
  assign bit_extender_1_out = {{15{1'b0}}, adder_1_cout};  // Bit_Extender bit_extender_1
  Subtractor #(.width(16)) subtractor_1 (
    .a(DataIn_B_8), .b(DataIn_A_8), .out(subtractor_1_out), .bout(subtractor_1_bout));  // open: bin
  assign bit_extender_2_out = {{15{1'b0}}, subtractor_1_bout};  // Bit_Extender bit_extender_2
  Multiplier #(.width(16)) multiplier_1 (
    .a(DataIn_A_8), .b(DataIn_B_8), .out(multiplier_1_out), .cout(multiplier_1_cout));  // open: cin
  Divider #(.width(16)) divider_1 (
    .a(DataIn_B_8), .b(DataIn_A_8), .out(divider_1_out), .rem(divider_1_rem));  // open: upper
  Adder #(.width(16)) adder_2 (.a(DataIn_A_8), .b({16{1'b0}}), .out(adder_2_out), .cin(1'b1), .cout(adder_2_cout));
  assign bit_extender_3_out = {{15{1'b0}}, adder_2_cout};  // Bit_Extender bit_extender_3
  Subtractor #(.width(16)) subtractor_2 (
    .a(DataIn_A_8), .b({16{1'b0}}), .out(subtractor_2_out), .bin(1'b1), .bout(subtractor_2_bout));
  assign bit_extender_4_out = {{15{1'b0}}, subtractor_2_bout};  // Bit_Extender bit_extender_4
  assign and_1_out = DataIn_A_8 & DataIn_B_8;  // AND_Gate and_1, 16 bits wide
  assign or_1_out = DataIn_A_8 | DataIn_B_8;  // OR_Gate or_1, 16 bits wide
  assign not_1_out = ~DataIn_A_8;  // NOT_Gate not_1, 16 bits wide
  Shifter #(.width(32), .shift("lr")) shifter_1 (
    .in({{16{1'b0}}, DataIn_A_8}), .\dist (DataIn_B_8[4:0]), .out(shifter_1_out));
  Shifter #(.width(32)) shifter_2 (.in({{16{1'b0}}, DataIn_A_8}), .\dist (DataIn_B_8[4:0]), .out(shifter_2_out));
  Shifter #(.width(32), .shift("rr")) shifter_3 (
    .in({{16{1'b0}}, DataIn_A_8}), .\dist (DataIn_B_8[4:0]), .out(shifter_3_out));
  Shifter #(.width(32), .shift("rl")) shifter_4 (
    .in({{16{1'b0}}, DataIn_A_8}), .\dist (DataIn_B_8[4:0]), .out(shifter_4_out));
  Multiplexer #(.select(4), .width(32)) multiplexer_1 (
    .in0({DataIn_B_8, DataIn_A_8}), .in1({DataIn_B_8, DataIn_A_8}), .in2({bit_extender_1_out, adder_1_out}),
    .in3({bit_extender_2_out, subtractor_1_out}), .in4({multiplier_1_cout, multiplier_1_out}),
    .in5({divider_1_rem, divider_1_out}), .in6({bit_extender_3_out, adder_2_out}),
    .in7({bit_extender_4_out, subtractor_2_out}), .in8({{16{1'b0}}, and_1_out}),
    .in9({{16{1'b0}}, or_1_out}), .in10({{16{1'b0}}, not_1_out}), .in11({DataIn_B_8, DataIn_A_8}),
    .in12(shifter_1_out), .in13(shifter_2_out), .in14(shifter_3_out), .in15(shifter_4_out), .out(DataOut),
    .sel(Opera));  // open: en
  // also tied to GND on the sheet: adder_2_cout
endmodule

module l_s (
  input  [7:0] Datain_A,
  input  [7:0] Datain_B,
  input  _0_for_load__1_for_store,
  output [7:0] out_4,
  output [7:0] out_5
);

  Multiplexer #(.width(8), .enable("false")) multiplexer_1 (
    .in0(Datain_A), .in1(Datain_B), .out(out_4), .sel(_0_for_load__1_for_store));
  Multiplexer #(.width(8), .enable("false")) multiplexer_2 (
    .in0(Datain_B), .in1(Datain_A), .out(out_5), .sel(_0_for_load__1_for_store));
endmodule

module ac_ram_enable (
  input  [3:0] Opcode_in,
  input  shift,
  output [3:0] out_3,
  output o_p_for_RAM,
  output [3:0] out_5
);

  wire comparator_1_eq, comparator_2_eq, or_1_out;

  Comparator #(.width(4), .mode("unsigned")) comparator_1 (
    .a(Opcode_in), .b(4'b0001), .eq(comparator_1_eq));  // open: gt, lt
  Comparator #(.width(4), .mode("unsigned")) comparator_2 (
    .a(Opcode_in), .b(4'b1011), .eq(comparator_2_eq));  // open: gt, lt
  or or_1 (or_1_out, comparator_1_eq, comparator_2_eq);
  and and_1 (o_p_for_RAM, or_1_out, shift);

  assign out_3 = 4'b0001;
  assign out_5 = 4'b1011;
endmodule

module psw (
  input  [15:0] Final_O,
  input  [7:0] OPERAND_A,
  input  [7:0] OPERAND_B,
  input  [15:0] zero_16bit,
  input  in_5,
  input  in_6,
  input  [3:0] opcode,
  output [7:0] FlagBits
);

  wire and_1_out, and_2_out, and_3_out, and_4_out, not_1_out, not_2_out, not_3_out,
       sign_bit_of_Mul_and_Div_out;

  xor sign_bit_of_Mul_and_Div (sign_bit_of_Mul_and_Div_out, OPERAND_A[7], OPERAND_B[7]);
  not not_1 (not_1_out, opcode[1]);
  Adder adder_1 (.a(OPERAND_A), .b(OPERAND_B), .cout(FlagBits[0]));  // open: out, cin
  not not_2 (not_2_out, opcode[3]);
  and and_1 (and_1_out, not_1_out, opcode[2]);
  Adder #(.width(4)) adder_2 (.a(OPERAND_A[3:0]), .b(OPERAND_B[3:0]), .cout(FlagBits[5]));  // open: out, cin
  and and_2 (and_2_out, and_1_out, not_2_out);
  not not_3 (not_3_out, and_2_out);
  Comparator #(.width(16)) comparator_1 (.a(Final_O), .b(zero_16bit), .eq(FlagBits[3]));  // open: gt, lt
  and and_3 (and_3_out, Final_O[7], not_3_out);
  and and_4 (and_4_out, sign_bit_of_Mul_and_Div_out, and_2_out);
  or or_1 (FlagBits[4], and_3_out, and_4_out);
  xor odd_parity_1 (FlagBits[1], Final_O[0], Final_O[1], Final_O[2], Final_O[3], Final_O[4], Final_O[5], Final_O[6], Final_O[7], Final_O[8], Final_O[9], Final_O[10], Final_O[11], Final_O[12], Final_O[13], Final_O[14], Final_O[15]);
  not not_4 (FlagBits[2], FlagBits[1]);

  assign FlagBits[7:6] = {in_6, in_5};

  // Notes on the sheet:
  //   sign bit(other 14ops)
  //   Zero
  //   Half Carry
endmodule
