// Logisim project indirect.circ as structural Verilog
module sfg (
  input  [15:0] in_1,
  input  in_2,
  input  in_3,
  input  in_4,
  input  [31:0] in_5,
  input  in_6,
  input  in_7,
  input  in_8,
  input  in_9,
  input  [3:0] in_10,
  output [11:0] out_11,
  output [11:0] out_12,
  output out_13,
  output [31:0] out_14,
  output [11:0] out_15,
  output out_16,
  output out_17
);

  wire clock_1_out, shift_register_1_out, undriven_2, undriven_3;
  wire [11:0] bit_extender_1_out, undriven;

  Clock clock_1 (.out(clock_1_out));
  Shift_Register #(.length(2)) shift_register_1 (
    .in(shift_register_1_out), .clk(clock_1_out), .out(shift_register_1_out));  // open: shift, load, clr, d0, q0, d1, q1
  Demultiplexer #(.width(12)) demultiplexer_1 (.out0(out_11), .out1(out_12), .in(in_1[11:0]), .sel(in_2));  // open: en
  Bit_Extender #(.in_width(32), .out_width(12)) bit_extender_1 (.in(out_14), .out(bit_extender_1_out));
  Multiplexer #(.width(12)) multiplexer_1 (.in0(out_12), .in1(undriven), .out(out_15), .sel(in_3));  // open: en
  Multiplexer multiplexer_2 (.in0(undriven_2), .in1(undriven_3), .out(out_16), .sel(in_9));  // open: en
  RAM #(.addrWidth(12), .dataWidth(32), .bus("separate")) ram_1 (
    .addr(out_15), .din(in_5), .data(out_14), .clk(clock_1_out), .ld(in_4));  // open: str, sel, clr
  Multiplexer #(.select(4)) multiplexer_3 (
    .in0(in_6), .in1(in_7), .in2(in_8), .out(out_17), .sel(in_10));  // open: in3, in4, in5, in6, in7, in8, in9, in10, in11, in12, in13, in14, in15, en

  assign out_13 = in_2;
endmodule
