// Logisim project negator_com_shifter.circ as structural Verilog: 1 circuit, main circuit main
module main (
  input  [3:0] in_1,
  input  [3:0] in_2,
  input  [3:0] in_3,
  input  [3:0] in_4,
  input  [1:0] in_5,
  input  [3:0] in_6,
  input  [1:0] in_7,
  input  [3:0] in_8,
  input  [1:0] in_9,
  input  [3:0] in_10,
  input  [1:0] in_11,
  input  [3:0] in_12,
  input  [1:0] in_13,
  output [3:0] out_14,
  output out_15,
  output out_16,
  output out_17,
  output [3:0] out_18,
  output [3:0] out_19,
  output [3:0] out_20,
  output [3:0] out_21,
  output [3:0] out_22
);

  Negator #(.width(4)) negator_1 (.in(in_1), .out(out_14));
  Comparator #(.width(4)) comparator_1 (.a(in_2), .b(in_3), .gt(out_15), .eq(out_16), .lt(out_17));
  Shifter #(.width(4)) shifter_1 (.in(in_4), .\dist (in_5), .out(out_18));
  Shifter #(.width(4), .shift("lr")) shifter_2 (.in(in_6), .\dist (in_7), .out(out_19));
  Shifter #(.width(4), .shift("ar")) shifter_3 (.in(in_8), .\dist (in_9), .out(out_20));
  Shifter #(.width(4), .shift("rl")) shifter_4 (.in(in_10), .\dist (in_11), .out(out_21));
  Shifter #(.width(4), .shift("rr")) shifter_5 (.in(in_12), .\dist (in_13), .out(out_22));
endmodule
