// Logisim project usinf ram.circ as structural Verilog
module main (
  input  [7:0] Addr,
  input  [7:0] Data_In,
  input  in_3,
  output [7:0] Data_out
);

  wire clock_1_out, not_1_out;

  Clock clock_1 (.out(clock_1_out));
  not not_1 (not_1_out, in_3);
  RAM #(.bus("separate")) ram_1 (
    .addr(Addr), .din(Data_In), .data(Data_out), .str(not_1_out), .clk(clock_1_out), .ld(in_3));  // open: sel, clr
endmodule

module addr9 (
  input  [8:0] Addr,
  input  [3:0] Data_in,
  input  R_W_prime,
  output [3:0] Data_out
);

  wire Clock_out, not_1_out;

  Clock Clock (.out(Clock_out));
  not not_1 (not_1_out, R_W_prime);
  RAM #(.addrWidth(9), .dataWidth(4), .bus("separate")) ram_1 (
    .addr(Addr), .din(Data_in), .data(Data_out), .str(not_1_out), .clk(Clock_out), .ld(R_W_prime));  // open: sel, clr
  Hex_Digit_Display hex_digit_display_1 (.value(Data_out));  // open: dp
endmodule

module _256_162 (
  input  [7:0] Address,
  input  [15:0] Data_in,
  input  in_3,
  output [7:0] out_4,
  output [7:0] out_5,
  output [15:0] out_6
);

  wire clock_1_out, not_1_out;

  Clock clock_1 (.out(clock_1_out));
  not not_1 (not_1_out, in_3);
  RAM #(.bus("separate")) ram_1 (
    .addr(Address), .din(Data_in[15:8]), .data(out_4), .str(not_1_out), .clk(clock_1_out), .ld(in_3));  // open: sel, clr
  RAM #(.bus("separate")) ram_2 (
    .addr(Address), .din(Data_in[7:0]), .data(out_5), .str(not_1_out), .clk(clock_1_out), .ld(in_3));  // open: sel, clr

  assign out_6 = {out_4, out_5};
endmodule
