// Logisim project Register.circ as structural Verilog: 11 circuits, main circuit main
module main (
  input  in_1
);

  wire clock_1_out, not_1_out;
  wire [3:0] Results_q_2, Results_q_3;
  wire [7:0] RA_q, ram_1_data, RB_q, Results_q, undriven;
  wire [11:0] IR_q, MAR_q, MBR_q, rom_1_data;
  wire [15:0] or_1_out, undriven_2;

  Clock clock_1 (.out(clock_1_out));
  Register_part #(.width(12)) MAR (.Q(MAR_q));  // open: D, en, clk, clr
  not not_1 (not_1_out, in_1);
  ROM #(.addrWidth(12), .dataWidth(12)) rom_1 (.addr(MAR_q), .data(rom_1_data));  // open: sel
  Register_part #(.width(12)) IR (.D(MBR_q), .Q(IR_q), .clk(clock_1_out));  // open: en, clr
  Register_part #(.width(12)) MBR (.D(rom_1_data), .Q(MBR_q), .clk(clock_1_out));  // open: en, clr
  RAM #(.bus("separate")) ram_1 (
    .addr(undriven), .din(RB_q), .data(ram_1_data), .str(not_1_out), .clk(clock_1_out), .ld(in_1));  // open: sel, clr
  Register_part RA (.Q(RA_q), .clk(clock_1_out));  // open: D, en, clr
  Register_part RB (.D(ram_1_data), .Q(RB_q), .clk(clock_1_out));  // open: en, clr
  dhva3 dhva3_1 ();  // open: A, B, SELECT, ALUoutput, Register, Exchange, Store
  assign or_1_out = undriven_2;  // OR_Gate or_1, 16 bits wide OR_Gate
  Hex_Digit_Display hex_digit_display_1 (.value(Results_q_2));  // open: dp
  Hex_Digit_Display hex_digit_display_2 (.value(Results_q_3));  // open: dp
  Register_part #(.width(16)) Results (
    .D(or_1_out), .Q({Results_q_3, Results_q_2, Results_q}), .clk(clock_1_out));  // open: en, clr
  Hex_Digit_Display hex_digit_display_3 (.value(Results_q[7:4]));  // open: dp
  Hex_Digit_Display hex_digit_display_4 (.value(Results_q[3:0]));  // open: dp

  // Notes on the sheet:
  //   contents of rom_1 (hex, n*v repeats v):
  //   b22
endmodule

module Register (
  input  [7:0] Data_in,
  input  R_W,
  input  [3:0] input01,
  input  [3:0] Input_02,
  input  Clock,
  output [7:0] Regi_out_01,
  output [7:0] Regi_out_02
);

  wire decoder_1_out0, decoder_1_out1, decoder_1_out2, decoder_1_out3, decoder_1_out4, decoder_1_out5,
       decoder_1_out6, decoder_1_out7, decoder_1_out8, decoder_1_out9, decoder_1_out10, decoder_1_out11,
       decoder_1_out12, decoder_1_out13, decoder_1_out14, decoder_1_out15, not_1_out;
  wire [7:0] R0_q, R1_q, R2_q, R3_q, R4_q, R5_q, R6_q, R7_q, R8_q, R9_q, R10_q, R11_q, R12_q, R13_q, R14_q,
       R15_q;

  Hex_Digit_Display hex_digit_display_1 (.value(Data_in[7:4]));  // open: dp
  Hex_Digit_Display hex_digit_display_2 (.value(Data_in[3:0]));  // open: dp
  Hex_Digit_Display hex_digit_display_3 (.value(Input_02));  // open: dp
  Decoder #(.select(4), .disabled(0)) decoder_1 (
    .out0(decoder_1_out0), .out1(decoder_1_out1), .out2(decoder_1_out2), .out3(decoder_1_out3),
    .out4(decoder_1_out4), .out5(decoder_1_out5), .out6(decoder_1_out6), .out7(decoder_1_out7),
    .out8(decoder_1_out8), .out9(decoder_1_out9), .out10(decoder_1_out10), .out11(decoder_1_out11),
    .out12(decoder_1_out12), .out13(decoder_1_out13), .out14(decoder_1_out14), .out15(decoder_1_out15),
    .sel(input01), .en(not_1_out));
  not not_1 (not_1_out, R_W);
  Hex_Digit_Display hex_digit_display_4 (.value(input01));  // open: dp
  Register_part R0 (.D(Data_in), .en(decoder_1_out0), .Q(R0_q), .clk(Clock));  // open: clr
  Register_part R2 (.D(Data_in), .en(decoder_1_out2), .Q(R2_q), .clk(Clock));  // open: clr
  Register_part R4 (.D(Data_in), .en(decoder_1_out4), .Q(R4_q), .clk(Clock));  // open: clr
  Register_part R6 (.D(Data_in), .en(decoder_1_out6), .Q(R6_q), .clk(Clock));  // open: clr
  Register_part R8 (.D(Data_in), .en(decoder_1_out8), .Q(R8_q), .clk(Clock));  // open: clr
  Register_part R10 (.D(Data_in), .en(decoder_1_out10), .Q(R10_q), .clk(Clock));  // open: clr
  Register_part R12 (.D(Data_in), .en(decoder_1_out12), .Q(R12_q), .clk(Clock));  // open: clr
  Register_part R14 (.D(Data_in), .en(decoder_1_out14), .Q(R14_q), .clk(Clock));  // open: clr
  Register_part R1 (.D(Data_in), .en(decoder_1_out1), .Q(R1_q), .clk(Clock));  // open: clr
  Register_part R3 (.D(Data_in), .en(decoder_1_out3), .Q(R3_q), .clk(Clock));  // open: clr
  Register_part R5 (.D(Data_in), .en(decoder_1_out5), .Q(R5_q), .clk(Clock));  // open: clr
  Register_part R7 (.D(Data_in), .en(decoder_1_out7), .Q(R7_q), .clk(Clock));  // open: clr
  Register_part R9 (.D(Data_in), .en(decoder_1_out9), .Q(R9_q), .clk(Clock));  // open: clr
  Register_part R11 (.D(Data_in), .en(decoder_1_out11), .Q(R11_q), .clk(Clock));  // open: clr
  Register_part R13 (.D(Data_in), .en(decoder_1_out13), .Q(R13_q), .clk(Clock));  // open: clr
  Register_part R15 (.D(Data_in), .en(decoder_1_out15), .Q(R15_q), .clk(Clock));  // open: clr
  Multiplexer #(.select(4), .width(8)) multiplexer_1 (
    .in0(R0_q), .in1(R1_q), .in2(R2_q), .in3(R3_q), .in4(R4_q), .in5(R5_q), .in6(R6_q), .in7(R7_q),
    .in8(R8_q), .in9(R9_q), .in10(R10_q), .in11(R11_q), .in12(R12_q), .in13(R13_q), .in14(R14_q),
    .in15(R15_q), .out(Regi_out_01), .sel(input01), .en(R_W));
  Hex_Digit_Display hex_digit_display_5 (.value(Regi_out_01[7:4]));  // open: dp
  Hex_Digit_Display hex_digit_display_6 (.value(Regi_out_02[7:4]));  // open: dp
  Multiplexer #(.select(4), .width(8)) multiplexer_2 (
    .in0(R0_q), .in1(R1_q), .in2(R2_q), .in3(R3_q), .in4(R4_q), .in5(R5_q), .in6(R6_q), .in7(R7_q),
    .in8(R8_q), .in9(R9_q), .in10(R10_q), .in11(R11_q), .in12(R12_q), .in13(R13_q), .in14(R14_q),
    .in15(R15_q), .out(Regi_out_02), .sel(Input_02), .en(R_W));
  Hex_Digit_Display hex_digit_display_7 (.value(Regi_out_01[3:0]));  // open: dp
  Hex_Digit_Display hex_digit_display_8 (.value(Regi_out_02[3:0]));  // open: dp

  // Notes on the sheet:
  //   Register (4bits)
  //   Regi_Out_01
  //   Regi_out_02
endmodule

module ALU (
  input  [7:0] Decrement,
  input  [7:0] in_2,
  input  [7:0] A,
  input  [7:0] B,
  input  [3:0] SELECT,
  input  [3:0] _1,
  output [15:0] ALUoutput
);

  wire adder_2_cout, subtractor_2_bout;
  wire [2:0] bit_extender_1_out;
  wire [7:0] adder_1_out, adder_2_out, and_1_out, bit_extender_6_out, bit_extender_7_out, divider_1_out,
       divider_1_rem, multiplier_1_cout, multiplier_1_out, not_1_out, or_1_out, shifter_1_out, shifter_2_out,
       shifter_3_out, shifter_4_out, subtractor_1_out, subtractor_2_out;
  wire [15:0] bit_extender_2_out, bit_extender_3_out, bit_extender_4_out, bit_extender_5_out,
       bit_extender_8_out, bit_extender_9_out, bit_extender_10_out, bit_extender_11_out, bit_extender_12_out,
       bit_extender_13_out, bit_extender_14_out;

  Hex_Digit_Display hex_digit_display_1 (.value(A[7:4]));  // open: dp
  Hex_Digit_Display hex_digit_display_2 (.value(B[7:4]));  // open: dp
  Hex_Digit_Display hex_digit_display_3 (.value(A[3:0]));  // open: dp
  Hex_Digit_Display hex_digit_display_4 (.value(B[3:0]));  // open: dp
  Bit_Extender #(.out_width(3)) bit_extender_1 (.in(B), .out(bit_extender_1_out));
  Adder adder_1 (.a(A), .b(Decrement), .out(adder_1_out));  // open: cin, cout
  Subtractor subtractor_1 (.a(A), .b(in_2), .out(subtractor_1_out));  // open: bin, bout
  assign bit_extender_2_out = {{8{1'b0}}, B};  // Bit_Extender bit_extender_2
  assign bit_extender_3_out = {{8{1'b0}}, A};  // Bit_Extender bit_extender_3
  Adder adder_2 (.a(A), .b(B), .out(adder_2_out), .cout(adder_2_cout));  // open: cin
  Subtractor subtractor_2 (.a(A), .b(B), .out(subtractor_2_out), .bout(subtractor_2_bout));  // open: bin
  Multiplier multiplier_1 (.a(A), .b(B), .out(multiplier_1_out), .cout(multiplier_1_cout));  // open: cin
  Divider divider_1 (.a(A), .b(B), .out(divider_1_out), .rem(divider_1_rem));  // open: upper
  assign and_1_out = A & B;  // AND_Gate and_1, 8 bits wide
  assign or_1_out = A | B;  // OR_Gate or_1, 8 bits wide
  assign not_1_out = ~B;  // NOT_Gate not_1, 8 bits wide
  Shifter #(.shift("lr")) shifter_1 (.in(A), .\dist (bit_extender_1_out), .out(shifter_1_out));
  Shifter shifter_2 (.in(A), .\dist (bit_extender_1_out), .out(shifter_2_out));
  Shifter #(.shift("rr")) shifter_3 (.in(A), .\dist (bit_extender_1_out), .out(shifter_3_out));
  Shifter #(.shift("rl")) shifter_4 (.in(A), .\dist (bit_extender_1_out), .out(shifter_4_out));
  assign bit_extender_4_out = {{8{1'b0}}, adder_1_out};  // Bit_Extender bit_extender_4
  assign bit_extender_5_out = {{8{1'b0}}, subtractor_1_out};  // Bit_Extender bit_extender_5
  assign bit_extender_6_out = {{7{1'b0}}, adder_2_cout};  // Bit_Extender bit_extender_6
  assign bit_extender_7_out = {{7{1'b0}}, subtractor_2_bout};  // Bit_Extender bit_extender_7
  assign bit_extender_8_out = {{8{1'b0}}, and_1_out};  // Bit_Extender bit_extender_8
  assign bit_extender_9_out = {{8{1'b0}}, or_1_out};  // Bit_Extender bit_extender_9
  assign bit_extender_10_out = {{8{1'b0}}, not_1_out};  // Bit_Extender bit_extender_10
  assign bit_extender_11_out = {{8{1'b0}}, shifter_1_out};  // Bit_Extender bit_extender_11
  assign bit_extender_12_out = {{8{1'b0}}, shifter_2_out};  // Bit_Extender bit_extender_12
  assign bit_extender_13_out = {{8{1'b0}}, shifter_3_out};  // Bit_Extender bit_extender_13
  assign bit_extender_14_out = {{8{1'b0}}, shifter_4_out};  // Bit_Extender bit_extender_14
  Multiplexer #(.select(4), .width(16), .disabled(0)) multiplexer_1 (
    .in0(bit_extender_2_out), .in1(bit_extender_3_out), .in2({bit_extender_6_out, adder_2_out}),
    .in3({bit_extender_7_out, subtractor_2_out}), .in4({multiplier_1_cout, multiplier_1_out}),
    .in5({divider_1_rem, divider_1_out}), .in6(bit_extender_4_out), .in7(bit_extender_5_out),
    .in8(bit_extender_8_out), .in9(bit_extender_9_out), .in10(bit_extender_10_out), .in11({A, B}),
    .in12(bit_extender_11_out), .in13(bit_extender_12_out), .in14(bit_extender_13_out),
    .in15(bit_extender_14_out), .out(ALUoutput), .sel(SELECT));  // open: en

  // Notes on the sheet:
  //   BitExtender
  //   Exchange
  //   Store
  //   Sub
  //   Mul
  //   Div
  //   And
  //   OR
  //   ShiftRight
  //   ShiftLeft
  //   Rotateright
  //   RotateLeft
  //   ALU-8bit 
  //   Increment
  //   Load
  //   Add
  //   Not
  //   0-adder|1-sub|2-mpy|3-div|4-and|5-or|6-xnor|7-xor|8-lls|9-lrs|10-ars|11-rr|12-rl
endmodule

// PC
module Program_counter (
  input  [11:0] PC_INput,
  input  PC_enable,
  input  Clock,
  input  PC_reset,
  output [11:0] PC_OUT
);

  wire [11:0] adder_1_out;

  Hex_Digit_Display hex_digit_display_1 (.value(PC_INput[11:8]));  // open: dp
  Hex_Digit_Display hex_digit_display_2 (.value(PC_INput[3:0]));  // open: dp
  Hex_Digit_Display hex_digit_display_3 (.value(PC_INput[7:4]));  // open: dp
  Adder #(.width(12)) adder_1 (.a(PC_INput), .b(PC_OUT), .out(adder_1_out), .cin(1'b1));  // open: cout
  Hex_Digit_Display hex_digit_display_4 (.value(PC_OUT[11:8]));  // open: dp
  Hex_Digit_Display hex_digit_display_5 (.value(PC_OUT[7:4]));  // open: dp
  Register_part #(.width(12)) register_1 (.D(adder_1_out), .en(PC_enable), .Q(PC_OUT), .clk(Clock), .clr(PC_reset));
  Hex_Digit_Display hex_digit_display_6 (.value(PC_OUT[3:0]));  // open: dp
endmodule

module maina (
  input  in_1
);

  wire clock_1_out;
  wire [7:0] ram_1_data, undriven;
  wire [11:0] IR_q, MAR_q, MBR_q, rom_1_data;

  Clock clock_1 (.out(clock_1_out));
  Program_counter PC ();  // open: PC_INput, PC_enable, Clock, PC_reset, PC_OUT
  Register_part #(.width(12)) MAR (.Q(MAR_q));  // open: D, en, clk, clr
  ROM #(.addrWidth(12), .dataWidth(12)) rom_1 (.addr(MAR_q), .data(rom_1_data));  // open: sel
  Register_part #(.width(12)) IR (.D(MBR_q), .Q(IR_q), .clk(clock_1_out), .clr(in_1));  // open: en
  Register_part #(.width(12)) MBR (.D(rom_1_data), .Q(MBR_q), .clk(clock_1_out), .clr(in_1));  // open: en
  RAM #(.bus("separate")) ram_1 (
    .addr(undriven), .data(ram_1_data), .clk(clock_1_out));  // open: din, str, sel, ld, clr

  // Notes on the sheet:
  //   contents of rom_1 (hex, n*v repeats v):
  //   202
endmodule

// iyfj
module circuit (
);

  wire [1:0] undriven;
  wire [3:0] bitselector_1_out;
  wire [15:0] bit_extender_1_out;
  wire [31:0] ram_1_data;

  // Transmission_Gate transmission_1: pin names not known
  Controlled_Inverter controlled_inverter_1 ();  // open: in, out, en
  Register_part register_1 ();  // open: D, en, Q, clk, clr
  Counter counter_1 ();  // open: load, D, count, Q, carry, clk, clr
  Priority_Encoder priority_encoder_1 ();  // open: in0, in1, in2, in3, in4, in5, in6, in7, out, en_in, gs, en_out
  Random random_1 ();  // open: clk, next, out, clr
  Bit_Extender #(.in_width(32)) bit_extender_1 (.in(ram_1_data), .out(bit_extender_1_out));
  S_R_Flip_Flop s_r_ff_1 ();  // open: S, clk, R, Q, Qn, preset, reset, en
  BitSelector #(.width(16), .group(4)) bitselector_1 (.out(bitselector_1_out), .sel(undriven));  // open: in
  RAM #(.addrWidth(16), .dataWidth(32), .bus("separate")) ram_1 (
    .addr(bit_extender_1_out), .data(ram_1_data));  // open: din, str, sel, clk, ld, clr
  BitFinder bitfinder_1 ();  // open: in, index, found
endmodule

module dhva3 (
  input  [7:0] A,
  input  [7:0] B,
  input  [3:0] SELECT,
  output [15:0] ALUoutput,
  output [15:0] Register,
  output [15:0] Exchange,
  output [15:0] Store
);

  wire adder_1_cout, subtractor_1_bout;
  wire [2:0] bit_extender_2_out;
  wire [7:0] adder_1_out, adder_2_out, and_1_out, bit_extender_1_out, bit_extender_5_out, bit_extender_6_out,
       divider_1_out, divider_1_rem, multiplier_1_cout, multiplier_1_out, not_1_out, or_1_out, shifter_1_out,
       shifter_2_out, shifter_3_out, shifter_4_out, subtractor_1_out, subtractor_2_out;
  wire [15:0] bit_extender_3_out, bit_extender_4_out, bit_extender_7_out, bit_extender_8_out,
       bit_extender_9_out, bit_extender_10_out, bit_extender_11_out, bit_extender_12_out,
       bit_extender_13_out, bit_extender_14_out, bit_extender_15_out, demultiplexer_1_out0,
       demultiplexer_1_out2, demultiplexer_1_out3, demultiplexer_1_out4, demultiplexer_1_out5,
       demultiplexer_1_out6, demultiplexer_1_out7, demultiplexer_1_out8, demultiplexer_1_out9,
       demultiplexer_1_out10, demultiplexer_1_out12, demultiplexer_1_out13, demultiplexer_1_out14,
       demultiplexer_1_out15;

  Hex_Digit_Display hex_digit_display_1 (.value(A[7:4]));  // open: dp
  Hex_Digit_Display hex_digit_display_2 (.value(B[7:4]));  // open: dp
  Hex_Digit_Display hex_digit_display_3 (.value(A[3:0]));  // open: dp
  Hex_Digit_Display hex_digit_display_4 (.value(B[3:0]));  // open: dp
  assign bit_extender_1_out = {{7{1'b0}}, 1'b1};  // Bit_Extender bit_extender_1
  Bit_Extender #(.out_width(3)) bit_extender_2 (.in(B), .out(bit_extender_2_out));
  assign bit_extender_3_out = {{8{1'b0}}, B};  // Bit_Extender bit_extender_3
  assign bit_extender_4_out = {{8{1'b0}}, A};  // Bit_Extender bit_extender_4
  Adder adder_1 (.a(A), .b(B), .out(adder_1_out), .cout(adder_1_cout));  // open: cin
  Subtractor subtractor_1 (.a(A), .b(B), .out(subtractor_1_out), .bout(subtractor_1_bout));  // open: bin
  Multiplier multiplier_1 (.a(A), .b(B), .out(multiplier_1_out), .cout(multiplier_1_cout));  // open: cin
  Divider divider_1 (.a(A), .b(B), .out(divider_1_out), .rem(divider_1_rem));  // open: upper
  Adder adder_2 (.a(A), .b(bit_extender_1_out), .out(adder_2_out));  // open: cin, cout
  Subtractor subtractor_2 (.a(A), .b(bit_extender_1_out), .out(subtractor_2_out));  // open: bin, bout
  assign and_1_out = A & B;  // AND_Gate and_1, 8 bits wide
  assign or_1_out = A | B;  // OR_Gate or_1, 8 bits wide
  assign not_1_out = ~A;  // NOT_Gate not_1, 8 bits wide
  Shifter #(.shift("lr")) shifter_1 (.in(A), .\dist (bit_extender_2_out), .out(shifter_1_out));
  Shifter shifter_2 (.in(A), .\dist (bit_extender_2_out), .out(shifter_2_out));
  Shifter #(.shift("rr")) shifter_3 (.in(A), .\dist (bit_extender_2_out), .out(shifter_3_out));
  Shifter #(.shift("rl")) shifter_4 (.in(A), .\dist (bit_extender_2_out), .out(shifter_4_out));
  assign bit_extender_5_out = {{7{1'b0}}, adder_1_cout};  // Bit_Extender bit_extender_5
  assign bit_extender_6_out = {{7{1'b0}}, subtractor_1_bout};  // Bit_Extender bit_extender_6
  assign bit_extender_7_out = {{8{1'b0}}, adder_2_out};  // Bit_Extender bit_extender_7
  assign bit_extender_8_out = {{8{1'b0}}, subtractor_2_out};  // Bit_Extender bit_extender_8
  assign bit_extender_9_out = {{8{1'b0}}, and_1_out};  // Bit_Extender bit_extender_9
  assign bit_extender_10_out = {{8{1'b0}}, or_1_out};  // Bit_Extender bit_extender_10
  assign bit_extender_11_out = {{8{1'b0}}, not_1_out};  // Bit_Extender bit_extender_11
  assign bit_extender_12_out = {{8{1'b0}}, shifter_1_out};  // Bit_Extender bit_extender_12
  assign bit_extender_13_out = {{8{1'b0}}, shifter_2_out};  // Bit_Extender bit_extender_13
  assign bit_extender_14_out = {{8{1'b0}}, shifter_3_out};  // Bit_Extender bit_extender_14
  assign bit_extender_15_out = {{8{1'b0}}, shifter_4_out};  // Bit_Extender bit_extender_15
  Hex_Digit_Display hex_digit_display_5 (.value(ALUoutput[15:12]));  // open: dp
  Multiplexer #(.select(4), .width(16), .disabled(0)) multiplexer_1 (
    .in0(bit_extender_3_out), .in1(bit_extender_4_out), .in2({bit_extender_5_out, adder_1_out}),
    .in3({bit_extender_6_out, subtractor_1_out}), .in4({multiplier_1_cout, multiplier_1_out}),
    .in5({divider_1_rem, divider_1_out}), .in6(bit_extender_7_out), .in7(bit_extender_8_out),
    .in8(bit_extender_9_out), .in9(bit_extender_10_out), .in10(bit_extender_11_out), .in11({A, B}),
    .in12(bit_extender_12_out), .in13(bit_extender_13_out), .in14(bit_extender_14_out),
    .in15(bit_extender_15_out), .out(ALUoutput), .sel(SELECT));  // open: en
  Hex_Digit_Display hex_digit_display_6 (.value(ALUoutput[7:4]));  // open: dp
  Hex_Digit_Display hex_digit_display_7 (.value(ALUoutput[11:8]));  // open: dp
  Hex_Digit_Display hex_digit_display_8 (.value(SELECT));  // open: dp
  Hex_Digit_Display hex_digit_display_9 (.value(ALUoutput[3:0]));  // open: dp
  Demultiplexer #(.select(4), .width(16)) demultiplexer_1 (
    .out0(demultiplexer_1_out0), .out1(Store), .out2(demultiplexer_1_out2), .out3(demultiplexer_1_out3),
    .out4(demultiplexer_1_out4), .out5(demultiplexer_1_out5), .out6(demultiplexer_1_out6),
    .out7(demultiplexer_1_out7), .out8(demultiplexer_1_out8), .out9(demultiplexer_1_out9),
    .out10(demultiplexer_1_out10), .out11(Exchange), .out12(demultiplexer_1_out12),
    .out13(demultiplexer_1_out13), .out14(demultiplexer_1_out14), .out15(demultiplexer_1_out15),
    .in(ALUoutput), .sel(SELECT));  // open: en
  assign Register = demultiplexer_1_out0 | demultiplexer_1_out2 | demultiplexer_1_out3 | demultiplexer_1_out4 | demultiplexer_1_out5 | demultiplexer_1_out6 | demultiplexer_1_out7 | demultiplexer_1_out8 | demultiplexer_1_out9 | demultiplexer_1_out10 | demultiplexer_1_out12 | demultiplexer_1_out13 | demultiplexer_1_out14 | demultiplexer_1_out15;  // OR_Gate or_2, 16 bits wide
  Hex_Digit_Display hex_digit_display_10 (.value(Register[15:12]));  // open: dp
  Hex_Digit_Display hex_digit_display_11 (.value(Register[11:8]));  // open: dp
  Hex_Digit_Display hex_digit_display_12 (.value(Exchange[15:12]));  // open: dp
  Hex_Digit_Display hex_digit_display_13 (.value(Store[15:12]));  // open: dp
  Hex_Digit_Display hex_digit_display_14 (.value(Register[3:0]));  // open: dp
  Hex_Digit_Display hex_digit_display_15 (.value(Register[7:4]));  // open: dp
  Hex_Digit_Display hex_digit_display_16 (.value(Exchange[7:4]));  // open: dp
  Hex_Digit_Display hex_digit_display_17 (.value(Exchange[11:8]));  // open: dp
  Hex_Digit_Display hex_digit_display_18 (.value(Store[11:8]));  // open: dp
  Hex_Digit_Display hex_digit_display_19 (.value(Store[7:4]));  // open: dp
  Hex_Digit_Display hex_digit_display_20 (.value(Exchange[3:0]));  // open: dp
  Hex_Digit_Display hex_digit_display_21 (.value(Store[3:0]));  // open: dp

  // Notes on the sheet:
  //   BitExtender
  //   Increment-----------------------------
  //   Decrement-----------------------
  //   Exchange
  //   Load
  //   Store
  //   Add
  //   Sub
  //   Mul
  //   Div
  //   And
  //   OR
  //   ShiftRight
  //   ShiftLeft
  //   Rotateright
  //   RotateLeft
  //   ALU-8bit 
  //   Not
  //   0-adder|1-sub|2-mpy|3-div|4-and|5-or|6-xnor|7-xor|8-lls|9-lrs|10-ars|11-rr|12-rl
endmodule

module \final  (
  input  [11:0] PC_input,
  output [11:0] PC_INPUT_2
);

  wire Clock, not_1_out, not_2_out, PC_shift_out, Reset, selector_1_output, selector_2_output;
  wire [3:0] dhva3_1_exchange_2, MAR_q, MAR_q_2, MAR_q_3, RZ_q, RZ_q_2, RZ_q_3, RZ_q_4;
  wire [7:0] dhva3_1_exchange, multiplexer_1_out, multiplexer_2_out, or_1_out, or_1_out_2, or_2_out,
       or_2_out_2, RA_q, ram_1_data, RB_q, register_1_regi_out_01, register_1_regi_out_02;
  wire [7:4] dhva3_1_exchange_3;
  wire [11:0] IR_q, MBR_q, rom_1_data;
  wire [15:0] bit_extender_1_out, bit_extender_2_out, dhva3_1_aluoutput, dhva3_1_register, dhva3_1_store;

  Hex_Digit_Display hex_digit_display_1 (.value(PC_input[7:4]));  // open: dp
  Hex_Digit_Display hex_digit_display_2 (.value(PC_input[11:8]));  // open: dp
  Hex_Digit_Display hex_digit_display_3 (.value(MAR_q_3));  // open: dp
  Hex_Digit_Display hex_digit_display_4 (.value(PC_input[3:0]));  // open: dp
  Shift_Register #(.length(6)) PC_shift (
    .in(PC_shift_out), .clk(Clock), .out(PC_shift_out));  // open: shift, load, clr, d0, q0, d1, q1, d2, q2, d3, q3, d4, q4, d5, q5
  Hex_Digit_Display hex_digit_display_5 (.value(dhva3_1_exchange_2));  // open: dp
  Hex_Digit_Display hex_digit_display_6 (.value(dhva3_1_exchange_3));  // open: dp
  Hex_Digit_Display hex_digit_display_7 (.value(MAR_q_2));  // open: dp
  Hex_Digit_Display hex_digit_display_8 (.value(MAR_q));  // open: dp
  Program_counter program_counter_1 (
    .PC_INput(PC_input), .PC_enable(PC_shift_out), .Clock(Clock), .PC_reset(Reset), .PC_OUT(PC_INPUT_2));
  Register_part #(.width(12)) MAR (
    .D(PC_INPUT_2), .Q({MAR_q_3, MAR_q_2, MAR_q}), .clk(Clock), .clr(Reset));  // open: en
  not not_1 (not_1_out, PC_shift_out);
  ROM #(.addrWidth(12), .dataWidth(12)) rom_1 (.addr({MAR_q_3, MAR_q_2, MAR_q}), .data(rom_1_data));  // open: sel
  Register_part #(.width(12)) MBR (.D(rom_1_data), .Q(MBR_q), .clk(Clock), .clr(Reset));  // open: en
  not not_2 (not_2_out, not_1_out);
  selector selector_1 (.Input({or_1_out_2, or_1_out}), .Output(selector_1_output));
  Multiplexer #(.width(8)) multiplexer_1 (
    .in0(RA_q), .in1(or_1_out), .out(multiplexer_1_out), .sel(selector_1_output));  // open: en
  Register_part #(.width(12)) IR (.D(MBR_q), .Q(IR_q), .clk(Clock), .clr(Reset));  // open: en
  RAM #(.bus("separate")) ram_1 (
    .addr(register_1_regi_out_02), .din(multiplexer_2_out), .data(ram_1_data), .str(not_2_out), .clk(Clock),
    .ld(not_1_out));  // open: sel, clr
  assign {or_1_out_2, or_1_out} = bit_extender_1_out | dhva3_1_register;  // OR_Gate or_1, 16 bits wide
  Register register_1 (
    .Data_in(multiplexer_1_out), .R_W(not_1_out), .input01(IR_q[7:4]), .Input_02(IR_q[3:0]), .Clock(Clock),
    .Regi_out_01(register_1_regi_out_01), .Regi_out_02(register_1_regi_out_02));
  Multiplexer #(.width(8)) multiplexer_2 (
    .in0(RB_q), .in1(or_2_out), .out(multiplexer_2_out), .sel(selector_2_output));  // open: en
  Register_part RA (.D(register_1_regi_out_01), .Q(RA_q), .clk(Clock), .clr(Reset));  // open: en
  assign {or_2_out_2, or_2_out} = bit_extender_2_out | dhva3_1_store;  // OR_Gate or_2, 16 bits wide
  selector selector_2 (.Input({or_2_out_2, or_2_out}), .Output(selector_2_output));
  Hex_Digit_Display hex_digit_display_9 (.value(RZ_q_3));  // open: dp
  Hex_Digit_Display hex_digit_display_10 (.value(RZ_q_4));  // open: dp
  Register_part RB (.D(ram_1_data), .Q(RB_q), .clk(Clock), .clr(Reset));  // open: en
  Hex_Digit_Display hex_digit_display_11 (.value(RZ_q_2));  // open: dp
  Hex_Digit_Display hex_digit_display_12 (.value(RZ_q));  // open: dp
  Register_part #(.width(16)) RZ (
    .D(dhva3_1_aluoutput), .Q({RZ_q_4, RZ_q_3, RZ_q_2, RZ_q}), .clk(Clock), .clr(Reset));  // open: en
  dhva3 dhva3_1 (
    .A(RA_q), .B(RB_q), .SELECT(IR_q[11:8]), .ALUoutput(dhva3_1_aluoutput), .Register(dhva3_1_register),
    .Exchange({dhva3_1_exchange_3, dhva3_1_exchange_2, dhva3_1_exchange}), .Store(dhva3_1_store));
  assign bit_extender_1_out = {{8{1'b0}}, dhva3_1_exchange};  // Bit_Extender bit_extender_1
  assign bit_extender_2_out = {{8{1'b0}}, {dhva3_1_exchange_3, dhva3_1_exchange_2}};  // Bit_Extender bit_extender_2
  Button button_1 (.out(Clock));
  Button button_2 (.out(Reset));

  // Notes on the sheet:
  //   PC
  //   Code Memory
  //   contents of rom_1 (hex, n*v repeats v):
  //   b67 524 431 512 246
  //   ALU
  //   Register
endmodule

module tetegrd (
  input  [3:0] in_1,
  input  [3:0] in_2,
  input  in_3,
  input  [3:0] in_4,
  input  [15:0] in_5,
  output out_6,
  output out_7
);

  wire [3:0] controlled_buffer_1_out, even_parity_1_out, transmission_1_p3, transmission_1_p4, undriven;
  wire [3:1] multiplexer_1_out;

  Multiplexer #(.width(4)) multiplexer_1 (
    .in0(in_1), .in1(in_4), .out({multiplexer_1_out, out_6}), .sel(in_4[0]));  // open: en
  BitFinder bitfinder_1 ();  // open: in, index, found
  // Transmission_Gate transmission_1: pin names not known; wires that end beside it: in_5, out_7, transmission_1_p3, transmission_1_p4
  BitSelector bitselector_1 ();  // open: in, out, sel
  Priority_Encoder priority_encoder_1 ();  // open: in0, in1, in2, in3, in4, in5, in6, in7, out, en_in, gs, en_out
  assign controlled_buffer_1_out = in_3 ? undriven : 4'bz;  // Controlled_Buffer controlled_buffer_1
  assign even_parity_1_out = ~(transmission_1_p4 ^ transmission_1_p3);  // Even_Parity even_parity_1, 4 bits wide
  // Pins of 1 and 4 bits meet at {multiplexer_1_out, out_6}
  // Pins of 1 and 4 bits meet at in_4
endmodule

module selector (
  input  [15:0] Input,
  output Output
);

  wire bit_extender_1_out, or_1_out;

  or or_1 (or_1_out, Input[0], Input[1], Input[2], Input[3], Input[4], Input[5], Input[6], Input[7], Input[8], Input[9], Input[10], Input[11], Input[12], Input[13], Input[14], Input[15]);
  Comparator #(.width(1), .mode("unsigned")) comparator_1 (
    .a(or_1_out), .b(bit_extender_1_out), .eq(Output));  // open: gt, lt
  Bit_Extender #(.in_width(1), .out_width(1)) bit_extender_1 (.in(1'b1), .out(bit_extender_1_out));
endmodule

module sgfsdh (
  input  [1:0] in_1,
  input  [1:0] in_2,
  input  [15:0] in_3,
  input  [15:0] in_4,
  input  [15:0] in_5,
  input  [15:0] in_6,
  output [3:0] out_7,
  output [15:0] out_8,
  output [15:0] out_9
);

  wire undriven, undriven_2;
  wire [1:0] xor_2_out;

  assign out_7[1:0] = in_1 ^ in_2;  // XOR_Gate xor_1, 2 bits wide
  selector selector_1 ();  // open: Input, Output
  selector selector_2 ();  // open: Input, Output
  assign xor_2_out = out_7[1:0] ^ in_2;  // XOR_Gate xor_2, 2 bits wide
  Multiplexer #(.width(16)) multiplexer_1 (.in0(in_3), .in1(in_4), .out(out_8), .sel(undriven));  // open: en
  Multiplexer #(.width(16)) multiplexer_2 (.in0(in_5), .in1(in_6), .out(out_9), .sel(undriven_2));  // open: en
  assign out_7[3:2] = out_7[1:0] ^ xor_2_out;  // XOR_Gate xor_3, 2 bits wide
endmodule
